// Logisim project 推箱子.circ as structural Verilog: 26 circuits, main circuit ◇单周期RISC-V
module \推箱子  (
);

  wire AluSrcB, and_4_out, and_5_out, and_6_out, and_7_out, and_8_out, and_9_out, and_10_out, and_11_out, B,
       Beq, blt, Bne, CLK, comparator_1_eq, comparator_2_eq, comparator_3_eq, comparator_4_eq,
       comparator_5_eq, comparator_6_eq, ecall, en, equal, Go, halt, J, JAL, JALR, less, lhu, MemToReg,
       MemWrite, not_1_out, not_2_out, not_3_out, not_4_out, not_5_out, or_1_out, or_3_out, or_5_out,
       RegWrite, RST, S_Type, U_type;
  wire [1:0] priority_encoder_1_out;
  wire [2:0] s00, s01, s02, s03, s10, s11, s12, s13, s20, s21, s22, s23;
  wire [3:0] AluOP;
  wire [4:0] multiplexer_3_out, multiplexer_4_out;
  wire [14:0] bit_extender_7_out, bit_extender_8_out, bit_extender_9_out, bit_extender_10_out,
       bit_extender_11_out, bit_extender_12_out, bit_extender_13_out, bit_extender_14_out,
       bit_extender_15_out, bit_extender_16_out, bit_extender_17_out, bit_extender_18_out,
       bit_extender_19_out, bit_extender_20_out, bit_extender_21_out, bit_extender_22_out,
       bit_extender_23_out, bit_extender_24_out, bit_extender_25_out, bit_extender_26_out,
       bit_extender_27_out, bit_extender_28_out, bit_extender_29_out, bit_extender_30_out,
       bit_extender_31_out, bit_extender_32_out, bit_extender_33_out, bit_extender_34_out,
       bit_extender_35_out, bit_extender_36_out, bit_extender_37_out, bit_extender_38_out,
       bit_extender_39_out, bit_extender_40_out, bit_extender_41_out, bit_extender_42_out,
       bit_extender_43_out, bit_extender_44_out, bit_extender_45_out, bit_extender_46_out,
       bit_extender_47_out, bit_extender_48_out, bit_extender_49_out, bit_extender_50_out,
       bit_extender_51_out, bit_extender_52_out, bit_extender_53_out, bit_extender_54_out,
       bit_extender_55_out, bit_extender_56_out, bit_extender_57_out, bit_extender_58_out,
       bit_extender_59_out, bit_extender_60_out, bit_extender_61_out, bit_extender_62_out,
       bit_extender_63_out, bit_extender_64_out, bit_extender_65_out, bit_extender_66_out, shifter_4_out,
       shifter_5_out, shifter_6_out, shifter_7_out, shifter_8_out, shifter_9_out, shifter_10_out,
       shifter_11_out, shifter_12_out, shifter_13_out, shifter_14_out, shifter_15_out, shifter_16_out,
       shifter_17_out, shifter_18_out, shifter_19_out, shifter_20_out, shifter_21_out, shifter_22_out,
       shifter_23_out, shifter_24_out, shifter_25_out, shifter_26_out, shifter_27_out, shifter_28_out,
       shifter_29_out, shifter_30_out, shifter_31_out, shifter_32_out, shifter_33_out, shifter_34_out,
       shifter_35_out, shifter_36_out, shifter_37_out, shifter_38_out, shifter_39_out, shifter_40_out,
       shifter_41_out, shifter_42_out, shifter_43_out, x1, x2, x3, x4, x5, x6, x7, x8, x9, x10, x11, x12,
       x13, x14, x15, x16, x17, x18, x19, x20;
  wire [15:0] multiplexer_9_out, \总周期数 ;
  wire [31:0] adder_2_out, aluresult, b_t, bit_extender_1_out, bit_extender_2_out, bit_extender_3_out,
       bit_extender_4_out, bit_extender_5_out, bit_extender_6_out, IR, jal_t, jalr_t, LedData, Loc, MDin,
       MDout, multiplexer_1_out, multiplexer_2_out, multiplexer_5_out, multiplexer_6_out, multiplexer_7_out,
       multiplexer_8_out, PC, PC_4, R1, RDin, result, shifter_1_out, shifter_2_out, shifter_3_out, v00, v01,
       v02, v03, v10, v11, v12, v13, v20, v21, v22, v23;
  wire [31:9] y_0, y_1, y_2, y_3;

  Clock #(.highDuration(1), .lowDuration(1)) clock_1 (.out(CLK));
  Button u_RST (.out(RST));
  Priority_Encoder #(.select(2), .disabled("Z")) priority_encoder_1 (
    .in0(1'b1), .in1(B), .in2(JAL), .in3(JALR), .out(priority_encoder_1_out));  // open: gs, en_out, en_in
  Multiplexer #(.select(2), .width(32), .disabled("Z"), .enable("false")) multiplexer_1 (
    .in0(PC_4), .in1(b_t), .in2(jal_t), .in3(jalr_t), .out(multiplexer_1_out), .sel(priority_encoder_1_out));
  or or_1 (or_1_out, Go, not_1_out);
  Register #(.width(32), .trigger("rising"), .Select("low")) u_PC (
    .D(multiplexer_1_out), .en(or_1_out), .Q(PC), .clk(CLK), .clr(RST));
  not not_1 (not_1_out, halt);
  Adder #(.width(32)) adder_1 (.a(PC), .b(32'h4), .out(PC_4));  // open: cin, cout
  Comparator #(.width(32), .mode("twosComplement")) comparator_1 (
    .a(R1), .b(32'h22), .eq(comparator_1_eq));  // open: gt, lt
  not not_2 (not_2_out, comparator_1_eq);
  and and_1 (halt, not_2_out, ecall);
  Multiplexer #(.select(1), .width(32), .disabled("Z"), .enable("false")) multiplexer_2 (
    .in0({32{1'b0}}), .in1(MDin), .out(multiplexer_2_out), .sel(en));
  // RiscV_Probe riscv_probe_1: pin names not known; wires that end beside it: IR
  and and_2 (en, ecall, comparator_1_eq);
  or or_2 (J, JALR, JAL);
  ROM #(.addrWidth(10), .dataWidth(32), .Select("high")) rom_1 (.addr(PC[11:2]), .data(IR));
  Register #(.width(32), .trigger("rising"), .Select("low")) register_1 (
    .D(multiplexer_2_out), .en(en), .Q(LedData), .clk(CLK), .clr(RST));
  DotMatrix #(.inputtype("row"), .matrixcols(5), .matrixrows(5), .persist(0), .dotshape("square")) dotmatrix_1 (
    .row0({5{1'b1}}), .row1(5'b10101), .row2({5{1'b1}}), .row3(5'b10101), .row4({5{1'b1}}));
  DotMatrix #(.inputtype("row"), .matrixcols(5), .matrixrows(5), .persist(0), .dotshape("square")) dotmatrix_2 (
    .row0(5'b00100), .row1(5'b01010), .row2(5'b10001), .row3(5'b01010), .row4(5'b00100));
  Multiplexer #(.select(1), .width(5), .disabled("Z"), .enable("false")) multiplexer_3 (
    .in0(IR[19:15]), .in1(5'b10001), .out(multiplexer_3_out), .sel(ecall));
  DotMatrix #(.inputtype("row"), .matrixcols(25), .matrixrows(30), .persist(0), .dotshape("square")) dotmatrix_3 (
    .row0({25{1'b1}}), .row1(25'h15ad6b5), .row2({25{1'b1}}), .row3(25'h15ad6b5), .row4({25{1'b1}}),
    .row5({25{1'b1}}), .row6(25'h15ad6b5), .row7({25{1'b1}}), .row8(25'h15ad6b5), .row9({25{1'b1}}),
    .row10({25{1'b1}}), .row11(25'h15ad6b5), .row12({25{1'b1}}), .row13(25'h15ad6b5), .row14({25{1'b1}}),
    .row15({25{1'b1}}), .row16(25'h15ad6b5), .row17({25{1'b1}}), .row18(25'h15ad6b5), .row19({25{1'b1}}),
    .row20({25{1'b1}}), .row21(25'h15ad6b5), .row22({25{1'b1}}), .row23(25'h15ad6b5), .row24({25{1'b1}}),
    .row25({25{1'b1}}), .row26(25'h15ad6b5), .row27({25{1'b1}}), .row28(25'h15ad6b5), .row29({25{1'b1}}));
  \单周期硬布线控制器  \u_单周期硬布线控制器_1  (
    .Funct({IR[30], IR[25], IR[14:12]}), .OP(IR[6:2]), .ALU_OP(AluOP), .MemToReg(MemToReg),
    .MemWrite(MemWrite), .ALU_SRC(AluSrcB), .RegWrite(RegWrite), .ecall(ecall), .S_type(S_Type), .Jalr(JALR),
    .Beq(Beq), .JAL(JAL), .Bne(Bne), .in_3(IR[21]), .blt(blt), .U_type(U_type), .lhu(lhu));  // open: uret, csrrsi, csrrci
  Multiplexer #(.select(1), .width(5), .disabled("Z"), .enable("false")) multiplexer_4 (
    .in0(IR[24:20]), .in1(5'b01010), .out(multiplexer_4_out), .sel(ecall));
  assign bit_extender_1_out = {{20{IR[31]}}, IR[31:20]};  // Bit_Extender bit_extender_1
  assign bit_extender_2_out = {{20{IR[31]}}, {IR[31:25], IR[11:7]}};  // Bit_Extender bit_extender_2
  assign bit_extender_3_out = {{12{IR[31]}}, IR[31:12]};  // Bit_Extender bit_extender_3
  assign bit_extender_4_out = {{20{IR[31]}}, {IR[31], IR[7], IR[30:25], IR[11:8]}};  // Bit_Extender bit_extender_4
  assign bit_extender_5_out = {{12{IR[31]}}, {IR[31], IR[19:12], IR[20], IR[30:21]}};  // Bit_Extender bit_extender_5
  DotMatrix #(.inputtype("row"), .matrixcols(5), .matrixrows(5), .persist(0), .dotshape("square")) dotmatrix_4 (
    .row0(5'b00100), .row1(5'b01110), .row2(5'b10101), .row3(5'b00100), .row4(5'b01010));
  DotMatrix #(.inputtype("row"), .matrixcols(5), .matrixrows(5), .persist(0), .dotshape("square")) dotmatrix_5 (
    .row0({5{1'b0}}), .row1({5{1'b0}}), .row2({5{1'b0}}), .row3({5{1'b0}}), .row4({5{1'b0}}));
  Multiplexer #(.select(1), .width(32), .disabled("Z"), .enable("false")) multiplexer_5 (
    .in0(bit_extender_1_out), .in1(bit_extender_2_out), .out(multiplexer_5_out), .sel(S_Type));
  Shifter #(.width(32), .shift("ll")) shifter_1 (.in(bit_extender_3_out), .\dist (5'b01100), .out(shifter_1_out));
  Regifile regifile_1 (
    .Din(RDin), .Clk(CLK), .R1(R1), .R2(MDin), .WE(RegWrite), .W_num(IR[11:7]), .R1_num(multiplexer_3_out),
    .R2_num(multiplexer_4_out));
  Shifter #(.width(32), .shift("ll")) shifter_2 (.in(bit_extender_4_out), .\dist (5'b00001), .out(shifter_2_out));
  Shifter #(.width(32), .shift("ll")) shifter_3 (.in(bit_extender_5_out), .\dist (5'b00001), .out(shifter_3_out));
  DotMatrix #(.inputtype("row"), .matrixcols(25), .matrixrows(5), .persist(0), .dotshape("square")) dotmatrix_6 (
    .row0({25{1'b1}}), .row1(25'h15ad6b5), .row2({25{1'b1}}), .row3(25'h15ad6b5), .row4({25{1'b1}}));
  DotMatrix #(.inputtype("row"), .matrixcols(15), .matrixrows(20), .persist(0), .dotshape("square")) dotmatrix_7 (
    .row0(x20), .row1(x19), .row2(x18), .row3(x17), .row4(x16), .row5(x15), .row6(x14), .row7(x13),
    .row8(x12), .row9(x11), .row10(x10), .row11(x9), .row12(x8), .row13(x7), .row14(x6), .row15(x5),
    .row16(x4), .row17(x3), .row18(x2), .row19(x1));
  DotMatrix #(.inputtype("row"), .matrixcols(25), .matrixrows(5), .persist(0), .dotshape("square")) dotmatrix_8 (
    .row0({25{1'b1}}), .row1(25'h15ad6b5), .row2({25{1'b1}}), .row3(25'h15ad6b5), .row4({25{1'b1}}));
  Multiplexer #(.select(1), .width(32), .disabled("Z"), .enable("false")) multiplexer_6 (
    .in0(MDin), .in1(multiplexer_5_out), .out(multiplexer_6_out), .sel(AluSrcB));
  Multiplexer #(.select(1), .width(32), .disabled("Z"), .enable("false")) multiplexer_7 (
    .in0(result), .in1(adder_2_out), .out(multiplexer_7_out), .sel(U_type));
  Adder #(.width(32)) adder_2 (.a(shifter_1_out), .b(PC), .out(adder_2_out));  // open: cin, cout
  Adder #(.width(32)) adder_3 (.a(shifter_2_out), .b(PC), .out(b_t));  // open: cin, cout
  Adder #(.width(32)) adder_4 (.a(shifter_3_out), .b(PC), .out(jal_t));  // open: cin, cout
  assign jalr_t = aluresult & 32'hfffffffe;  // AND_Gate and_3, 32 bits wide
  DotMatrix #(.inputtype("row"), .matrixcols(5), .matrixrows(5), .persist(0), .dotshape("square")) dotmatrix_9 (
    .row0({5{1'b1}}), .row1(5'b10101), .row2(5'b11011), .row3(5'b10101), .row4({5{1'b1}}));
  DotMatrix #(.inputtype("row"), .matrixcols(5), .matrixrows(5), .persist(0), .dotshape("square")) dotmatrix_10 (
    .row0({5{1'b1}}), .row1({5{1'b1}}), .row2({5{1'b1}}), .row3({5{1'b1}}), .row4({5{1'b1}}));
  DotMatrix #(.inputtype("row"), .matrixcols(5), .matrixrows(5), .persist(0), .dotshape("square")) dotmatrix_11 (
    .row0(5'b00100), .row1(5'b01110), .row2(5'b10101), .row3(5'b01110), .row4(5'b01110));
  ALU alu_1 (
    .X(R1), .Y(multiplexer_6_out), .AluOP(AluOP), .Equal(equal), .Result(aluresult), .out_6(less));  // open: Result_2, out_4
  Multiplexer #(.select(1), .width(32), .disabled("Z"), .enable("false")) multiplexer_8 (
    .in0(multiplexer_7_out), .in1(PC_4), .out(multiplexer_8_out), .sel(J));
  DotMatrix #(.inputtype("row"), .matrixcols(10), .matrixrows(20), .persist(0), .dotshape("square")) dotmatrix_12 (
    .row0({10{1'b1}}), .row1(10'h2b5), .row2({10{1'b1}}), .row3(10'h2b5), .row4({10{1'b1}}),
    .row5({10{1'b1}}), .row6(10'h2b5), .row7({10{1'b1}}), .row8(10'h2b5), .row9({10{1'b1}}),
    .row10({10{1'b1}}), .row11(10'h2b5), .row12({10{1'b1}}), .row13(10'h2b5), .row14({10{1'b1}}),
    .row15({10{1'b1}}), .row16(10'h2b5), .row17({10{1'b1}}), .row18(10'h2b5), .row19({10{1'b1}}));
  not not_3 (not_3_out, halt);
  Multiplexer #(.select(1), .width(16), .disabled("Z"), .enable("false")) multiplexer_9 (
    .in0(MDout[15:0]), .in1(MDout[31:16]), .out(multiplexer_9_out), .sel(aluresult[1]));
  not not_4 (not_4_out, equal);
  or or_3 (or_3_out, Go, not_3_out);
  Counter #(.width(16), .max('hffff), .ongoal("wrap"), .trigger("rising"), .behavior("new")) counter_1 (
    .count(or_3_out), .Q(\总周期数 ), .clk(CLK), .clr(RST));  // open: load, D, carry, preset, down
  not not_5 (not_5_out, MemWrite);
  Multiplexer #(.select(1), .width(32), .disabled("Z"), .enable("false")) multiplexer_10 (
    .in0(multiplexer_8_out), .in1(bit_extender_6_out), .out(RDin), .sel(lhu));
  assign bit_extender_6_out = {{16{1'b0}}, multiplexer_9_out};  // Bit_Extender bit_extender_6
  and and_4 (and_4_out, blt, less);
  and and_5 (and_5_out, Bne, not_4_out);
  and and_6 (and_6_out, Beq, equal);
  RAM #(.addrWidth(10), .dataWidth(32), .bus("separate"), .Select("high")) ram_1 (
    .addr(aluresult[11:2]), .din(MDin), .data(MDout), .str(MemWrite), .clk(CLK), .ld(not_5_out));  // open: sel, clr
  Multiplexer #(.select(1), .width(32), .disabled("Z"), .enable("false")) multiplexer_11 (
    .in0(aluresult), .in1(MDout), .out(result), .sel(MemToReg));
  or or_4 (B, and_4_out, or_5_out);
  or or_5 (or_5_out, and_5_out, and_6_out);
  Comparator #(.width(5), .mode("unsigned")) comparator_2 (
    .a(IR[11:7]), .b({5{1'b0}}), .eq(comparator_2_eq));  // open: gt, lt
  Comparator #(.width(5), .mode("unsigned")) comparator_3 (
    .a(IR[11:7]), .b(5'b00001), .eq(comparator_3_eq));  // open: gt, lt
  Comparator #(.width(5), .mode("unsigned")) comparator_4 (
    .a(IR[11:7]), .b(5'b00010), .eq(comparator_4_eq));  // open: gt, lt
  and and_7 (and_7_out, comparator_2_eq, RegWrite);
  Register #(.width(32), .trigger("rising"), .Select("low")) \y0状态  (
    .D(RDin), .en(and_8_out), .Q({y_0, s00, s10, s20}), .clk(CLK), .clr(RST));
  and and_8 (and_8_out, comparator_3_eq, RegWrite);
  Multiplexer #(.select(3), .width(32), .disabled("Z"), .enable("false")) multiplexer_12 (
    .in0({32{1'b0}}), .in1(32'h23aa4500), .in2(32'hfd775f80), .in3(32'h22a2a200), .in4(32'h23aae700),
    .in5({32{1'b1}}), .out(v00), .sel(s00));  // open: in6, in7
  Multiplexer #(.select(3), .width(32), .disabled("Z"), .enable("false")) multiplexer_13 (
    .in0({32{1'b0}}), .in1(32'h23aa4500), .in2(32'hfd775f80), .in3(32'h22a2a200), .in4(32'h23aae700),
    .in5({32{1'b1}}), .out(v10), .sel(s10));  // open: in6, in7
  Multiplexer #(.select(3), .width(32), .disabled("Z"), .enable("false")) multiplexer_14 (
    .in0({32{1'b0}}), .in1(32'h23aa4500), .in2(32'hfd775f80), .in3(32'h22a2a200), .in4(32'h23aae700),
    .in5({32{1'b1}}), .out(v20), .sel(s20));  // open: in6, in7
  Register #(.width(32), .trigger("rising"), .Select("low")) \y1状态  (
    .D(RDin), .en(and_9_out), .Q({y_1, s01, s11, s21}), .clk(CLK), .clr(RST));
  and and_9 (and_9_out, comparator_4_eq, RegWrite);
  Multiplexer #(.select(3), .width(32), .disabled("Z"), .enable("false")) multiplexer_15 (
    .in0({32{1'b0}}), .in1(32'h23aa4500), .in2(32'hfd775f80), .in3(32'h22a2a200), .in4(32'h23aae700),
    .in5({32{1'b1}}), .out(v01), .sel(s01));  // open: in6, in7
  Multiplexer #(.select(3), .width(32), .disabled("Z"), .enable("false")) multiplexer_16 (
    .in0({32{1'b0}}), .in1(32'h23aa4500), .in2(32'hfd775f80), .in3(32'h22a2a200), .in4(32'h23aae700),
    .in5({32{1'b1}}), .out(v11), .sel(s11));  // open: in6, in7
  Multiplexer #(.select(3), .width(32), .disabled("Z"), .enable("false")) multiplexer_17 (
    .in0({32{1'b0}}), .in1(32'h23aa4500), .in2(32'hfd775f80), .in3(32'h22a2a200), .in4(32'h23aae700),
    .in5({32{1'b1}}), .out(v21), .sel(s21));  // open: in6, in7
  Register #(.width(32), .trigger("rising"), .Select("low")) \u_人物坐标  (
    .D(RDin), .en(and_7_out), .Q(Loc), .clk(CLK), .clr(RST));
  assign bit_extender_7_out = {{10{1'b0}}, v00[11:7]};  // Bit_Extender bit_extender_7
  assign bit_extender_8_out = {{10{1'b0}}, v10[11:7]};  // Bit_Extender bit_extender_8
  assign bit_extender_9_out = {{10{1'b0}}, v20[11:7]};  // Bit_Extender bit_extender_9
  assign bit_extender_10_out = {{10{1'b0}}, v00[16:12]};  // Bit_Extender bit_extender_10
  assign bit_extender_11_out = {{10{1'b0}}, v10[16:12]};  // Bit_Extender bit_extender_11
  assign bit_extender_12_out = {{10{1'b0}}, v20[16:12]};  // Bit_Extender bit_extender_12
  assign bit_extender_13_out = {{10{1'b0}}, v00[21:17]};  // Bit_Extender bit_extender_13
  assign bit_extender_14_out = {{10{1'b0}}, v10[21:17]};  // Bit_Extender bit_extender_14
  assign bit_extender_15_out = {{10{1'b0}}, v20[21:17]};  // Bit_Extender bit_extender_15
  assign bit_extender_16_out = {{10{1'b0}}, v00[26:22]};  // Bit_Extender bit_extender_16
  assign bit_extender_17_out = {{10{1'b0}}, v10[26:22]};  // Bit_Extender bit_extender_17
  assign bit_extender_18_out = {{10{1'b0}}, v20[26:22]};  // Bit_Extender bit_extender_18
  assign bit_extender_19_out = {{10{1'b0}}, v00[31:27]};  // Bit_Extender bit_extender_19
  assign bit_extender_20_out = {{10{1'b0}}, v10[31:27]};  // Bit_Extender bit_extender_20
  assign bit_extender_21_out = {{10{1'b0}}, v20[31:27]};  // Bit_Extender bit_extender_21
  assign bit_extender_22_out = {{10{1'b0}}, v01[11:7]};  // Bit_Extender bit_extender_22
  assign bit_extender_23_out = {{10{1'b0}}, v11[11:7]};  // Bit_Extender bit_extender_23
  assign bit_extender_24_out = {{10{1'b0}}, v21[11:7]};  // Bit_Extender bit_extender_24
  assign bit_extender_25_out = {{10{1'b0}}, v01[16:12]};  // Bit_Extender bit_extender_25
  assign bit_extender_26_out = {{10{1'b0}}, v11[16:12]};  // Bit_Extender bit_extender_26
  assign bit_extender_27_out = {{10{1'b0}}, v21[16:12]};  // Bit_Extender bit_extender_27
  assign bit_extender_28_out = {{10{1'b0}}, v01[21:17]};  // Bit_Extender bit_extender_28
  assign bit_extender_29_out = {{10{1'b0}}, v11[21:17]};  // Bit_Extender bit_extender_29
  assign bit_extender_30_out = {{10{1'b0}}, v21[21:17]};  // Bit_Extender bit_extender_30
  assign bit_extender_31_out = {{10{1'b0}}, v01[26:22]};  // Bit_Extender bit_extender_31
  assign bit_extender_32_out = {{10{1'b0}}, v11[26:22]};  // Bit_Extender bit_extender_32
  assign bit_extender_33_out = {{10{1'b0}}, v21[26:22]};  // Bit_Extender bit_extender_33
  assign bit_extender_34_out = {{10{1'b0}}, v01[31:27]};  // Bit_Extender bit_extender_34
  assign bit_extender_35_out = {{10{1'b0}}, v11[31:27]};  // Bit_Extender bit_extender_35
  assign bit_extender_36_out = {{10{1'b0}}, v21[31:27]};  // Bit_Extender bit_extender_36
  Shifter #(.width(15), .shift("ll")) shifter_4 (.in(bit_extender_7_out), .\dist (4'b1010), .out(shifter_4_out));
  Shifter #(.width(15), .shift("ll")) shifter_5 (.in(bit_extender_8_out), .\dist (4'b0101), .out(shifter_5_out));
  Shifter #(.width(15), .shift("ll")) shifter_6 (.in(bit_extender_10_out), .\dist (4'b1010), .out(shifter_6_out));
  Shifter #(.width(15), .shift("ll")) shifter_7 (.in(bit_extender_11_out), .\dist (4'b0101), .out(shifter_7_out));
  Shifter #(.width(15), .shift("ll")) shifter_8 (.in(bit_extender_13_out), .\dist (4'b1010), .out(shifter_8_out));
  Shifter #(.width(15), .shift("ll")) shifter_9 (.in(bit_extender_14_out), .\dist (4'b0101), .out(shifter_9_out));
  Shifter #(.width(15), .shift("ll")) shifter_10 (.in(bit_extender_16_out), .\dist (4'b1010), .out(shifter_10_out));
  Shifter #(.width(15), .shift("ll")) shifter_11 (.in(bit_extender_17_out), .\dist (4'b0101), .out(shifter_11_out));
  Shifter #(.width(15), .shift("ll")) shifter_12 (.in(bit_extender_19_out), .\dist (4'b1010), .out(shifter_12_out));
  Shifter #(.width(15), .shift("ll")) shifter_13 (.in(bit_extender_20_out), .\dist (4'b0101), .out(shifter_13_out));
  Shifter #(.width(15), .shift("ll")) shifter_14 (.in(bit_extender_22_out), .\dist (4'b1010), .out(shifter_14_out));
  Shifter #(.width(15), .shift("ll")) shifter_15 (.in(bit_extender_23_out), .\dist (4'b0101), .out(shifter_15_out));
  Shifter #(.width(15), .shift("ll")) shifter_16 (.in(bit_extender_25_out), .\dist (4'b1010), .out(shifter_16_out));
  Shifter #(.width(15), .shift("ll")) shifter_17 (.in(bit_extender_26_out), .\dist (4'b0101), .out(shifter_17_out));
  Shifter #(.width(15), .shift("ll")) shifter_18 (.in(bit_extender_28_out), .\dist (4'b1010), .out(shifter_18_out));
  Shifter #(.width(15), .shift("ll")) shifter_19 (.in(bit_extender_29_out), .\dist (4'b0101), .out(shifter_19_out));
  Shifter #(.width(15), .shift("ll")) shifter_20 (.in(bit_extender_31_out), .\dist (4'b1010), .out(shifter_20_out));
  Shifter #(.width(15), .shift("ll")) shifter_21 (.in(bit_extender_32_out), .\dist (4'b0101), .out(shifter_21_out));
  Shifter #(.width(15), .shift("ll")) shifter_22 (.in(bit_extender_34_out), .\dist (4'b1010), .out(shifter_22_out));
  Shifter #(.width(15), .shift("ll")) shifter_23 (.in(bit_extender_35_out), .\dist (4'b0101), .out(shifter_23_out));
  assign x1 = shifter_4_out | shifter_5_out | bit_extender_9_out;  // OR_Gate or_6, 15 bits wide
  assign x2 = shifter_6_out | shifter_7_out | bit_extender_12_out;  // OR_Gate or_7, 15 bits wide
  assign x3 = shifter_8_out | shifter_9_out | bit_extender_15_out;  // OR_Gate or_8, 15 bits wide
  assign x4 = shifter_10_out | shifter_11_out | bit_extender_18_out;  // OR_Gate or_9, 15 bits wide
  assign x5 = shifter_12_out | shifter_13_out | bit_extender_21_out;  // OR_Gate or_10, 15 bits wide
  assign x6 = shifter_14_out | shifter_15_out | bit_extender_24_out;  // OR_Gate or_11, 15 bits wide
  assign x7 = shifter_16_out | shifter_17_out | bit_extender_27_out;  // OR_Gate or_12, 15 bits wide
  assign x8 = shifter_18_out | shifter_19_out | bit_extender_30_out;  // OR_Gate or_13, 15 bits wide
  assign x9 = shifter_20_out | shifter_21_out | bit_extender_33_out;  // OR_Gate or_14, 15 bits wide
  assign x10 = shifter_22_out | shifter_23_out | bit_extender_36_out;  // OR_Gate or_15, 15 bits wide
  Comparator #(.width(5), .mode("unsigned")) comparator_5 (
    .a(IR[11:7]), .b(5'b00011), .eq(comparator_5_eq));  // open: gt, lt
  and and_10 (and_10_out, comparator_5_eq, RegWrite);
  Multiplexer #(.select(3), .width(32), .disabled("Z"), .enable("false")) multiplexer_18 (
    .in0({32{1'b0}}), .in1(32'h23aa4500), .in2(32'hfd775f80), .in3(32'h22a2a200), .in4(32'h23aae700),
    .in5({32{1'b1}}), .out(v02), .sel(s02));  // open: in6, in7
  Multiplexer #(.select(3), .width(32), .disabled("Z"), .enable("false")) multiplexer_19 (
    .in0({32{1'b0}}), .in1(32'h23aa4500), .in2(32'hfd775f80), .in3(32'h22a2a200), .in4(32'h23aae700),
    .in5({32{1'b1}}), .out(v12), .sel(s12));  // open: in6, in7
  Multiplexer #(.select(3), .width(32), .disabled("Z"), .enable("false")) multiplexer_20 (
    .in0({32{1'b0}}), .in1(32'h23aa4500), .in2(32'hfd775f80), .in3(32'h22a2a200), .in4(32'h23aae700),
    .in5({32{1'b1}}), .out(v22), .sel(s22));  // open: in6, in7
  Comparator #(.width(5), .mode("unsigned")) comparator_6 (
    .a(IR[11:7]), .b(5'b00100), .eq(comparator_6_eq));  // open: gt, lt
  and and_11 (and_11_out, comparator_6_eq, RegWrite);
  Multiplexer #(.select(3), .width(32), .disabled("Z"), .enable("false")) multiplexer_21 (
    .in0({32{1'b0}}), .in1(32'h23aa4500), .in2(32'hfd775f80), .in3(32'h22a2a200), .in4(32'h23aae700),
    .in5({32{1'b1}}), .out(v03), .sel(s03));  // open: in6, in7
  Multiplexer #(.select(3), .width(32), .disabled("Z"), .enable("false")) multiplexer_22 (
    .in0({32{1'b0}}), .in1(32'h23aa4500), .in2(32'hfd775f80), .in3(32'h22a2a200), .in4(32'h23aae700),
    .in5({32{1'b1}}), .out(v13), .sel(s13));  // open: in6, in7
  Multiplexer #(.select(3), .width(32), .disabled("Z"), .enable("false")) multiplexer_23 (
    .in0({32{1'b0}}), .in1(32'h23aa4500), .in2(32'hfd775f80), .in3(32'h22a2a200), .in4(32'h23aae700),
    .in5({32{1'b1}}), .out(v23), .sel(s23));  // open: in6, in7
  Register #(.width(32), .trigger("rising"), .Select("low")) \y2状态  (
    .D(RDin), .en(and_10_out), .Q({y_2, s02, s12, s22}), .clk(CLK), .clr(RST));
  Register #(.width(32), .trigger("rising"), .Select("low")) \y3状态  (
    .D(RDin), .en(and_11_out), .Q({y_3, s03, s13, s23}), .clk(CLK), .clr(RST));
  assign bit_extender_37_out = {{10{1'b0}}, v02[11:7]};  // Bit_Extender bit_extender_37
  assign bit_extender_38_out = {{10{1'b0}}, v12[11:7]};  // Bit_Extender bit_extender_38
  assign bit_extender_39_out = {{10{1'b0}}, v22[11:7]};  // Bit_Extender bit_extender_39
  assign bit_extender_40_out = {{10{1'b0}}, v02[16:12]};  // Bit_Extender bit_extender_40
  assign bit_extender_41_out = {{10{1'b0}}, v12[16:12]};  // Bit_Extender bit_extender_41
  assign bit_extender_42_out = {{10{1'b0}}, v22[16:12]};  // Bit_Extender bit_extender_42
  assign bit_extender_43_out = {{10{1'b0}}, v02[21:17]};  // Bit_Extender bit_extender_43
  assign bit_extender_44_out = {{10{1'b0}}, v12[21:17]};  // Bit_Extender bit_extender_44
  assign bit_extender_45_out = {{10{1'b0}}, v22[21:17]};  // Bit_Extender bit_extender_45
  assign bit_extender_46_out = {{10{1'b0}}, v02[26:22]};  // Bit_Extender bit_extender_46
  assign bit_extender_47_out = {{10{1'b0}}, v12[26:22]};  // Bit_Extender bit_extender_47
  assign bit_extender_48_out = {{10{1'b0}}, v22[26:22]};  // Bit_Extender bit_extender_48
  assign bit_extender_49_out = {{10{1'b0}}, v02[31:27]};  // Bit_Extender bit_extender_49
  assign bit_extender_50_out = {{10{1'b0}}, v12[31:27]};  // Bit_Extender bit_extender_50
  assign bit_extender_51_out = {{10{1'b0}}, v22[31:27]};  // Bit_Extender bit_extender_51
  assign bit_extender_52_out = {{10{1'b0}}, v03[11:7]};  // Bit_Extender bit_extender_52
  assign bit_extender_53_out = {{10{1'b0}}, v13[11:7]};  // Bit_Extender bit_extender_53
  assign bit_extender_54_out = {{10{1'b0}}, v23[11:7]};  // Bit_Extender bit_extender_54
  assign bit_extender_55_out = {{10{1'b0}}, v03[16:12]};  // Bit_Extender bit_extender_55
  assign bit_extender_56_out = {{10{1'b0}}, v13[16:12]};  // Bit_Extender bit_extender_56
  assign bit_extender_57_out = {{10{1'b0}}, v23[16:12]};  // Bit_Extender bit_extender_57
  assign bit_extender_58_out = {{10{1'b0}}, v03[21:17]};  // Bit_Extender bit_extender_58
  assign bit_extender_59_out = {{10{1'b0}}, v13[21:17]};  // Bit_Extender bit_extender_59
  assign bit_extender_60_out = {{10{1'b0}}, v23[21:17]};  // Bit_Extender bit_extender_60
  assign bit_extender_61_out = {{10{1'b0}}, v03[26:22]};  // Bit_Extender bit_extender_61
  assign bit_extender_62_out = {{10{1'b0}}, v13[26:22]};  // Bit_Extender bit_extender_62
  assign bit_extender_63_out = {{10{1'b0}}, v23[26:22]};  // Bit_Extender bit_extender_63
  assign bit_extender_64_out = {{10{1'b0}}, v03[31:27]};  // Bit_Extender bit_extender_64
  assign bit_extender_65_out = {{10{1'b0}}, v13[31:27]};  // Bit_Extender bit_extender_65
  assign bit_extender_66_out = {{10{1'b0}}, v23[31:27]};  // Bit_Extender bit_extender_66
  Shifter #(.width(15), .shift("ll")) shifter_24 (.in(bit_extender_37_out), .\dist (4'b1010), .out(shifter_24_out));
  Shifter #(.width(15), .shift("ll")) shifter_25 (.in(bit_extender_38_out), .\dist (4'b0101), .out(shifter_25_out));
  Shifter #(.width(15), .shift("ll")) shifter_26 (.in(bit_extender_40_out), .\dist (4'b1010), .out(shifter_26_out));
  Shifter #(.width(15), .shift("ll")) shifter_27 (.in(bit_extender_41_out), .\dist (4'b0101), .out(shifter_27_out));
  Shifter #(.width(15), .shift("ll")) shifter_28 (.in(bit_extender_43_out), .\dist (4'b1010), .out(shifter_28_out));
  Shifter #(.width(15), .shift("ll")) shifter_29 (.in(bit_extender_44_out), .\dist (4'b0101), .out(shifter_29_out));
  Shifter #(.width(15), .shift("ll")) shifter_30 (.in(bit_extender_46_out), .\dist (4'b1010), .out(shifter_30_out));
  Shifter #(.width(15), .shift("ll")) shifter_31 (.in(bit_extender_47_out), .\dist (4'b0101), .out(shifter_31_out));
  Shifter #(.width(15), .shift("ll")) shifter_32 (.in(bit_extender_49_out), .\dist (4'b1010), .out(shifter_32_out));
  Shifter #(.width(15), .shift("ll")) shifter_33 (.in(bit_extender_50_out), .\dist (4'b0101), .out(shifter_33_out));
  Shifter #(.width(15), .shift("ll")) shifter_34 (.in(bit_extender_52_out), .\dist (4'b1010), .out(shifter_34_out));
  Shifter #(.width(15), .shift("ll")) shifter_35 (.in(bit_extender_53_out), .\dist (4'b0101), .out(shifter_35_out));
  Shifter #(.width(15), .shift("ll")) shifter_36 (.in(bit_extender_55_out), .\dist (4'b1010), .out(shifter_36_out));
  Shifter #(.width(15), .shift("ll")) shifter_37 (.in(bit_extender_56_out), .\dist (4'b0101), .out(shifter_37_out));
  Shifter #(.width(15), .shift("ll")) shifter_38 (.in(bit_extender_58_out), .\dist (4'b1010), .out(shifter_38_out));
  Shifter #(.width(15), .shift("ll")) shifter_39 (.in(bit_extender_59_out), .\dist (4'b0101), .out(shifter_39_out));
  Shifter #(.width(15), .shift("ll")) shifter_40 (.in(bit_extender_61_out), .\dist (4'b1010), .out(shifter_40_out));
  Shifter #(.width(15), .shift("ll")) shifter_41 (.in(bit_extender_62_out), .\dist (4'b0101), .out(shifter_41_out));
  Shifter #(.width(15), .shift("ll")) shifter_42 (.in(bit_extender_64_out), .\dist (4'b1010), .out(shifter_42_out));
  Shifter #(.width(15), .shift("ll")) shifter_43 (.in(bit_extender_65_out), .\dist (4'b0101), .out(shifter_43_out));
  assign x11 = shifter_24_out | shifter_25_out | bit_extender_39_out;  // OR_Gate or_16, 15 bits wide
  assign x12 = shifter_26_out | shifter_27_out | bit_extender_42_out;  // OR_Gate or_17, 15 bits wide
  assign x13 = shifter_28_out | shifter_29_out | bit_extender_45_out;  // OR_Gate or_18, 15 bits wide
  assign x14 = shifter_30_out | shifter_31_out | bit_extender_48_out;  // OR_Gate or_19, 15 bits wide
  assign x15 = shifter_32_out | shifter_33_out | bit_extender_51_out;  // OR_Gate or_20, 15 bits wide
  assign x16 = shifter_34_out | shifter_35_out | bit_extender_54_out;  // OR_Gate or_21, 15 bits wide
  assign x17 = shifter_36_out | shifter_37_out | bit_extender_57_out;  // OR_Gate or_22, 15 bits wide
  assign x18 = shifter_38_out | shifter_39_out | bit_extender_60_out;  // OR_Gate or_23, 15 bits wide
  assign x19 = shifter_40_out | shifter_41_out | bit_extender_63_out;  // OR_Gate or_24, 15 bits wide
  assign x20 = shifter_42_out | shifter_43_out | bit_extender_66_out;  // OR_Gate or_25, 15 bits wide

  // Other names for the same wires on the sheet: W_num[4:0] = IR[11:7]; ly[1:0] = Loc[1:0]; lx[1:0] = Loc[3:2];
  //   R2[31:0] = MDin; v001[4:0] = v00[11:7]; v002[4:0] = v00[16:12]; v003[4:0] = v00[21:17]; v004[4:0] = v00[26:22];
  //   v005[4:0] = v00[31:27]; v011[4:0] = v01[11:7]; v012[4:0] = v01[16:12]; v013[4:0] = v01[21:17];
  //   v014[4:0] = v01[26:22]; v015[4:0] = v01[31:27]; v021[4:0] = v02[11:7]; v022[4:0] = v02[16:12];
  //   v023[4:0] = v02[21:17]; v024[4:0] = v02[26:22]; v025[4:0] = v02[31:27]; v031[4:0] = v03[11:7];
  //   v032[4:0] = v03[16:12]; v033[4:0] = v03[21:17]; v034[4:0] = v03[26:22]; v035[4:0] = v03[31:27];
  //   v101[4:0] = v10[11:7]; v102[4:0] = v10[16:12]; v103[4:0] = v10[21:17]; v104[4:0] = v10[26:22];
  //   v105[4:0] = v10[31:27]; v111[4:0] = v11[11:7]; v112[4:0] = v11[16:12]; v113[4:0] = v11[21:17];
  //   v114[4:0] = v11[26:22]; v115[4:0] = v11[31:27]; v121[4:0] = v12[11:7]; v122[4:0] = v12[16:12];
  //   v123[4:0] = v12[21:17]; v124[4:0] = v12[26:22]; v125[4:0] = v12[31:27]; v131[4:0] = v13[11:7];
  //   v132[4:0] = v13[16:12]; v133[4:0] = v13[21:17]; v134[4:0] = v13[26:22]; v135[4:0] = v13[31:27];
  //   v201[4:0] = v20[11:7]; v202[4:0] = v20[16:12]; v203[4:0] = v20[21:17]; v204[4:0] = v20[26:22];
  //   v205[4:0] = v20[31:27]; v211[4:0] = v21[11:7]; v212[4:0] = v21[16:12]; v213[4:0] = v21[21:17];
  //   v214[4:0] = v21[26:22]; v215[4:0] = v21[31:27]; v221[4:0] = v22[11:7]; v222[4:0] = v22[16:12];
  //   v223[4:0] = v22[21:17]; v224[4:0] = v22[26:22]; v225[4:0] = v22[31:27]; v231[4:0] = v23[11:7];
  //   v232[4:0] = v23[16:12]; v233[4:0] = v23[21:17]; v234[4:0] = v23[26:22]; v235[4:0] = v23[31:27];
  //   y_0[8:0] = {s00, s10, s20}; y_1[8:0] = {s01, s11, s21}; y_2[8:0] = {s02, s12, s22}; y_3[8:0] = {s03, s13, s23}

  // Notes on the sheet:
  //   指令探针
  //   指令存储器
  //   指令字
  //   contents of rom_1 (hex, n*v repeats v):
  //   1300093 1000113 d000193 c100213 693 100713 ffdff06f
  //   JAL
  //   JALR
  //   URET
  //   I型
  //   S型
  //   U型
  //   B型Imm
  //   J型Imm
  //   Beq
  //   Bne
  //   MemToReg
  //   MemWrite
  //   AluOP
  //   AluSrcB
  //   RegWrite
  //   S_Type
  //   auipc
  //   beq/bne/blt
  //   jal
  //   jalr
  //   数据存储器
  //   游戏界面
  //   转换到显示逻辑
endmodule

module \单周期RISC_V  (
  input  IR1,
  input  IR2,
  input  IR3,
  output RegWrite,
  output MemWrite,
  output [31:0] PC,
  output [31:0] IR,
  output [31:0] RDin,
  output [31:0] MDin,
  output [31:0] LedData
);

  wire AluSrcB, and_4_out, and_5_out, and_6_out, B, Beq, blt, Bne, CLK, clock_1_out, comparator_1_eq,
       comparator_2_eq, comparator_2_lt, d_ff_1_q, ecall, en, equal, Go, halt, IR1_t, IR2_t, IR3_t, IRA, IRB,
       IRC, J, JAL, JALR, less, lhu, MemToReg, nand_1_out, not_1_out, not_2_out, not_3_out, not_4_out,
       not_5_out, or_1_out, or_6_out, or_8_out, RST, S_Type, U_type, W1, W2, W3;
  wire [1:0] priority_encoder_1_out;
  wire [3:0] AluOP;
  wire [4:0] multiplexer_3_out, multiplexer_4_out;
  wire [12:0] CNT_num;
  wire [15:0] multiplexer_9_out, \总周期数 ;
  wire [31:0] adder_2_out, aluresult, b_t, bit_extender_1_out, bit_extender_2_out, bit_extender_3_out,
       bit_extender_4_out, bit_extender_5_out, bit_extender_6_out, jal_t, jalr_t, MDout, multiplexer_1_out,
       multiplexer_2_out, multiplexer_5_out, multiplexer_6_out, multiplexer_7_out, multiplexer_8_out, PC_4,
       R1, result, shifter_1_out, shifter_2_out, shifter_3_out;

  Button \u_继续运行  (.out(Go));
  Button _1 (.out(IRA));
  Button _2 (.out(IRB));
  Button _3 (.out(IRC));
  Button u_RST (.out(RST));
  LED #(.active("true")) led_1 (.in(W1));
  LED #(.active("true")) led_2 (.in(W2));
  LED #(.active("true")) led_3 (.in(W3));
  Priority_Encoder #(.select(2), .disabled("Z")) priority_encoder_1 (
    .in0(1'b1), .in1(B), .in2(JAL), .in3(JALR), .out(priority_encoder_1_out));  // open: gs, en_out, en_in
  Multiplexer #(.select(2), .width(32), .disabled("Z"), .enable("false")) multiplexer_1 (
    .in0(PC_4), .in1(b_t), .in2(jal_t), .in3(jalr_t), .out(multiplexer_1_out), .sel(priority_encoder_1_out));
  Hex_Digit_Display hex_digit_display_1 (.value(LedData[31:28]));  // open: dp
  Register #(.width(32), .trigger("rising"), .Select("low")) u_PC (
    .D(multiplexer_1_out), .en(or_1_out), .Q(PC), .clk(CLK), .clr(RST));
  or or_1 (or_1_out, Go, not_1_out);
  not not_1 (not_1_out, halt);
  Hex_Digit_Display hex_digit_display_2 (.value(LedData[27:24]));  // open: dp
  Hex_Digit_Display hex_digit_display_3 (.value(LedData[23:20]));  // open: dp
  Adder #(.width(32)) adder_1 (.a(PC), .b(32'h4), .out(PC_4));  // open: cin, cout
  Comparator #(.width(32), .mode("twosComplement")) comparator_1 (
    .a(R1), .b(32'h22), .eq(comparator_1_eq));  // open: gt, lt
  not not_2 (not_2_out, comparator_1_eq);
  and and_1 (halt, not_2_out, ecall);
  Hex_Digit_Display hex_digit_display_4 (.value(LedData[19:16]));  // open: dp
  Hex_Digit_Display hex_digit_display_5 (.value(LedData[15:12]));  // open: dp
  // RiscV_Probe riscv_probe_1: pin names not known; wires that end beside it: IR
  and and_2 (en, ecall, comparator_1_eq);
  Multiplexer #(.select(1), .width(32), .disabled("Z"), .enable("false")) multiplexer_2 (
    .in0({32{1'b0}}), .in1(MDin), .out(multiplexer_2_out), .sel(en));
  Hex_Digit_Display hex_digit_display_6 (.value(LedData[7:4]));  // open: dp
  Hex_Digit_Display hex_digit_display_7 (.value(LedData[11:8]));  // open: dp
  // Probe on \总周期数 
  or or_2 (J, JALR, JAL);
  ROM #(.addrWidth(10), .dataWidth(32), .Select("high")) rom_1 (.addr(PC[11:2]), .data(IR));
  Register #(.width(32), .trigger("rising"), .Select("low")) register_1 (
    .D(multiplexer_2_out), .en(en), .Q(LedData), .clk(CLK), .clr(RST));
  Hex_Digit_Display hex_digit_display_8 (.value(LedData[3:0]));  // open: dp
  \单周期硬布线控制器  \u_单周期硬布线控制器_1  (
    .Funct({IR[30], IR[25], IR[14:12]}), .OP(IR[6:2]), .ALU_OP(AluOP), .MemToReg(MemToReg),
    .MemWrite(MemWrite), .ALU_SRC(AluSrcB), .RegWrite(RegWrite), .ecall(ecall), .S_type(S_Type), .Jalr(JALR),
    .Beq(Beq), .JAL(JAL), .Bne(Bne), .in_3(IR[21]), .blt(blt), .U_type(U_type), .lhu(lhu));  // open: uret, csrrsi, csrrci
  Multiplexer #(.select(1), .width(5), .disabled("Z"), .enable("false")) multiplexer_3 (
    .in0(IR[19:15]), .in1(5'b10001), .out(multiplexer_3_out), .sel(ecall));
  Multiplexer #(.select(1), .width(5), .disabled("Z"), .enable("false")) multiplexer_4 (
    .in0(IR[24:20]), .in1(5'b01010), .out(multiplexer_4_out), .sel(ecall));
  assign bit_extender_1_out = {{20{IR[31]}}, IR[31:20]};  // Bit_Extender bit_extender_1
  assign bit_extender_2_out = {{20{IR[31]}}, {IR[31:25], IR[11:7]}};  // Bit_Extender bit_extender_2
  assign bit_extender_3_out = {{12{IR[31]}}, IR[31:12]};  // Bit_Extender bit_extender_3
  or or_3 (IR1_t, IR1, IRA);
  Multiplexer #(.select(1), .width(32), .disabled("Z"), .enable("false")) multiplexer_5 (
    .in0(bit_extender_1_out), .in1(bit_extender_2_out), .out(multiplexer_5_out), .sel(S_Type));
  Shifter #(.width(32), .shift("ll")) shifter_1 (.in(bit_extender_3_out), .\dist (5'b01100), .out(shifter_1_out));
  assign bit_extender_4_out = {{20{IR[31]}}, {IR[31], IR[7], IR[30:25], IR[11:8]}};  // Bit_Extender bit_extender_4
  assign bit_extender_5_out = {{12{IR[31]}}, {IR[31], IR[19:12], IR[20], IR[30:21]}};  // Bit_Extender bit_extender_5
  or or_4 (IR2_t, IR2, IRB);
  Regifile regifile_1 (
    .Din(RDin), .Clk(CLK), .R1(R1), .R2(MDin), .WE(RegWrite), .W_num(IR[11:7]), .R1_num(multiplexer_3_out),
    .R2_num(multiplexer_4_out));
  Shifter #(.width(32), .shift("ll")) shifter_2 (.in(bit_extender_4_out), .\dist (5'b00001), .out(shifter_2_out));
  Shifter #(.width(32), .shift("ll")) shifter_3 (.in(bit_extender_5_out), .\dist (5'b00001), .out(shifter_3_out));
  Multiplexer #(.select(1), .width(32), .disabled("Z"), .enable("false")) multiplexer_6 (
    .in0(MDin), .in1(multiplexer_5_out), .out(multiplexer_6_out), .sel(AluSrcB));
  Adder #(.width(32)) adder_2 (.a(shifter_1_out), .b(PC), .out(adder_2_out));  // open: cin, cout
  Adder #(.width(32)) adder_3 (.a(shifter_2_out), .b(PC), .out(b_t));  // open: cin, cout
  Adder #(.width(32)) adder_4 (.a(shifter_3_out), .b(PC), .out(jal_t));  // open: cin, cout
  assign jalr_t = aluresult & 32'hfffffffe;  // AND_Gate and_3, 32 bits wide
  or or_5 (IR3_t, IR3, IRC);
  Multiplexer #(.select(1), .width(32), .disabled("Z"), .enable("false")) multiplexer_7 (
    .in0(result), .in1(adder_2_out), .out(multiplexer_7_out), .sel(U_type));
  Multiplexer #(.select(1), .width(32), .disabled("Z"), .enable("false")) multiplexer_8 (
    .in0(multiplexer_7_out), .in1(PC_4), .out(multiplexer_8_out), .sel(J));
  not not_3 (not_3_out, halt);
  ALU alu_1 (
    .X(R1), .Y(multiplexer_6_out), .AluOP(AluOP), .Equal(equal), .Result(aluresult), .out_6(less));  // open: Result_2, out_4
  Multiplexer #(.select(1), .width(16), .disabled("Z"), .enable("false")) multiplexer_9 (
    .in0(MDout[15:0]), .in1(MDout[31:16]), .out(multiplexer_9_out), .sel(aluresult[1]));
  not not_4 (not_4_out, equal);
  or or_6 (or_6_out, Go, not_3_out);
  Counter #(.width(16), .max('hffff), .ongoal("wrap"), .trigger("rising"), .behavior("new")) counter_1 (
    .count(or_6_out), .Q(\总周期数 ), .clk(CLK), .clr(RST));  // open: load, D, carry, preset, down
  not not_5 (not_5_out, MemWrite);
  assign bit_extender_6_out = {{16{1'b0}}, multiplexer_9_out};  // Bit_Extender bit_extender_6
  and and_4 (and_4_out, Bne, not_4_out);
  RAM #(.addrWidth(10), .dataWidth(32), .bus("separate"), .Select("high")) ram_1 (
    .addr(aluresult[11:2]), .din(MDin), .data(MDout), .str(MemWrite), .clk(CLK), .ld(not_5_out));  // open: sel, clr
  Multiplexer #(.select(1), .width(32), .disabled("Z"), .enable("false")) multiplexer_10 (
    .in0(multiplexer_8_out), .in1(bit_extender_6_out), .out(RDin), .sel(lhu));
  and and_5 (and_5_out, blt, less);
  and and_6 (and_6_out, Beq, equal);
  Multiplexer #(.select(1), .width(32), .disabled("Z"), .enable("false")) multiplexer_11 (
    .in0(aluresult), .in1(MDout), .out(result), .sel(MemToReg));
  or or_7 (B, and_5_out, or_8_out);
  or or_8 (or_8_out, and_4_out, and_6_out);
  D_Flip_Flop #(.trigger("high"), .Pre_Clr_Positions("LEGACY"), .NegatePresetClear("false"), .enable("true"), .NewFFLayout("false")) d_ff_1 (.Q(d_ff_1_q));  // open: clk, D, Qn, preset, en, reset
  // Probe on 13'hc
  Comparator #(.width(13), .mode("twosComplement")) comparator_2 (
    .a(CNT_num), .b(13'hc), .eq(comparator_2_eq), .lt(comparator_2_lt));  // open: gt
  Clock #(.highDuration(1), .lowDuration(1)) clock_1 (.out(clock_1_out));
  Counter #(.width(13), .max('h1fff), .ongoal("stay"), .trigger("rising"), .behavior("old")) counter_2 (
    .count(comparator_2_lt), .Q(CNT_num), .clk(clock_1_out));  // open: load, D, carry, clr, preset
  nand nand_1 (nand_1_out, d_ff_1_q, comparator_2_eq);
  assign CLK = nand_1_out ? clock_1_out : 1'bz;  // Controlled_Buffer controlled_buffer_1
  Pull_Resistor #(.pull(1)) pull_resistor_1 (.node(CLK));

  // Other names for the same wires on the sheet: R2[31:0] = MDin

  // Notes on the sheet:
  //   中断源
  //   中断等待指示
  //   数码管输出应该用寄存器锁存，否则显示数据只能一闪而过
  //   数码管输出
  //   指令探针
  //   指令存储器
  //   指令字
  //   contents of rom_1 (hex, n*v repeats v):
  //   100493 100006f 100493 200913 300993 100006f 100493 200913 300993 100006f 100493 200913 300993
  //   100006f 100493 200913 300993 414000ef 100413 100493 1f49493 900533 2200893 73 24d493 48463 fedff06f
  //   900533 2200893 73 100493 249493 900533 2200893 73 48463 fedff06f 100493 1f49493 900533 2200893 73
  //   4034d493 900533 2200893 73 4044d493 900533 2200893 73 4044d493 900533 2200893 73 4044d493 900533
  //   2200893 73 4044d493 900533 2200893 73 4044d493 900533 2200893 73 4044d493 900533 2200893 73 4044d493
  //   900533 2200893 73 100413 1f41993 41f9d993 433 c00913 300b13 140413 f47413 800293 100313 499993
  //   89e9b3 1300533 2200893 73 406282b3 fe0294e3 140413 f00f93 1f47433 1c41413 800293 100313 49d993
  //   89e9b3 1300533 2200893 73 406282b3 fe0294e3 1c45413 406b0b33 b0463 f95ff06f 2b3 fff2c293 829293
  //   ff2e293 500533 2200893 73 fff00413 493 84a023 140413 448493 84a023 140413 448493 84a023 140413
  //   448493 84a023 140413 448493 84a023 140413 448493 84a023 140413 448493 84a023 140413 448493 84a023
  //   140413 448493 84a023 140413 448493 84a023 140413 448493 84a023 140413 448493 84a023 140413 448493
  //   84a023 140413 448493 84a023 140413 448493 84a023 140413 448493 84a023 140413 448493 140413 433
  //   3c00493 42983 4aa03 149a2b3 28663 134a023 1442023 ffc48493 fe9412e3 800533 2200893 73 440413 3c00493
  //   fc9416e3 a00893 73 100293 300313 800493 849493 7648493 1449493 900533 2200893 73 800e13 4054d4b3
  //   4064d4b3 900533 2200893 73 fffe0e13 fe0e14e3 a00893 73 13 430497 900533 2200893 73 430497 900533
  //   2200893 73 430497 900533 2200893 73 430497 900533 2200893 73 430497 900533 2200893 73 430497 900533
  //   2200893 73 430497 900533 2200893 73 430497 900533 2200893 73 a00893 73 313 1000e13 8400493 849493
  //   8348493 400913 891913 490913 849493 8248493 849493 8148493 891913 490913 891913 490913 932023
  //   12484b3 430313 fffe0e13 fe0e18e3 2000e13 313 35483 900533 2200893 73 230313 fffe0e13 fe0e14e3 a00893
  //   73 ff100493 900533 2200893 73 148493 fe04c8e3 a00893 73 413 140413 800533 2200893 73 240413 800533
  //   2200893 73 340413 800533 2200893 73 440413 800533 2200893 73 540413 800533 2200893 73 640413 800533
  //   2200893 73 740413 800533 2200893 73 840413 800533 2200893 2200893 73 8067
  //   JAL
  //   JALR
  //   URET
  //   I型
  //   S型
  //   U型
  //   B型Imm
  //   J型Imm
  //   Beq
  //   Bne
  //   MemToReg
  //   MemWrite
  //   AluOP
  //   AluSrcB
  //   RegWrite
  //   S_Type
  //   auipc
  //   beq/bne/blt
  //   jal
  //   jalr
  //   数据存储器
  //   为方便自动评测，需要输出PC，IR，寄存器堆写如数据RDin
  //   RAM写使能MemWrite、RAM写入数据MDin等信号
  //   控制位
  //   暂停节拍，不能为0
  //   戳工具置1进入计数暂停模式，ctrl+k时钟自动运行到对应节拍暂停
  //   ctrl+k关闭时钟连续运行，将控制位置零，进入单步调试模式调试
  //   用这个时钟源需要去掉电路中的其他时钟源
  //   可计数暂停的时钟源
endmodule

// 单周期硬布线控制器
module \单周期硬布线控制器  (
  input  [4:0] OP,
  input  [4:0] Funct,
  input  in_3,
  output [3:0] ALU_OP,
  output uret,
  output MemToReg,
  output ecall,
  output MemWrite,
  output ALU_SRC,
  output RegWrite,
  output S_type,
  output Beq,
  output Bne,
  output Jalr,
  output JAL,
  output blt,
  output U_type,
  output lhu,
  output csrrsi,
  output csrrci
);

  wire \控制信号自动生成_1_ecall ;

  \运算控制器自动生成  \u_运算控制器自动生成_1  (
    .OP2(OP[0]), .OP3(OP[1]), .OP4(OP[2]), .OP5(OP[3]), .OP6(OP[4]), .F12(Funct[0]), .F13(Funct[1]),
    .F14(Funct[2]), .F25(Funct[3]), .F30(Funct[4]), .S0(ALU_OP[0]), .S1(ALU_OP[1]), .S2(ALU_OP[2]),
    .S3(ALU_OP[3]));
  \控制信号自动生成  \u_控制信号自动生成_1  (
    .OP2(OP[0]), .OP3(OP[1]), .OP4(OP[2]), .OP5(OP[3]), .OP6(OP[4]), .MemToReg(MemToReg), .F12(Funct[0]),
    .F13(Funct[1]), .F14(Funct[2]), .F25(Funct[3]), .F30(Funct[4]), .MemWrite(MemWrite), .ALU_SRC(ALU_SRC),
    .RegWrite(RegWrite), .ecall(\控制信号自动生成_1_ecall ), .S_Type(S_type), .BEQ(Beq), .BNE(Bne), .JALR(Jalr),
    .JAL(JAL), .blt(blt), .U_type(U_type), .lhu(lhu), .csrrsi(csrrsi), .csrrci(csrrci));
  and and_1 (uret, in_3, \控制信号自动生成_1_ecall );
  and and_2 (ecall, ~in_3, \控制信号自动生成_1_ecall );  // AND_Gate

  // Other names for the same wires on the sheet: IR21 = in_3; OP_CODE[4:0] = OP

  // Notes on the sheet:
  //   运算器控制器，根据指令生成运算器功能选择信号
  //   控制信号生成，产生数据通路需要的其他控制信号
endmodule

// 运算器控制器
module \运算控制器自动生成  (
  input  OP2,
  input  OP3,
  input  OP4,
  input  OP5,
  input  OP6,
  input  F12,
  input  F13,
  input  F14,
  input  F25,
  input  F30,
  output S0,
  output S1,
  output S2,
  output S3
);

  wire and_1_out, and_2_out, and_3_out, and_4_out, and_5_out, and_6_out, and_7_out, and_8_out, and_9_out,
       and_10_out, and_11_out, and_12_out, and_13_out, and_14_out, and_15_out, and_16_out, and_17_out,
       and_18_out, and_19_out, and_20_out, and_21_out, and_22_out, and_23_out, and_24_out, and_25_out,
       and_26_out, and_27_out, and_28_out, and_29_out, and_30_out, and_31_out, and_32_out, and_33_out,
       and_34_out, and_35_out, and_36_out, and_37_out, and_38_out, and_39_out, and_40_out, and_41_out,
       and_42_out, and_43_out, and_44_out, not_1_out, not_2_out, not_3_out, not_4_out, not_5_out, not_6_out,
       not_7_out, not_8_out, not_9_out, not_10_out, not_11_out, not_12_out, not_13_out, not_14_out,
       not_15_out, not_16_out, not_17_out, not_18_out, not_19_out, not_20_out, not_21_out, not_22_out,
       not_23_out, not_24_out, not_25_out, not_26_out, not_27_out, not_28_out, not_29_out, not_30_out,
       not_31_out, not_32_out, not_33_out, not_34_out, not_35_out, not_36_out, not_37_out, not_38_out,
       not_39_out, not_40_out, not_41_out, not_42_out, not_43_out, not_44_out, not_45_out, not_46_out,
       not_47_out, not_48_out, not_49_out, not_50_out, not_51_out, not_52_out, not_53_out, not_54_out,
       not_55_out, not_56_out, not_57_out, not_58_out, not_59_out, not_60_out, not_61_out, not_62_out,
       not_63_out, not_64_out, not_65_out, not_66_out, not_67_out, not_68_out, not_69_out, not_70_out,
       not_71_out, not_72_out, not_73_out, not_74_out, not_75_out, not_76_out, not_77_out, not_78_out,
       not_79_out, not_80_out, not_81_out, not_82_out, not_83_out, not_84_out, not_85_out, not_86_out,
       not_87_out, not_88_out, not_89_out, not_90_out, not_91_out, not_92_out, not_93_out, not_94_out,
       not_95_out, not_96_out, not_97_out, not_98_out, not_99_out, not_100_out, not_101_out, not_102_out,
       not_103_out, not_104_out, not_105_out, not_106_out, not_107_out, not_108_out, not_109_out,
       not_110_out, not_111_out, not_112_out, not_113_out, not_114_out, not_115_out, not_116_out,
       not_117_out, not_118_out, not_119_out, not_120_out, not_121_out, not_122_out, not_123_out,
       not_124_out, not_125_out, not_126_out, not_127_out, not_128_out, not_129_out, not_130_out,
       not_131_out, not_132_out, not_133_out, not_134_out, not_135_out, not_136_out, not_137_out,
       not_138_out, not_139_out, not_140_out, not_141_out, not_142_out, not_143_out, not_144_out,
       not_145_out, not_146_out, not_147_out, not_148_out, not_149_out, not_150_out, not_151_out,
       not_152_out, not_153_out, not_154_out, not_155_out, not_156_out, not_157_out, not_158_out,
       not_159_out, not_160_out, not_161_out, not_162_out, not_163_out, not_164_out, not_165_out,
       not_166_out, not_167_out, not_168_out, not_169_out, not_170_out, not_171_out, not_172_out,
       not_173_out, not_174_out, not_175_out, not_176_out, not_177_out, not_178_out, not_179_out,
       not_180_out, not_181_out, not_182_out, not_183_out, not_184_out, not_185_out, not_186_out,
       not_187_out, not_188_out, not_189_out, not_190_out, not_191_out, not_192_out, not_193_out,
       not_194_out, not_195_out, not_196_out, not_197_out, not_198_out, not_199_out, not_200_out,
       not_201_out, not_202_out, not_203_out, not_204_out, not_205_out, not_206_out, not_207_out,
       not_208_out, not_209_out, not_210_out, not_211_out, not_212_out, not_213_out, not_214_out,
       not_215_out, not_216_out, not_217_out, not_218_out, not_219_out, not_220_out, not_221_out,
       not_222_out, not_223_out, not_224_out, not_225_out, not_226_out, not_227_out, not_228_out,
       not_229_out, not_230_out, not_231_out, not_232_out, not_233_out, not_234_out, not_235_out,
       not_236_out, not_237_out, not_238_out, not_239_out, not_240_out, not_241_out, not_242_out,
       not_243_out, not_244_out, not_245_out, not_246_out, not_247_out, not_248_out, not_249_out,
       not_250_out, not_251_out, not_252_out, not_253_out, not_254_out;

  not not_1 (not_1_out, F30);
  not not_2 (not_2_out, F25);
  not not_3 (not_3_out, F14);
  not not_4 (not_4_out, F13);
  not not_5 (not_5_out, F12);
  not not_6 (not_6_out, OP6);
  not not_7 (not_7_out, OP3);
  not not_8 (not_8_out, OP2);
  not not_9 (not_9_out, F30);
  not not_10 (not_10_out, F25);
  not not_11 (not_11_out, OP6);
  not not_12 (not_12_out, OP3);
  not not_13 (not_13_out, OP2);
  not not_14 (not_14_out, F30);
  not not_15 (not_15_out, F25);
  not not_16 (not_16_out, F14);
  not not_17 (not_17_out, F12);
  not not_18 (not_18_out, OP6);
  not not_19 (not_19_out, OP3);
  not not_20 (not_20_out, OP2);
  not not_21 (not_21_out, F14);
  not not_22 (not_22_out, F13);
  not not_23 (not_23_out, F12);
  not not_24 (not_24_out, OP6);
  not not_25 (not_25_out, OP5);
  not not_26 (not_26_out, OP3);
  not not_27 (not_27_out, OP2);
  not not_28 (not_28_out, OP6);
  not not_29 (not_29_out, OP5);
  not not_30 (not_30_out, OP3);
  not not_31 (not_31_out, OP2);
  not not_32 (not_32_out, F13);
  not not_33 (not_33_out, F12);
  not not_34 (not_34_out, OP6);
  not not_35 (not_35_out, OP5);
  not not_36 (not_36_out, OP3);
  not not_37 (not_37_out, OP2);
  not not_38 (not_38_out, F14);
  not not_39 (not_39_out, F12);
  not not_40 (not_40_out, OP6);
  not not_41 (not_41_out, OP5);
  not not_42 (not_42_out, OP3);
  not not_43 (not_43_out, OP2);
  not not_44 (not_44_out, F25);
  not not_45 (not_45_out, F13);
  not not_46 (not_46_out, OP6);
  not not_47 (not_47_out, OP5);
  not not_48 (not_48_out, OP3);
  not not_49 (not_49_out, OP2);
  not not_50 (not_50_out, F14);
  not not_51 (not_51_out, F12);
  not not_52 (not_52_out, OP6);
  not not_53 (not_53_out, OP5);
  not not_54 (not_54_out, OP4);
  not not_55 (not_55_out, OP3);
  not not_56 (not_56_out, OP2);
  not not_57 (not_57_out, F14);
  not not_58 (not_58_out, F12);
  not not_59 (not_59_out, OP6);
  not not_60 (not_60_out, OP4);
  not not_61 (not_61_out, OP3);
  not not_62 (not_62_out, OP2);
  not not_63 (not_63_out, F25);
  not not_64 (not_64_out, F13);
  not not_65 (not_65_out, OP6);
  not not_66 (not_66_out, OP3);
  not not_67 (not_67_out, OP2);
  not not_68 (not_68_out, OP6);
  not not_69 (not_69_out, OP5);
  not not_70 (not_70_out, OP3);
  not not_71 (not_71_out, F13);
  not not_72 (not_72_out, OP6);
  not not_73 (not_73_out, OP5);
  not not_74 (not_74_out, OP4);
  not not_75 (not_75_out, OP3);
  not not_76 (not_76_out, OP2);
  not not_77 (not_77_out, F13);
  not not_78 (not_78_out, F12);
  not not_79 (not_79_out, OP4);
  not not_80 (not_80_out, OP3);
  not not_81 (not_81_out, OP2);
  not not_82 (not_82_out, F25);
  not not_83 (not_83_out, F14);
  not not_84 (not_84_out, F13);
  not not_85 (not_85_out, F12);
  not not_86 (not_86_out, OP6);
  not not_87 (not_87_out, OP3);
  not not_88 (not_88_out, OP2);
  not not_89 (not_89_out, F30);
  not not_90 (not_90_out, F25);
  not not_91 (not_91_out, OP6);
  not not_92 (not_92_out, OP3);
  not not_93 (not_93_out, OP2);
  not not_94 (not_94_out, F30);
  not not_95 (not_95_out, F25);
  not not_96 (not_96_out, F14);
  not not_97 (not_97_out, F12);
  not not_98 (not_98_out, OP6);
  not not_99 (not_99_out, OP3);
  not not_100 (not_100_out, OP2);
  not not_101 (not_101_out, OP6);
  not not_102 (not_102_out, OP5);
  not not_103 (not_103_out, OP3);
  not not_104 (not_104_out, OP2);
  not not_105 (not_105_out, F14);
  not not_106 (not_106_out, F12);
  not not_107 (not_107_out, OP6);
  not not_108 (not_108_out, OP5);
  not not_109 (not_109_out, OP3);
  not not_110 (not_110_out, OP2);
  not not_111 (not_111_out, F30);
  not not_112 (not_112_out, F25);
  not not_113 (not_113_out, F13);
  not not_114 (not_114_out, OP6);
  not not_115 (not_115_out, OP5);
  not not_116 (not_116_out, OP3);
  not not_117 (not_117_out, OP2);
  not not_118 (not_118_out, F14);
  not not_119 (not_119_out, F13);
  not not_120 (not_120_out, F12);
  not not_121 (not_121_out, OP4);
  not not_122 (not_122_out, OP3);
  not not_123 (not_123_out, OP2);
  not not_124 (not_124_out, F14);
  not not_125 (not_125_out, F13);
  not not_126 (not_126_out, OP4);
  not not_127 (not_127_out, OP3);
  not not_128 (not_128_out, OP2);
  not not_129 (not_129_out, F14);
  not not_130 (not_130_out, F13);
  not not_131 (not_131_out, F12);
  not not_132 (not_132_out, OP4);
  not not_133 (not_133_out, OP3);
  not not_134 (not_134_out, F13);
  not not_135 (not_135_out, F12);
  not not_136 (not_136_out, OP4);
  not not_137 (not_137_out, OP3);
  not not_138 (not_138_out, OP2);
  not not_139 (not_139_out, F30);
  not not_140 (not_140_out, F25);
  not not_141 (not_141_out, F14);
  not not_142 (not_142_out, F13);
  not not_143 (not_143_out, F12);
  not not_144 (not_144_out, OP6);
  not not_145 (not_145_out, OP3);
  not not_146 (not_146_out, OP2);
  not not_147 (not_147_out, F25);
  not not_148 (not_148_out, F14);
  not not_149 (not_149_out, F13);
  not not_150 (not_150_out, F12);
  not not_151 (not_151_out, OP6);
  not not_152 (not_152_out, OP3);
  not not_153 (not_153_out, OP2);
  not not_154 (not_154_out, F30);
  not not_155 (not_155_out, F25);
  not not_156 (not_156_out, OP6);
  not not_157 (not_157_out, OP3);
  not not_158 (not_158_out, OP2);
  not not_159 (not_159_out, F30);
  not not_160 (not_160_out, F25);
  not not_161 (not_161_out, F14);
  not not_162 (not_162_out, OP6);
  not not_163 (not_163_out, OP3);
  not not_164 (not_164_out, OP2);
  not not_165 (not_165_out, F14);
  not not_166 (not_166_out, F13);
  not not_167 (not_167_out, F12);
  not not_168 (not_168_out, OP6);
  not not_169 (not_169_out, OP5);
  not not_170 (not_170_out, OP3);
  not not_171 (not_171_out, OP2);
  not not_172 (not_172_out, OP6);
  not not_173 (not_173_out, OP5);
  not not_174 (not_174_out, OP3);
  not not_175 (not_175_out, OP2);
  not not_176 (not_176_out, F14);
  not not_177 (not_177_out, F12);
  not not_178 (not_178_out, OP6);
  not not_179 (not_179_out, OP5);
  not not_180 (not_180_out, OP4);
  not not_181 (not_181_out, OP3);
  not not_182 (not_182_out, OP2);
  not not_183 (not_183_out, F14);
  not not_184 (not_184_out, F12);
  not not_185 (not_185_out, OP6);
  not not_186 (not_186_out, OP4);
  not not_187 (not_187_out, OP3);
  not not_188 (not_188_out, OP2);
  not not_189 (not_189_out, F14);
  not not_190 (not_190_out, F13);
  not not_191 (not_191_out, F12);
  not not_192 (not_192_out, OP4);
  not not_193 (not_193_out, OP3);
  not not_194 (not_194_out, OP2);
  not not_195 (not_195_out, F14);
  not not_196 (not_196_out, F13);
  not not_197 (not_197_out, OP4);
  not not_198 (not_198_out, OP3);
  not not_199 (not_199_out, OP2);
  not not_200 (not_200_out, F14);
  not not_201 (not_201_out, F13);
  not not_202 (not_202_out, F12);
  not not_203 (not_203_out, OP4);
  not not_204 (not_204_out, OP3);
  not not_205 (not_205_out, OP6);
  not not_206 (not_206_out, OP5);
  not not_207 (not_207_out, OP3);
  not not_208 (not_208_out, F13);
  not not_209 (not_209_out, OP6);
  not not_210 (not_210_out, OP5);
  not not_211 (not_211_out, OP4);
  not not_212 (not_212_out, OP3);
  not not_213 (not_213_out, OP2);
  not not_214 (not_214_out, F30);
  not not_215 (not_215_out, F25);
  not not_216 (not_216_out, F12);
  not not_217 (not_217_out, OP6);
  not not_218 (not_218_out, OP3);
  not not_219 (not_219_out, OP2);
  not not_220 (not_220_out, F30);
  not not_221 (not_221_out, F25);
  not not_222 (not_222_out, F14);
  not not_223 (not_223_out, F12);
  not not_224 (not_224_out, OP6);
  not not_225 (not_225_out, OP3);
  not not_226 (not_226_out, OP2);
  not not_227 (not_227_out, F30);
  not not_228 (not_228_out, F25);
  not not_229 (not_229_out, F14);
  not not_230 (not_230_out, OP6);
  not not_231 (not_231_out, OP3);
  not not_232 (not_232_out, OP2);
  not not_233 (not_233_out, F12);
  not not_234 (not_234_out, OP6);
  not not_235 (not_235_out, OP5);
  not not_236 (not_236_out, OP3);
  not not_237 (not_237_out, OP2);
  not not_238 (not_238_out, F13);
  not not_239 (not_239_out, F12);
  not not_240 (not_240_out, OP6);
  not not_241 (not_241_out, OP5);
  not not_242 (not_242_out, OP3);
  not not_243 (not_243_out, OP2);
  not not_244 (not_244_out, F14);
  not not_245 (not_245_out, F12);
  not not_246 (not_246_out, OP6);
  not not_247 (not_247_out, OP5);
  not not_248 (not_248_out, OP3);
  not not_249 (not_249_out, OP2);
  not not_250 (not_250_out, F13);
  not not_251 (not_251_out, F12);
  not not_252 (not_252_out, OP4);
  not not_253 (not_253_out, OP3);
  not not_254 (not_254_out, OP2);
  and and_1 (and_1_out, not_1_out, not_2_out, not_3_out, not_4_out, not_5_out, not_6_out, OP5, OP4, not_7_out, not_8_out);
  and and_2 (and_2_out, not_9_out, not_10_out, F14, F13, F12, not_11_out, OP5, OP4, not_12_out, not_13_out);
  and and_3 (and_3_out, not_14_out, not_15_out, not_16_out, F13, not_17_out, not_18_out, OP5, OP4, not_19_out, not_20_out);
  and and_4 (and_4_out, not_21_out, not_22_out, not_23_out, not_24_out, not_25_out, OP4, not_26_out, not_27_out);
  and and_5 (and_5_out, F14, F13, F12, not_28_out, not_29_out, OP4, not_30_out, not_31_out);
  and and_6 (and_6_out, F14, not_32_out, not_33_out, not_34_out, not_35_out, OP4, not_36_out, not_37_out);
  and and_7 (and_7_out, not_38_out, F13, not_39_out, not_40_out, not_41_out, OP4, not_42_out, not_43_out);
  and and_8 (and_8_out, F30, not_44_out, F14, not_45_out, F12, not_46_out, not_47_out, OP4, not_48_out, not_49_out);
  and and_9 (and_9_out, not_50_out, F13, not_51_out, not_52_out, not_53_out, not_54_out, not_55_out, not_56_out);
  and and_10 (and_10_out, not_57_out, F13, not_58_out, not_59_out, OP5, not_60_out, not_61_out, not_62_out);
  and and_11 (and_11_out, F30, not_63_out, F14, not_64_out, F12, not_65_out, OP5, OP4, not_66_out, not_67_out);
  and and_12 (and_12_out, not_68_out, not_69_out, OP4, not_70_out, OP2);
  and and_13 (and_13_out, F14, not_71_out, F12, not_72_out, not_73_out, not_74_out, not_75_out, not_76_out);
  and and_14 (and_14_out, F14, not_77_out, not_78_out, OP6, OP5, not_79_out, not_80_out, not_81_out);
  and and_15 (and_15_out, F30, not_82_out, not_83_out, not_84_out, not_85_out, not_86_out, OP5, OP4, not_87_out, not_88_out);
  and and_16 (and_16_out, not_89_out, not_90_out, F14, F13, F12, not_91_out, OP5, OP4, not_92_out, not_93_out);
  and and_17 (and_17_out, not_94_out, not_95_out, not_96_out, F13, not_97_out, not_98_out, OP5, OP4, not_99_out, not_100_out);
  and and_18 (and_18_out, F14, F13, F12, not_101_out, not_102_out, OP4, not_103_out, not_104_out);
  and and_19 (and_19_out, not_105_out, F13, not_106_out, not_107_out, not_108_out, OP4, not_109_out, not_110_out);
  and and_20 (and_20_out, not_111_out, not_112_out, F14, not_113_out, F12, not_114_out, not_115_out, OP4, not_116_out, not_117_out);
  and and_21 (and_21_out, not_118_out, not_119_out, not_120_out, OP6, OP5, not_121_out, not_122_out, not_123_out);
  and and_22 (and_22_out, not_124_out, not_125_out, F12, OP6, OP5, not_126_out, not_127_out, not_128_out);
  and and_23 (and_23_out, not_129_out, not_130_out, not_131_out, OP6, OP5, not_132_out, not_133_out, OP2);
  and and_24 (and_24_out, F14, not_134_out, not_135_out, OP6, OP5, not_136_out, not_137_out, not_138_out);
  and and_25 (and_25_out, not_139_out, not_140_out, not_141_out, not_142_out, not_143_out, not_144_out, OP5, OP4, not_145_out, not_146_out);
  and and_26 (and_26_out, F30, not_147_out, not_148_out, not_149_out, not_150_out, not_151_out, OP5, OP4, not_152_out, not_153_out);
  and and_27 (and_27_out, not_154_out, not_155_out, F14, F13, F12, not_156_out, OP5, OP4, not_157_out, not_158_out);
  and and_28 (and_28_out, not_159_out, not_160_out, not_161_out, F13, F12, not_162_out, OP5, OP4, not_163_out, not_164_out);
  and and_29 (and_29_out, not_165_out, not_166_out, not_167_out, not_168_out, not_169_out, OP4, not_170_out, not_171_out);
  and and_30 (and_30_out, F14, F13, F12, not_172_out, not_173_out, OP4, not_174_out, not_175_out);
  and and_31 (and_31_out, not_176_out, F13, not_177_out, not_178_out, not_179_out, not_180_out, not_181_out, not_182_out);
  and and_32 (and_32_out, not_183_out, F13, not_184_out, not_185_out, OP5, not_186_out, not_187_out, not_188_out);
  and and_33 (and_33_out, not_189_out, not_190_out, not_191_out, OP6, OP5, not_192_out, not_193_out, not_194_out);
  and and_34 (and_34_out, not_195_out, not_196_out, F12, OP6, OP5, not_197_out, not_198_out, not_199_out);
  and and_35 (and_35_out, not_200_out, not_201_out, not_202_out, OP6, OP5, not_203_out, not_204_out, OP2);
  and and_36 (and_36_out, not_205_out, not_206_out, OP4, not_207_out, OP2);
  and and_37 (and_37_out, F14, not_208_out, F12, not_209_out, not_210_out, not_211_out, not_212_out, not_213_out);
  and and_38 (and_38_out, not_214_out, not_215_out, F14, F13, not_216_out, not_217_out, OP5, OP4, not_218_out, not_219_out);
  and and_39 (and_39_out, not_220_out, not_221_out, not_222_out, F13, not_223_out, not_224_out, OP5, OP4, not_225_out, not_226_out);
  and and_40 (and_40_out, not_227_out, not_228_out, not_229_out, F13, F12, not_230_out, OP5, OP4, not_231_out, not_232_out);
  and and_41 (and_41_out, F14, F13, not_233_out, not_234_out, not_235_out, OP4, not_236_out, not_237_out);
  and and_42 (and_42_out, F14, not_238_out, not_239_out, not_240_out, not_241_out, OP4, not_242_out, not_243_out);
  and and_43 (and_43_out, not_244_out, F13, not_245_out, not_246_out, not_247_out, OP4, not_248_out, not_249_out);
  and and_44 (and_44_out, F14, not_250_out, not_251_out, OP6, OP5, not_252_out, not_253_out, not_254_out);
  or or_1 (S0, and_1_out, and_2_out, and_3_out, and_4_out, and_5_out, and_6_out, and_7_out, and_8_out, and_9_out, and_10_out, and_11_out, and_12_out, and_13_out, and_14_out);
  or or_2 (S1, and_15_out, and_16_out, and_17_out, and_18_out, and_19_out, and_20_out, and_21_out, and_22_out, and_23_out, and_24_out);
  or or_3 (S2, and_25_out, and_26_out, and_27_out, and_28_out, and_29_out, and_30_out, and_31_out, and_32_out, and_33_out, and_34_out, and_35_out, and_36_out, and_37_out);
  or or_4 (S3, and_38_out, and_39_out, and_40_out, and_41_out, and_42_out, and_43_out, and_44_out);
endmodule

// 控制信号生成
module \控制信号自动生成  (
  input  OP2,
  input  OP3,
  input  OP4,
  input  OP5,
  input  OP6,
  input  F12,
  input  F13,
  input  F14,
  input  F25,
  input  F30,
  output MemToReg,
  output MemWrite,
  output ALU_SRC,
  output RegWrite,
  output ecall,
  output S_Type,
  output BEQ,
  output BNE,
  output JALR,
  output JAL,
  output blt,
  output U_type,
  output lhu,
  output csrrsi,
  output csrrci
);

  wire and_1_out, and_2_out, and_4_out, and_5_out, and_6_out, and_7_out, and_8_out, and_9_out, and_10_out,
       and_11_out, and_12_out, and_13_out, and_14_out, and_15_out, and_16_out, and_17_out, and_18_out,
       and_19_out, and_20_out, and_21_out, and_22_out, not_1_out, not_2_out, not_3_out, not_4_out, not_5_out,
       not_6_out, not_7_out, not_8_out, not_9_out, not_10_out, not_11_out, not_12_out, not_13_out,
       not_14_out, not_15_out, not_16_out, not_17_out, not_18_out, not_19_out, not_20_out, not_21_out,
       not_22_out, not_23_out, not_24_out, not_25_out, not_26_out, not_27_out, not_28_out, not_29_out,
       not_30_out, not_31_out, not_32_out, not_33_out, not_34_out, not_35_out, not_36_out, not_37_out,
       not_38_out, not_39_out, not_40_out, not_41_out, not_42_out, not_43_out, not_44_out, not_45_out,
       not_46_out, not_47_out, not_48_out, not_49_out, not_50_out, not_51_out, not_52_out, not_53_out,
       not_54_out, not_55_out, not_56_out, not_57_out, not_58_out, not_59_out, not_60_out, not_61_out,
       not_62_out, not_63_out, not_64_out, not_65_out, not_66_out, not_67_out, not_68_out, not_69_out,
       not_70_out, not_71_out, not_72_out, not_73_out, not_74_out, not_75_out, not_76_out, not_77_out,
       not_78_out, not_79_out, not_80_out, not_81_out, not_82_out, not_83_out, not_84_out, not_85_out,
       not_86_out, not_87_out, not_88_out, not_89_out, not_90_out, not_91_out, not_92_out, not_93_out,
       not_94_out, not_95_out, not_96_out, not_97_out, not_98_out, not_99_out, not_100_out, not_101_out,
       not_102_out, not_103_out, not_104_out, not_105_out, not_106_out, not_107_out, not_108_out,
       not_109_out, not_110_out, not_111_out, not_112_out, not_113_out, not_114_out, not_115_out,
       not_116_out, not_117_out, not_118_out, not_119_out, not_120_out, not_121_out, not_122_out,
       not_123_out, not_124_out, not_125_out, not_126_out, not_127_out, not_128_out, not_129_out,
       not_130_out, not_131_out, not_132_out, not_133_out, not_134_out, not_135_out, not_136_out,
       not_137_out, not_138_out, not_139_out, not_140_out, not_141_out, not_142_out, not_143_out,
       not_144_out, not_145_out, not_146_out, not_147_out, not_148_out, not_149_out, not_150_out,
       not_151_out, not_152_out, not_153_out, not_154_out, not_155_out;

  not not_1 (not_1_out, OP2);
  not not_2 (not_2_out, OP3);
  not not_3 (not_3_out, OP4);
  not not_4 (not_4_out, OP5);
  not not_5 (not_5_out, OP6);
  not not_6 (not_6_out, F12);
  not not_7 (not_7_out, F14);
  not not_8 (not_8_out, OP2);
  not not_9 (not_9_out, OP3);
  not not_10 (not_10_out, OP4);
  not not_11 (not_11_out, OP5);
  not not_12 (not_12_out, OP6);
  not not_13 (not_13_out, F13);
  not not_14 (not_14_out, OP2);
  not not_15 (not_15_out, OP3);
  not not_16 (not_16_out, OP4);
  not not_17 (not_17_out, OP6);
  not not_18 (not_18_out, F12);
  not not_19 (not_19_out, F14);
  not not_20 (not_20_out, OP2);
  not not_21 (not_21_out, OP3);
  not not_22 (not_22_out, OP4);
  not not_23 (not_23_out, OP6);
  not not_24 (not_24_out, F12);
  not not_25 (not_25_out, F14);
  not not_26 (not_26_out, OP2);
  not not_27 (not_27_out, OP3);
  not not_28 (not_28_out, OP4);
  not not_29 (not_29_out, OP5);
  not not_30 (not_30_out, OP6);
  not not_31 (not_31_out, F13);
  not not_32 (not_32_out, OP3);
  not not_33 (not_33_out, OP5);
  not not_34 (not_34_out, OP6);
  not not_35 (not_35_out, F12);
  not not_36 (not_36_out, OP3);
  not not_37 (not_37_out, OP5);
  not not_38 (not_38_out, OP6);
  not not_39 (not_39_out, F13);
  not not_40 (not_40_out, F25);
  not not_41 (not_41_out, F30);
  not not_42 (not_42_out, OP3);
  not not_43 (not_43_out, OP5);
  not not_44 (not_44_out, OP6);
  not not_45 (not_45_out, F25);
  not not_46 (not_46_out, OP3);
  not not_47 (not_47_out, OP5);
  not not_48 (not_48_out, OP6);
  not not_49 (not_49_out, OP3);
  not not_50 (not_50_out, OP4);
  not not_51 (not_51_out, F12);
  not not_52 (not_52_out, F13);
  not not_53 (not_53_out, F14);
  not not_54 (not_54_out, OP3);
  not not_55 (not_55_out, OP5);
  not not_56 (not_56_out, OP6);
  not not_57 (not_57_out, OP2);
  not not_58 (not_58_out, OP3);
  not not_59 (not_59_out, OP5);
  not not_60 (not_60_out, OP6);
  not not_61 (not_61_out, F12);
  not not_62 (not_62_out, F14);
  not not_63 (not_63_out, OP2);
  not not_64 (not_64_out, OP3);
  not not_65 (not_65_out, OP4);
  not not_66 (not_66_out, OP5);
  not not_67 (not_67_out, OP6);
  not not_68 (not_68_out, F13);
  not not_69 (not_69_out, OP2);
  not not_70 (not_70_out, OP3);
  not not_71 (not_71_out, OP6);
  not not_72 (not_72_out, F12);
  not not_73 (not_73_out, F13);
  not not_74 (not_74_out, F14);
  not not_75 (not_75_out, F25);
  not not_76 (not_76_out, OP3);
  not not_77 (not_77_out, OP5);
  not not_78 (not_78_out, OP6);
  not not_79 (not_79_out, F12);
  not not_80 (not_80_out, OP3);
  not not_81 (not_81_out, OP5);
  not not_82 (not_82_out, OP6);
  not not_83 (not_83_out, F13);
  not not_84 (not_84_out, F25);
  not not_85 (not_85_out, F30);
  not not_86 (not_86_out, OP3);
  not not_87 (not_87_out, OP5);
  not not_88 (not_88_out, OP6);
  not not_89 (not_89_out, OP2);
  not not_90 (not_90_out, OP3);
  not not_91 (not_91_out, OP6);
  not not_92 (not_92_out, F13);
  not not_93 (not_93_out, F25);
  not not_94 (not_94_out, OP2);
  not not_95 (not_95_out, OP3);
  not not_96 (not_96_out, OP6);
  not not_97 (not_97_out, F25);
  not not_98 (not_98_out, F30);
  not not_99 (not_99_out, OP4);
  not not_100 (not_100_out, F12);
  not not_101 (not_101_out, F13);
  not not_102 (not_102_out, F14);
  not not_103 (not_103_out, OP3);
  not not_104 (not_104_out, OP5);
  not not_105 (not_105_out, OP6);
  not not_106 (not_106_out, OP4);
  not not_107 (not_107_out, OP2);
  not not_108 (not_108_out, OP3);
  not not_109 (not_109_out, F12);
  not not_110 (not_110_out, F13);
  not not_111 (not_111_out, F14);
  not not_112 (not_112_out, F25);
  not not_113 (not_113_out, F30);
  not not_114 (not_114_out, OP2);
  not not_115 (not_115_out, OP3);
  not not_116 (not_116_out, OP4);
  not not_117 (not_117_out, OP6);
  not not_118 (not_118_out, F12);
  not not_119 (not_119_out, F14);
  not not_120 (not_120_out, OP2);
  not not_121 (not_121_out, OP3);
  not not_122 (not_122_out, OP4);
  not not_123 (not_123_out, F12);
  not not_124 (not_124_out, F13);
  not not_125 (not_125_out, F14);
  not not_126 (not_126_out, OP2);
  not not_127 (not_127_out, OP3);
  not not_128 (not_128_out, OP4);
  not not_129 (not_129_out, F13);
  not not_130 (not_130_out, F14);
  not not_131 (not_131_out, OP3);
  not not_132 (not_132_out, OP4);
  not not_133 (not_133_out, F12);
  not not_134 (not_134_out, F13);
  not not_135 (not_135_out, F14);
  not not_136 (not_136_out, OP4);
  not not_137 (not_137_out, OP2);
  not not_138 (not_138_out, OP3);
  not not_139 (not_139_out, OP4);
  not not_140 (not_140_out, F12);
  not not_141 (not_141_out, F13);
  not not_142 (not_142_out, OP3);
  not not_143 (not_143_out, OP5);
  not not_144 (not_144_out, OP6);
  not not_145 (not_145_out, OP2);
  not not_146 (not_146_out, OP3);
  not not_147 (not_147_out, OP4);
  not not_148 (not_148_out, OP5);
  not not_149 (not_149_out, OP6);
  not not_150 (not_150_out, F13);
  not not_151 (not_151_out, F12);
  not not_152 (not_152_out, OP3);
  not not_153 (not_153_out, OP2);
  not not_154 (not_154_out, OP3);
  not not_155 (not_155_out, OP2);
  and and_1 (and_1_out, not_1_out, not_2_out, not_3_out, not_4_out, not_5_out, not_6_out, F13, not_7_out);
  and and_2 (and_2_out, not_8_out, not_9_out, not_10_out, not_11_out, not_12_out, F12, not_13_out, F14);
  and and_3 (MemWrite, not_14_out, not_15_out, not_16_out, OP5, not_17_out, not_18_out, F13, not_19_out);
  and and_4 (and_4_out, not_20_out, not_21_out, not_22_out, not_23_out, not_24_out, F13, not_25_out);
  and and_5 (and_5_out, not_26_out, not_27_out, not_28_out, not_29_out, not_30_out, F12, not_31_out, F14);
  and and_6 (and_6_out, not_32_out, OP4, not_33_out, not_34_out, not_35_out);
  and and_7 (and_7_out, not_36_out, OP4, not_37_out, not_38_out, not_39_out, not_40_out, not_41_out);
  and and_8 (and_8_out, not_42_out, OP4, not_43_out, not_44_out, F14, not_45_out);
  and and_9 (and_9_out, not_46_out, OP4, not_47_out, not_48_out, F13, F14);
  and and_10 (and_10_out, OP2, not_49_out, not_50_out, OP5, OP6, not_51_out, not_52_out, not_53_out);
  and and_11 (and_11_out, OP2, not_54_out, OP4, not_55_out, not_56_out);
  and and_12 (and_12_out, not_57_out, not_58_out, not_59_out, not_60_out, not_61_out, F13, not_62_out);
  and and_13 (and_13_out, not_63_out, not_64_out, not_65_out, not_66_out, not_67_out, F12, not_68_out, F14);
  and and_14 (and_14_out, not_69_out, not_70_out, OP4, not_71_out, not_72_out, not_73_out, not_74_out, not_75_out);
  and and_15 (and_15_out, not_76_out, OP4, not_77_out, not_78_out, not_79_out);
  and and_16 (and_16_out, not_80_out, OP4, not_81_out, not_82_out, not_83_out, not_84_out, not_85_out);
  and and_17 (and_17_out, not_86_out, OP4, not_87_out, not_88_out, F13, F14);
  and and_18 (and_18_out, not_89_out, not_90_out, OP4, not_91_out, F12, not_92_out, F14, not_93_out, F30);
  and and_19 (and_19_out, not_94_out, not_95_out, OP4, OP5, not_96_out, F13, not_97_out, not_98_out);
  and and_20 (and_20_out, OP2, not_99_out, OP5, OP6, not_100_out, not_101_out, not_102_out);
  and and_21 (and_21_out, OP2, not_103_out, OP4, not_104_out, not_105_out);
  and and_22 (and_22_out, OP2, OP3, not_106_out, OP5, OP6);
  and and_23 (ecall, not_107_out, not_108_out, OP4, OP5, OP6, not_109_out, not_110_out, not_111_out, not_112_out, not_113_out);
  and and_24 (S_Type, not_114_out, not_115_out, not_116_out, OP5, not_117_out, not_118_out, F13, not_119_out);
  and and_25 (BEQ, not_120_out, not_121_out, not_122_out, OP5, OP6, not_123_out, not_124_out, not_125_out);
  and and_26 (BNE, not_126_out, not_127_out, not_128_out, OP5, OP6, F12, not_129_out, not_130_out);
  and and_27 (JALR, OP2, not_131_out, not_132_out, OP5, OP6, not_133_out, not_134_out, not_135_out);
  and and_28 (JAL, OP2, OP3, not_136_out, OP5, OP6);
  and and_29 (blt, not_137_out, not_138_out, not_139_out, OP5, OP6, not_140_out, not_141_out, F14);
  and and_30 (U_type, OP2, not_142_out, OP4, not_143_out, not_144_out);
  and and_31 (lhu, not_145_out, not_146_out, not_147_out, not_148_out, not_149_out, F12, not_150_out, F14);
  and and_32 (csrrsi, F14, F13, not_151_out, OP6, OP5, OP4, not_152_out, not_153_out);
  and and_33 (csrrci, F14, F13, F12, OP6, OP5, OP4, not_154_out, not_155_out);
  or or_1 (MemToReg, and_1_out, and_2_out);
  or or_2 (ALU_SRC, and_4_out, and_5_out, and_6_out, and_7_out, and_8_out, and_9_out, and_10_out, and_11_out);
  or or_3 (RegWrite, and_12_out, and_13_out, and_14_out, and_15_out, and_16_out, and_17_out, and_18_out, and_19_out, and_20_out, and_21_out, and_22_out);
endmodule

// ALU
module ALU (
  input  [31:0] X,
  input  [31:0] Y,
  input  [3:0] AluOP,
  output out_4,
  output Equal,
  output out_6,
  output [31:0] Result,
  output [31:0] Result_2
);

  wire [0:0] comparator_1_lt, comparator_2_lt;
  wire [31:0] adder_1_out, AND_out, divider_1_out, divider_1_rem, multiplier_1_cout, multiplier_1_out,
       NOR_out, OR_out, shifter_1_out, shifter_2_out, shifter_3_out, subtractor_1_out, XOR_out;

  assign AND_out = X & Y;  // AND_Gate AND, 32 bits wide
  assign OR_out = X | Y;  // OR_Gate OR, 32 bits wide
  Shifter #(.width(32), .shift("ll")) shifter_1 (.in(X), .\dist (Y[4:0]), .out(shifter_1_out));
  Shifter #(.width(32), .shift("ar")) shifter_2 (.in(X), .\dist (Y[4:0]), .out(shifter_2_out));
  Shifter #(.width(32), .shift("lr")) shifter_3 (.in(X), .\dist (Y[4:0]), .out(shifter_3_out));
  Multiplier #(.width(32)) multiplier_1 (.a(X), .b(Y), .out(multiplier_1_out), .cout(multiplier_1_cout));  // open: cin
  Divider #(.width(32)) divider_1 (.a(X), .b(Y), .out(divider_1_out), .rem(divider_1_rem));  // open: upper
  Adder #(.width(32)) adder_1 (.a(X), .b(Y), .out(adder_1_out));  // open: cin, cout
  Subtractor #(.width(32)) subtractor_1 (.a(X), .b(Y), .out(subtractor_1_out));  // open: bin, bout
  assign XOR_out = X ^ Y;  // XOR_Gate XOR, 32 bits wide
  assign NOR_out = ~(X | Y);  // NOR_Gate NOR, 32 bits wide
  Comparator #(.width(32), .mode("twosComplement")) comparator_1 (
    .a(X), .b(Y), .eq(Equal), .lt(comparator_1_lt[0]));  // open: gt
  Comparator #(.width(32), .mode("unsigned")) comparator_2 (.a(X), .b(Y), .lt(comparator_2_lt[0]));  // open: gt, eq
  Multiplexer #(.select(4), .width(32), .disabled("Z"), .enable("false")) multiplexer_1 (
    .in0(shifter_1_out), .in1(shifter_2_out), .in2(shifter_3_out), .in3(multiplier_1_out),
    .in4(divider_1_out), .in5(adder_1_out), .in6(subtractor_1_out), .in7(AND_out), .in8(OR_out),
    .in9(XOR_out), .in10(NOR_out), .in11({{31{1'b0}}, comparator_1_lt[0]}),
    .in12({{31{1'b0}}, comparator_2_lt[0]}), .in13({32{1'b0}}), .in14({32{1'b0}}), .in15({32{1'b0}}),
    .out(Result), .sel(AluOP));
  Multiplexer #(.select(4), .width(32), .disabled("Z"), .enable("false")) multiplexer_2 (
    .in0({32{1'b0}}), .in1({32{1'b0}}), .in2({32{1'b0}}), .in3(multiplier_1_cout), .in4(divider_1_rem),
    .in5({32{1'b0}}), .in6({32{1'b0}}), .in7({32{1'b0}}), .in8({32{1'b0}}), .in9({32{1'b0}}),
    .in10({32{1'b0}}), .in11({32{1'b0}}), .in12({32{1'b0}}), .in13({32{1'b0}}), .in14({32{1'b0}}),
    .in15({32{1'b0}}), .out(Result_2), .sel(AluOP));
  Multiplexer #(.select(4), .width(1), .disabled("Z"), .enable("false")) multiplexer_3 (
    .in0(1'b0), .in1(1'b0), .in2(1'b0), .in3(1'b0), .in4(1'b0), .in5(1'b0), .in6(1'b0), .in7(1'b0),
    .in8(1'b0), .in9(1'b0), .in10(1'b0), .in11(comparator_1_lt[0]), .in12(comparator_2_lt[0]), .in13(1'b0),
    .in14(1'b0), .in15(1'b0), .out(out_6), .sel(AluOP));
  not not_1 (out_4, out_6);

  // Other names for the same wires on the sheet: Result2[31:0] = Result_2; S[3:0] = AluOP; tunnel = out_6;
  //   tunnel_t = out_4

  // Notes on the sheet:
  //   不要改变此引脚区域内容，也不要改变ALU封装形式
  //   输入引脚
  //   输出引脚
endmodule

module Regifile (
  input  [31:0] Din,
  input  Clk,
  input  WE,
  input  [4:0] R1_num,
  input  [4:0] W_num,
  input  [4:0] R2_num,
  output [31:0] R1,
  output [31:0] R2
);

  // RegisterFile registerfile_1: pin names not known; wires that end beside it: Din, Clk, WE, W_num, R1_num, R2_num, R1, R2
endmodule

module \理想流水线  (
  output RegWrite,
  output MemWrite,
  output [31:0] IF_PC,
  output [31:0] ID_PC,
  output [31:0] EX_PC,
  output [31:0] M_PC,
  output [31:0] WB_PC,
  output [31:0] RDin,
  output [31:0] MDin,
  output [31:0] LedData
);

  wire alu_1_equal, alu_1_out_6, and_3_out, and_4_out, and_5_out, and_6_out, B, blt, CLK, clock_1_out,
       comparator_1_eq, comparator_1_lt, comparator_2_eq, d_ff_1_q, ecall, en, ex_mem_1_haltout,
       ex_mem_1_jout, ex_mem_1_lhuout, ex_mem_1_memtoregout, ex_mem_1_regwriteout, ex_mem_1_utypeout, Go,
       halt, id_ex_1_alusrcout, id_ex_1_beqout, id_ex_1_bneout, id_ex_1_ecallout, id_ex_1_lhuout,
       id_ex_1_memtoregout, id_ex_1_memwriteout, id_ex_1_regwriteout, id_ex_1_utypeout, IR1, IR2, IR3, JAL,
       JALR, mem_wb_1_jout, mem_wb_1_lhuout, mem_wb_1_memtoregout, mem_wb_1_utypeout, nand_1_out, nor_1_out,
       not_1_out, not_2_out, not_3_out, not_4_out, not_5_out, not_6_out, or_1_out, or_2_out, or_3_out,
       or_4_out, RST, S_Type, W1, W2, W3, \单周期硬布线控制器_1_alu_src , \单周期硬布线控制器_1_beq , \单周期硬布线控制器_1_blt ,
       \单周期硬布线控制器_1_bne , \单周期硬布线控制器_1_jal , \单周期硬布线控制器_1_jalr , \单周期硬布线控制器_1_lhu , \单周期硬布线控制器_1_memtoreg ,
       \单周期硬布线控制器_1_memwrite , \单周期硬布线控制器_1_regwrite , \单周期硬布线控制器_1_u_type , \单周期硬布线控制器_1_uret ;
  wire [1:0] priority_encoder_1_out;
  wire [3:0] id_ex_1_aluopout, \单周期硬布线控制器_1_alu_op ;
  wire [4:0] ex_mem_1_writeregout, id_ex_1_writeregout_prime, multiplexer_2_out, multiplexer_3_out, W_num;
  wire [12:0] CNT_num;
  wire [15:0] \LoadUse次数 , multiplexer_9_out, \总周期数 , \插入气泡数 , \无条件分支数 , \条件分支成功数 ;
  wire [31:0] adder_2_out, adder_5_out, aluresult, b_t, bit_extender_1_out, bit_extender_2_out,
       bit_extender_3_out, bit_extender_4_out, bit_extender_5_out, bit_extender_6_out, EX_IR,
       ex_mem_1_aluresultout, ex_mem_1_aupicimmout, ex_mem_1_immout, id_ex_1_imm1out_prime,
       id_ex_1_imm2out_prime, id_ex_1_imm3out_prime, id_ex_1_imm4out_prime, id_ex_1_r1out,
       id_ex_1_r2out_prime, ID_IR, IF_IR, jal_t, jalr_t, MEM_IR, mem_wb_1_aluresultout, mem_wb_1_auipcimmout,
       mem_wb_1_immout, mem_wb_1_memdataout, multiplexer_1_out, multiplexer_4_out, multiplexer_5_out,
       multiplexer_6_out, multiplexer_7_out, multiplexer_8_out, multiplexer_10_out, PC_4, ram_1_data,
       regifile_1_r1, regifile_1_r2, shifter_1_out, shifter_2_out, shifter_3_out, WB_IR;

  Button \u_总复位  (.out(RST));
  Button _1 (.out(IR1));
  Button _2 (.out(IR2));
  Button _3 (.out(IR3));
  // Probe on \总周期数 
  // Probe on \总周期数 
  Button \u_继续运行  (.out(Go));
  LED #(.active("true")) led_1 (.in(W1));
  LED #(.active("true")) led_2 (.in(W2));
  LED #(.active("true")) led_3 (.in(W3));
  Hex_Digit_Display hex_digit_display_1 (.value(LedData[31:28]));  // open: dp
  // Probe on IF_PC[19:0]
  // RiscV_Probe riscv_probe_1: pin names not known; wires that end beside it: IF_IR
  Priority_Encoder #(.select(2), .disabled("Z")) priority_encoder_1 (
    .in0(1'b1), .in1(B), .in2(JAL), .in3(JALR), .out(priority_encoder_1_out));  // open: gs, en_out, en_in
  Hex_Digit_Display hex_digit_display_2 (.value(LedData[27:24]));  // open: dp
  Hex_Digit_Display hex_digit_display_3 (.value(LedData[23:20]));  // open: dp
  // Probe on ID_PC[19:0]
  // RiscV_Probe riscv_probe_2: pin names not known; wires that end beside it: ID_IR
  Multiplexer #(.select(2), .width(32), .disabled("Z"), .enable("false")) multiplexer_1 (
    .in0(PC_4), .in1(b_t), .in2(jal_t), .in3(jalr_t), .out(multiplexer_1_out), .sel(priority_encoder_1_out));
  or or_1 (or_1_out, Go, not_1_out);
  not not_1 (not_1_out, halt);
  or or_2 (or_2_out, Go, not_2_out);
  not not_2 (not_2_out, halt);
  Hex_Digit_Display hex_digit_display_4 (.value(LedData[19:16]));  // open: dp
  Hex_Digit_Display hex_digit_display_5 (.value(LedData[15:12]));  // open: dp
  Register #(.width(32), .trigger("rising"), .Select("low")) PC (
    .D(multiplexer_1_out), .en(or_1_out), .Q(IF_PC), .clk(CLK), .clr(RST));
  Counter #(.width(16), .max('hffff), .ongoal("wrap"), .trigger("rising"), .behavior("new")) counter_1 (
    .count(or_2_out), .Q(\总周期数 ), .clk(CLK), .clr(RST));  // open: load, D, carry, preset, down
  Hex_Digit_Display hex_digit_display_6 (.value(LedData[11:8]));  // open: dp
  Hex_Digit_Display hex_digit_display_7 (.value(LedData[7:4]));  // open: dp
  // Probe on EX_PC[19:0]
  // RiscV_Probe riscv_probe_3: pin names not known; wires that end beside it: EX_IR
  Adder #(.width(32)) adder_1 (.a(IF_PC), .b(32'h4), .out(PC_4));  // open: cin, cout
  Hex_Digit_Display hex_digit_display_8 (.value(LedData[3:0]));  // open: dp
  ROM #(.addrWidth(10), .dataWidth(32), .Select("high")) rom_1 (.addr(IF_PC[11:2]), .data(IF_IR));
  nor nor_1 (nor_1_out, Go, not_3_out);
  not not_3 (not_3_out, halt);
  // Probe on \总周期数 
  // Probe on M_PC[19:0]
  // RiscV_Probe riscv_probe_4: pin names not known; wires that end beside it: MEM_IR
  // Probe on \总周期数 
  // Probe on \无条件分支数 
  // Probe on \条件分支成功数 
  // Probe on \插入气泡数 
  // Probe on \LoadUse次数 
  IF_ID if_id_1 (
    .IR(IF_IR), .PC(IF_PC), .IROUT(ID_IR), .PCOUT(ID_PC), .CLK(CLK), .RST(RST), .FLUSH(1'b0), .EN(nor_1_out));  // open: PREDICT, PREDICTOUT
  // Probe on IF_PC[11:0]
  // Probe on WB_PC[19:0]
  // RiscV_Probe riscv_probe_5: pin names not known; wires that end beside it: WB_IR
  // RiscV_Probe riscv_probe_6: pin names not known; wires that end beside it: CLK, RST, ID_IR
  // Probe on EX_PC[11:0]
  // Probe on ID_PC[11:0]
  // Probe on M_PC[11:0]
  D_Flip_Flop #(.trigger("high"), .Pre_Clr_Positions("LEGACY"), .NegatePresetClear("false"), .enable("true"), .NewFFLayout("false")) d_ff_1 (.Q(d_ff_1_q));  // open: clk, D, Qn, preset, en, reset
  // Probe on 13'hc
  Multiplexer #(.select(1), .width(5), .disabled("Z"), .enable("false")) multiplexer_2 (
    .in0(ID_IR[19:15]), .in1(5'b10001), .out(multiplexer_2_out), .sel(ecall));
  assign bit_extender_1_out = {{20{ID_IR[31]}}, ID_IR[31:20]};  // Bit_Extender bit_extender_1
  assign bit_extender_2_out = {{20{ID_IR[31]}}, {ID_IR[31:25], ID_IR[11:7]}};  // Bit_Extender bit_extender_2
  assign bit_extender_3_out = {{12{ID_IR[31]}}, ID_IR[31:12]};  // Bit_Extender bit_extender_3
  // Probe on WB_PC[11:0]
  Comparator #(.width(13), .mode("twosComplement")) comparator_1 (
    .a(CNT_num), .b(13'hc), .eq(comparator_1_eq), .lt(comparator_1_lt));  // open: gt
  Clock #(.highDuration(1), .lowDuration(1)) clock_1 (.out(clock_1_out));
  \单周期硬布线控制器  \u_单周期硬布线控制器_1  (
    .Funct({ID_IR[30], ID_IR[25], ID_IR[14:12]}), .OP(ID_IR[6:2]), .ALU_OP(\单周期硬布线控制器_1_alu_op ),
    .MemToReg(\单周期硬布线控制器_1_memtoreg ), .MemWrite(\单周期硬布线控制器_1_memwrite ), .ALU_SRC(\单周期硬布线控制器_1_alu_src ),
    .RegWrite(\单周期硬布线控制器_1_regwrite ), .ecall(ecall), .S_type(S_Type), .Jalr(\单周期硬布线控制器_1_jalr ),
    .Beq(\单周期硬布线控制器_1_beq ), .JAL(\单周期硬布线控制器_1_jal ), .Bne(\单周期硬布线控制器_1_bne ), .in_3(ID_IR[21]),
    .uret(\单周期硬布线控制器_1_uret ), .blt(\单周期硬布线控制器_1_blt ), .U_type(\单周期硬布线控制器_1_u_type ), .lhu(\单周期硬布线控制器_1_lhu ));  // open: csrrsi, csrrci
  Multiplexer #(.select(1), .width(5), .disabled("Z"), .enable("false")) multiplexer_3 (
    .in0(ID_IR[24:20]), .in1(5'b01010), .out(multiplexer_3_out), .sel(ecall));
  assign bit_extender_4_out = {{20{ID_IR[31]}}, {ID_IR[31], ID_IR[7], ID_IR[30:25], ID_IR[11:8]}};  // Bit_Extender bit_extender_4
  assign bit_extender_5_out = {{12{ID_IR[31]}}, {ID_IR[31], ID_IR[19:12], ID_IR[20], ID_IR[30:21]}};  // Bit_Extender bit_extender_5
  nand nand_1 (nand_1_out, d_ff_1_q, comparator_1_eq);
  Counter #(.width(13), .max('h1fff), .ongoal("stay"), .trigger("rising"), .behavior("old")) counter_2 (
    .count(comparator_1_lt), .Q(CNT_num), .clk(clock_1_out));  // open: load, D, carry, clr, preset
  Multiplexer #(.select(1), .width(32), .disabled("Z"), .enable("false")) multiplexer_4 (
    .in0(bit_extender_1_out), .in1(bit_extender_2_out), .out(multiplexer_4_out), .sel(S_Type));
  Shifter #(.width(32), .shift("ll")) shifter_1 (.in(bit_extender_3_out), .\dist (5'b01100), .out(shifter_1_out));
  Shifter #(.width(32), .shift("ll")) shifter_2 (.in(bit_extender_4_out), .\dist (5'b00001), .out(shifter_2_out));
  Shifter #(.width(32), .shift("ll")) shifter_3 (.in(bit_extender_5_out), .\dist (5'b00001), .out(shifter_3_out));
  assign CLK = nand_1_out ? clock_1_out : 1'bz;  // Controlled_Buffer controlled_buffer_1
  Regifile regifile_1 (
    .Din(RDin), .Clk(CLK), .R1(regifile_1_r1), .R2(regifile_1_r2), .WE(RegWrite), .W_num(W_num),
    .R1_num(multiplexer_2_out), .R2_num(multiplexer_3_out));
  Pull_Resistor #(.pull(1)) pull_resistor_1 (.node(CLK));
  ID_EX id_ex_1 (
    .CLK(CLK), .RST(RST), .JAL(\单周期硬布线控制器_1_jal ), .JALOUT(JAL), .JALR(\单周期硬布线控制器_1_jalr ), .JALROUT(JALR),
    .URET(\单周期硬布线控制器_1_uret ), .beq(\单周期硬布线控制器_1_beq ), .BEQOUT(id_ex_1_beqout), .BNE(\单周期硬布线控制器_1_bne ),
    .BNEOUT(id_ex_1_bneout), .MEMTOREG(\单周期硬布线控制器_1_memtoreg ), .MEMTOREGOUT(id_ex_1_memtoregout),
    .MEMWRITE(\单周期硬布线控制器_1_memwrite ), .MEMWRITEOUT(id_ex_1_memwriteout), .ALUOP(\单周期硬布线控制器_1_alu_op ),
    .ALUOPOUT(id_ex_1_aluopout), .ALUSRC(\单周期硬布线控制器_1_alu_src ), .ALUSRCOUT(id_ex_1_alusrcout),
    .REGWRITE(\单周期硬布线控制器_1_regwrite ), .REGWRITEOUT(id_ex_1_regwriteout), .U_type(\单周期硬布线控制器_1_u_type ),
    .UTYPEOUT(id_ex_1_utypeout), .BLT(\单周期硬布线控制器_1_blt ), .BLTOUT(blt), .ECALL(ecall),
    .ECALLOUT(id_ex_1_ecallout), .lhu(\单周期硬布线控制器_1_lhu ), .lhuOUT(id_ex_1_lhuout), .R1(regifile_1_r1),
    .R1OUT(id_ex_1_r1out), .R2(regifile_1_r2), .R2OUT_prime(id_ex_1_r2out_prime), .WRITEREG(ID_IR[11:7]),
    .WRITEREGOUT_prime(id_ex_1_writeregout_prime), .PC(ID_PC), .PCOUT_prime(EX_PC), .IR(ID_IR),
    .IROUT_prime(EX_IR), .IMM1(multiplexer_4_out), .IMM1OUT_prime(id_ex_1_imm1out_prime),
    .IMM2(shifter_2_out), .IMM2OUT_prime(id_ex_1_imm2out_prime), .IMM3(shifter_3_out),
    .IMM3OUT_prime(id_ex_1_imm3out_prime), .IMM4(shifter_1_out), .IMM4OUT_prime(id_ex_1_imm4out_prime),
    .EN(nor_1_out), .FLUSH(1'b0));  // open: URETOUT, R1F, R1FOUT, R2F, R2FOUT, PREDICT, PREDICTOUT
  or or_3 (or_3_out, JALR, JAL);
  and and_1 (en, id_ex_1_ecallout, comparator_2_eq);
  Comparator #(.width(32), .mode("twosComplement")) comparator_2 (
    .a(id_ex_1_r1out), .b(32'h22), .eq(comparator_2_eq));  // open: gt, lt
  Adder #(.width(32)) adder_2 (.a(id_ex_1_imm4out_prime), .b(EX_PC), .out(adder_2_out));  // open: cin, cout
  Adder #(.width(32)) adder_3 (.a(EX_PC), .b(id_ex_1_imm2out_prime), .out(b_t));  // open: cin, cout
  Adder #(.width(32)) adder_4 (.a(id_ex_1_imm3out_prime), .b(EX_PC), .out(jal_t));  // open: cin, cout
  assign jalr_t = aluresult & 32'hfffffffe;  // AND_Gate and_2, 32 bits wide
  and and_3 (and_3_out, id_ex_1_ecallout, not_4_out);
  not not_4 (not_4_out, comparator_2_eq);
  Multiplexer #(.select(1), .width(32), .disabled("Z"), .enable("false")) multiplexer_5 (
    .in0({32{1'b0}}), .in1(id_ex_1_r2out_prime), .out(multiplexer_5_out), .sel(en));
  and and_4 (and_4_out, id_ex_1_beqout, alu_1_equal);
  Multiplexer #(.select(1), .width(32), .disabled("Z"), .enable("false")) multiplexer_6 (
    .in0(id_ex_1_r2out_prime), .in1(id_ex_1_imm1out_prime), .out(multiplexer_6_out), .sel(id_ex_1_alusrcout));
  Register #(.width(32), .trigger("rising"), .Select("low")) register_1 (
    .D(multiplexer_5_out), .en(en), .Q(LedData), .clk(CLK));  // open: clr
  and and_5 (and_5_out, id_ex_1_bneout, not_5_out);
  not not_5 (not_5_out, alu_1_equal);
  ALU alu_1 (
    .X(id_ex_1_r1out), .Y(multiplexer_6_out), .AluOP(id_ex_1_aluopout), .Equal(alu_1_equal),
    .Result(aluresult), .out_6(alu_1_out_6));  // open: Result_2, out_4
  Adder #(.width(32)) adder_5 (.a(EX_PC), .b(32'h4), .out(adder_5_out));  // open: cin, cout
  or or_4 (or_4_out, and_4_out, and_5_out);
  and and_6 (and_6_out, blt, alu_1_out_6);
  or or_5 (B, and_6_out, or_4_out);
  EX_MEM ex_mem_1 (
    .J(or_3_out), .MEMWRITE(id_ex_1_memwriteout), .MEMTOREG(id_ex_1_memtoregout),
    .REGWRITE(id_ex_1_regwriteout), .UTYPE(id_ex_1_utypeout), .HALT(and_3_out), .lhu(id_ex_1_lhuout),
    .ALURESULT(aluresult), .WRITEDATA_R2(id_ex_1_r2out_prime), .WRITEREG(id_ex_1_writeregout_prime),
    .PC(EX_PC), .IR(EX_IR), .IMM(adder_5_out), .AUIPC_IMM(adder_2_out), .JOUT(ex_mem_1_jout),
    .MEMWRITEOUT(MemWrite), .MEMTOREGOUT(ex_mem_1_memtoregout), .REGWRITEOUT(ex_mem_1_regwriteout),
    .UTYPEOUT(ex_mem_1_utypeout), .HALTOUT(ex_mem_1_haltout), .lhuOUT(ex_mem_1_lhuout),
    .ALURESULTOUT(ex_mem_1_aluresultout), .WRITEDATAOUT_R2(MDin), .WRITEREGOUT(ex_mem_1_writeregout),
    .PCOUT(M_PC), .IROUT(MEM_IR), .IMMOUT(ex_mem_1_immout), .AUPICIMMOUT(ex_mem_1_aupicimmout), .CLK(CLK),
    .RST(RST), .FLUSH(1'b0), .EN(nor_1_out));
  RAM #(.addrWidth(10), .dataWidth(32), .bus("separate"), .Select("high")) ram_1 (
    .addr(ex_mem_1_aluresultout[11:2]), .din(MDin), .data(ram_1_data), .str(MemWrite), .clk(CLK),
    .ld(not_6_out));  // open: sel, clr
  not not_6 (not_6_out, MemWrite);
  MEM_WB mem_wb_1 (
    .J(ex_mem_1_jout), .MEMTOREG(ex_mem_1_memtoregout), .REGWRITE(ex_mem_1_regwriteout),
    .UTYPE(ex_mem_1_utypeout), .HALT(ex_mem_1_haltout), .ALURESULT(ex_mem_1_aluresultout),
    .MEMDATA(ram_1_data), .lhu(ex_mem_1_lhuout), .WRITEREG(ex_mem_1_writeregout), .PC(M_PC), .IR(MEM_IR),
    .IMM(ex_mem_1_immout), .AUIPCIMM(ex_mem_1_aupicimmout), .JOUT(mem_wb_1_jout),
    .MEMTOREGOUT(mem_wb_1_memtoregout), .REGWRITEOUT(RegWrite), .UTYPEOUT(mem_wb_1_utypeout), .HALTOUT(halt),
    .ALURESULTOUT(mem_wb_1_aluresultout), .MEMDATAOUT(mem_wb_1_memdataout), .lhuout(mem_wb_1_lhuout),
    .WRITEREGOUT(W_num), .PCOUT(WB_PC), .IROUT(WB_IR), .IMMOUT(mem_wb_1_immout),
    .AUIPCIMMOUT(mem_wb_1_auipcimmout), .CLK(CLK), .RST(RST), .FLUSH(1'b0), .EN(nor_1_out));
  Multiplexer #(.select(1), .width(32), .disabled("Z"), .enable("false")) multiplexer_7 (
    .in0(mem_wb_1_aluresultout), .in1(mem_wb_1_memdataout), .out(multiplexer_7_out),
    .sel(mem_wb_1_memtoregout));
  Multiplexer #(.select(1), .width(32), .disabled("Z"), .enable("false")) multiplexer_8 (
    .in0(multiplexer_7_out), .in1(mem_wb_1_auipcimmout), .out(multiplexer_8_out), .sel(mem_wb_1_utypeout));
  Multiplexer #(.select(1), .width(16), .disabled("Z"), .enable("false")) multiplexer_9 (
    .in0(mem_wb_1_memdataout[15:0]), .in1(mem_wb_1_memdataout[31:16]), .out(multiplexer_9_out),
    .sel(mem_wb_1_aluresultout[1]));
  Multiplexer #(.select(1), .width(32), .disabled("Z"), .enable("false")) multiplexer_10 (
    .in0(multiplexer_8_out), .in1(mem_wb_1_immout), .out(multiplexer_10_out), .sel(mem_wb_1_jout));
  assign bit_extender_6_out = {{16{1'b0}}, multiplexer_9_out};  // Bit_Extender bit_extender_6
  Multiplexer #(.select(1), .width(32), .disabled("Z"), .enable("false")) multiplexer_11 (
    .in0(multiplexer_10_out), .in1(bit_extender_6_out), .out(RDin), .sel(mem_wb_1_lhuout));

  // Other names for the same wires on the sheet: writereg[4:0] = ID_IR[11:7]; MEM_PC[31:0] = M_PC

  // Notes on the sheet:
  //   中断源
  //   时空图监测，可删除
  //   中断等待指示
  //   数码管输出
  //   取指
  //   contents of rom_1 (hex, n*v repeats v):
  //   413 493 913 993 46413 14e493 296913 39e993 842023 942223 1242423 1342623 a00893 493 913 993 73
  //   指令探针
  //   指令存储器
  //   控制位
  //   指令字
  //   I型
  //   S型
  //   U型
  //   流水调试日志用
  //   暂停节拍，不能为0
  //   用这个时钟源需要去掉电路中的其他时钟源
  //   译码
  //   JAL
  //   blt
  //   JALR
  //   URET
  //   lhu
  //   B型Imm
  //   J型Imm
  //   戳工具置1进入计数暂停模式，ctrl+k时钟自动运行到对应节拍暂停
  //   ctrl+k关闭时钟连续运行，将控制位置零，进入单步调试模式调试
  //   Beq
  //   Bne
  //   MemToReg
  //   MemWrite
  //   AluOP
  //   AluSrcB
  //   RegWrite
  //   S_Type
  //   可计数暂停的时钟源
  //   auipc
  //   为方便自动评测，需要输出流水线各段保存的PC值，注意是PC不是PC+4，另外ID段寄存器写入信息，Mem段内存写入信息也要输出
  //   jal
  //   jalr
  //   beq/bne/blt
  //   执行
  //   PC+4
  //   访存
  //   数据存储器
  //   写回
endmodule
module \气泡流水线  (
  output RegWrite,
  output MemWrite,
  output [31:0] IF_PC,
  output [31:0] ID_PC,
  output [31:0] EX_PC,
  output [31:0] M_PC,
  output [31:0] WB_PC,
  output [31:0] RDin,
  output [31:0] MDin,
  output [31:0] LedData
);

  wire alu_1_equal, alu_1_out_6, and_1_out, and_2_out, and_3_out, and_6_out, and_7_out, and_8_out, and_9_out,
       and_10_out, B, blt, Branch, CLK, clock_1_out, comparator_1_eq, comparator_1_lt, comparator_2_eq,
       d_ff_1_q, ecall, en, ex_mem_1_haltout, ex_mem_1_jout, ex_mem_1_lhuout, ex_mem_1_memtoregout,
       ex_mem_1_utypeout, EX_RegWrite, Go, halt, id_ex_1_alusrcout, id_ex_1_beqout, id_ex_1_bneout,
       id_ex_1_ecallout, id_ex_1_lhuout, id_ex_1_memtoregout, id_ex_1_memwriteout, id_ex_1_utypeout, IR1,
       IR2, IR3, JAL, JALR, MEM_RegWrite, mem_wb_1_jout, mem_wb_1_lhuout, mem_wb_1_memtoregout,
       mem_wb_1_utypeout, nand_1_out, not_1_out, not_2_out, not_3_out, not_4_out, not_5_out, or_2_out,
       or_3_out, or_4_out, or_5_out, or_6_out, or_7_out, or_8_out, or_9_out, pause, RST, S_Type, W1, W2, W3,
       \单周期硬布线控制器_1_alu_src , \单周期硬布线控制器_1_beq , \单周期硬布线控制器_1_blt , \单周期硬布线控制器_1_bne , \单周期硬布线控制器_1_jal ,
       \单周期硬布线控制器_1_jalr , \单周期硬布线控制器_1_lhu , \单周期硬布线控制器_1_memtoreg , \单周期硬布线控制器_1_memwrite ,
       \单周期硬布线控制器_1_regwrite , \单周期硬布线控制器_1_u_type , \单周期硬布线控制器_1_uret ;
  wire [1:0] priority_encoder_1_out;
  wire [3:0] id_ex_1_aluopout, \单周期硬布线控制器_1_alu_op ;
  wire [4:0] EX_WriteReg, MEM_WriteReg, multiplexer_2_out, multiplexer_3_out, W_num;
  wire [12:0] CNT_num;
  wire [15:0] \LoadUse次数 , multiplexer_9_out, \总周期数 , \插入气泡数 , \无条件分支数 , \条件分支成功数 ;
  wire [31:0] adder_2_out, adder_5_out, aluresult, b_t, bit_extender_1_out, bit_extender_2_out,
       bit_extender_3_out, bit_extender_4_out, bit_extender_5_out, bit_extender_6_out, EX_IR,
       ex_mem_1_aluresultout, ex_mem_1_aupicimmout, ex_mem_1_immout, id_ex_1_imm1out_prime,
       id_ex_1_imm2out_prime, id_ex_1_imm3out_prime, id_ex_1_imm4out_prime, id_ex_1_r1out,
       id_ex_1_r2out_prime, ID_IR, IF_IR, jal_t, jalr_t, MEM_IR, mem_wb_1_aluresultout, mem_wb_1_auipcimmout,
       mem_wb_1_immout, mem_wb_1_memdataout, multiplexer_1_out, multiplexer_4_out, multiplexer_5_out,
       multiplexer_6_out, multiplexer_7_out, multiplexer_8_out, multiplexer_10_out, PC_4, ram_1_data,
       \regfile气泡_重定向_1_r1 , \regfile气泡_重定向_1_r2 , shifter_1_out, shifter_2_out, shifter_3_out, WB_IR;

  Button \u_总复位  (.out(RST));
  Button _1 (.out(IR1));
  Button _2 (.out(IR2));
  Button _3 (.out(IR3));
  // Probe on \总周期数 
  // Probe on \总周期数 
  Button \u_继续运行  (.out(Go));
  LED #(.active("true")) led_1 (.in(W1));
  LED #(.active("true")) led_2 (.in(W2));
  LED #(.active("true")) led_3 (.in(W3));
  or or_1 (Branch, B, JAL, JALR);
  Hex_Digit_Display hex_digit_display_1 (.value(LedData[31:28]));  // open: dp
  // Probe on IF_PC[19:0]
  // RiscV_Probe riscv_probe_1: pin names not known; wires that end beside it: IF_IR
  Priority_Encoder #(.select(2), .disabled("Z")) priority_encoder_1 (
    .in0(1'b1), .in1(B), .in2(JAL), .in3(JALR), .out(priority_encoder_1_out));  // open: gs, en_out, en_in
  Hex_Digit_Display hex_digit_display_2 (.value(LedData[23:20]));  // open: dp
  Hex_Digit_Display hex_digit_display_3 (.value(LedData[27:24]));  // open: dp
  // Probe on ID_PC[19:0]
  // RiscV_Probe riscv_probe_2: pin names not known; wires that end beside it: ID_IR
  \气泡冲突检测逻辑  \u_气泡冲突检测逻辑_1  (
    .MEM_REGWRITE(MEM_RegWrite), .EX_REGWRITE(EX_RegWrite), .EX_WRITEREG(EX_WriteReg),
    .MEM_WRITEREG(MEM_WriteReg), .ID_IR(ID_IR), .confl(pause));
  Multiplexer #(.select(2), .width(32), .disabled("Z"), .enable("false")) multiplexer_1 (
    .in0(PC_4), .in1(b_t), .in2(jal_t), .in3(jalr_t), .out(multiplexer_1_out), .sel(priority_encoder_1_out));
  and and_1 (and_1_out, ~pause, or_2_out);  // AND_Gate
  or or_2 (or_2_out, Go, not_1_out);
  not not_1 (not_1_out, halt);
  or or_3 (or_3_out, Go, not_2_out);
  not not_2 (not_2_out, halt);
  Hex_Digit_Display hex_digit_display_4 (.value(LedData[15:12]));  // open: dp
  Hex_Digit_Display hex_digit_display_5 (.value(LedData[19:16]));  // open: dp
  Register #(.width(32), .trigger("rising"), .Select("low")) PC (
    .D(multiplexer_1_out), .en(and_1_out), .Q(IF_PC), .clk(CLK), .clr(RST));
  Counter #(.width(16), .max('hffff), .ongoal("wrap"), .trigger("rising"), .behavior("new")) counter_1 (
    .count(or_3_out), .Q(\总周期数 ), .clk(CLK), .clr(RST));  // open: load, D, carry, preset, down
  Hex_Digit_Display hex_digit_display_6 (.value(LedData[11:8]));  // open: dp
  Hex_Digit_Display hex_digit_display_7 (.value(LedData[7:4]));  // open: dp
  // Probe on EX_PC[19:0]
  // RiscV_Probe riscv_probe_3: pin names not known; wires that end beside it: EX_IR
  Adder #(.width(32)) adder_1 (.a(IF_PC), .b(32'h4), .out(PC_4));  // open: cin, cout
  Hex_Digit_Display hex_digit_display_8 (.value(LedData[3:0]));  // open: dp
  ROM #(.addrWidth(10), .dataWidth(32), .Select("high")) rom_1 (.addr(IF_PC[11:2]), .data(IF_IR));
  // Probe on \总周期数 
  // Probe on M_PC[19:0]
  // RiscV_Probe riscv_probe_4: pin names not known; wires that end beside it: MEM_IR
  // Probe on \总周期数 
  // Probe on \无条件分支数 
  // Probe on \条件分支成功数 
  // Probe on \插入气泡数 
  // Probe on \LoadUse次数 
  IF_ID if_id_1 (
    .IR(IF_IR), .PC(IF_PC), .IROUT(ID_IR), .PCOUT(ID_PC), .CLK(CLK), .RST(RST), .FLUSH(Branch), .EN(or_4_out));  // open: PREDICT, PREDICTOUT
  or or_4 (or_4_out, and_2_out, pause);
  and and_2 (and_2_out, ~Go, halt);  // AND_Gate
  // Probe on IF_PC[11:0]
  // Probe on WB_PC[19:0]
  // RiscV_Probe riscv_probe_5: pin names not known; wires that end beside it: WB_IR, pause
  // RiscV_Probe riscv_probe_6: pin names not known; wires that end beside it: CLK, RST, ID_IR
  // Probe on EX_PC[11:0]
  // Probe on ID_PC[11:0]
  // Probe on M_PC[11:0]
  D_Flip_Flop #(.trigger("high"), .Pre_Clr_Positions("LEGACY"), .NegatePresetClear("false"), .enable("true"), .NewFFLayout("false")) d_ff_1 (.Q(d_ff_1_q));  // open: clk, D, Qn, preset, en, reset
  // Probe on 13'hc
  Counter #(.width(16), .max('hffff), .ongoal("wrap"), .trigger("rising"), .behavior("new")) counter_2 (
    .count(pause), .Q(\插入气泡数 ), .clk(CLK), .clr(RST));  // open: load, D, carry, preset, down
  Multiplexer #(.select(1), .width(5), .disabled("Z"), .enable("false")) multiplexer_2 (
    .in0(ID_IR[19:15]), .in1(5'b10001), .out(multiplexer_2_out), .sel(ecall));
  assign bit_extender_1_out = {{20{ID_IR[31]}}, ID_IR[31:20]};  // Bit_Extender bit_extender_1
  assign bit_extender_2_out = {{20{ID_IR[31]}}, {ID_IR[31:25], ID_IR[11:7]}};  // Bit_Extender bit_extender_2
  assign bit_extender_3_out = {{12{ID_IR[31]}}, ID_IR[31:12]};  // Bit_Extender bit_extender_3
  // Probe on WB_PC[11:0]
  Comparator #(.width(13), .mode("twosComplement")) comparator_1 (
    .a(CNT_num), .b(13'hc), .eq(comparator_1_eq), .lt(comparator_1_lt));  // open: gt
  Clock #(.highDuration(1), .lowDuration(1)) clock_1 (.out(clock_1_out));
  \单周期硬布线控制器  \u_单周期硬布线控制器_1  (
    .Funct({ID_IR[30], ID_IR[25], ID_IR[14:12]}), .OP(ID_IR[6:2]), .ALU_OP(\单周期硬布线控制器_1_alu_op ),
    .MemToReg(\单周期硬布线控制器_1_memtoreg ), .MemWrite(\单周期硬布线控制器_1_memwrite ), .ALU_SRC(\单周期硬布线控制器_1_alu_src ),
    .RegWrite(\单周期硬布线控制器_1_regwrite ), .ecall(ecall), .S_type(S_Type), .Jalr(\单周期硬布线控制器_1_jalr ),
    .Beq(\单周期硬布线控制器_1_beq ), .JAL(\单周期硬布线控制器_1_jal ), .Bne(\单周期硬布线控制器_1_bne ), .in_3(ID_IR[21]),
    .uret(\单周期硬布线控制器_1_uret ), .blt(\单周期硬布线控制器_1_blt ), .U_type(\单周期硬布线控制器_1_u_type ), .lhu(\单周期硬布线控制器_1_lhu ));  // open: csrrsi, csrrci
  Multiplexer #(.select(1), .width(5), .disabled("Z"), .enable("false")) multiplexer_3 (
    .in0(ID_IR[24:20]), .in1(5'b01010), .out(multiplexer_3_out), .sel(ecall));
  assign bit_extender_4_out = {{20{ID_IR[31]}}, {ID_IR[31], ID_IR[7], ID_IR[30:25], ID_IR[11:8]}};  // Bit_Extender bit_extender_4
  assign bit_extender_5_out = {{12{ID_IR[31]}}, {ID_IR[31], ID_IR[19:12], ID_IR[20], ID_IR[30:21]}};  // Bit_Extender bit_extender_5
  nand nand_1 (nand_1_out, d_ff_1_q, comparator_1_eq);
  Counter #(.width(13), .max('h1fff), .ongoal("stay"), .trigger("rising"), .behavior("old")) counter_3 (
    .count(comparator_1_lt), .Q(CNT_num), .clk(clock_1_out));  // open: load, D, carry, clr, preset
  Multiplexer #(.select(1), .width(32), .disabled("Z"), .enable("false")) multiplexer_4 (
    .in0(bit_extender_1_out), .in1(bit_extender_2_out), .out(multiplexer_4_out), .sel(S_Type));
  Shifter #(.width(32), .shift("ll")) shifter_1 (.in(bit_extender_3_out), .\dist (5'b01100), .out(shifter_1_out));
  Shifter #(.width(32), .shift("ll")) shifter_2 (.in(bit_extender_4_out), .\dist (5'b00001), .out(shifter_2_out));
  Shifter #(.width(32), .shift("ll")) shifter_3 (.in(bit_extender_5_out), .\dist (5'b00001), .out(shifter_3_out));
  assign CLK = nand_1_out ? clock_1_out : 1'bz;  // Controlled_Buffer controlled_buffer_1
  \regfile气泡_重定向  \regfile气泡_重定向_1  (
    .Din(RDin), .Clk(CLK), .R1(\regfile气泡_重定向_1_r1 ), .R2(\regfile气泡_重定向_1_r2 ), .WE(RegWrite),
    .W_num(W_num), .R1_num(multiplexer_2_out), .R2_num(multiplexer_3_out));
  Pull_Resistor #(.pull(1)) pull_resistor_1 (.node(CLK));
  ID_EX id_ex_1 (
    .CLK(CLK), .RST(RST), .JAL(\单周期硬布线控制器_1_jal ), .JALOUT(JAL), .JALR(\单周期硬布线控制器_1_jalr ), .JALROUT(JALR),
    .URET(\单周期硬布线控制器_1_uret ), .beq(\单周期硬布线控制器_1_beq ), .BEQOUT(id_ex_1_beqout), .BNE(\单周期硬布线控制器_1_bne ),
    .BNEOUT(id_ex_1_bneout), .MEMTOREG(\单周期硬布线控制器_1_memtoreg ), .MEMTOREGOUT(id_ex_1_memtoregout),
    .MEMWRITE(\单周期硬布线控制器_1_memwrite ), .MEMWRITEOUT(id_ex_1_memwriteout), .ALUOP(\单周期硬布线控制器_1_alu_op ),
    .ALUOPOUT(id_ex_1_aluopout), .ALUSRC(\单周期硬布线控制器_1_alu_src ), .ALUSRCOUT(id_ex_1_alusrcout),
    .REGWRITE(\单周期硬布线控制器_1_regwrite ), .REGWRITEOUT(EX_RegWrite), .U_type(\单周期硬布线控制器_1_u_type ),
    .UTYPEOUT(id_ex_1_utypeout), .BLT(\单周期硬布线控制器_1_blt ), .BLTOUT(blt), .ECALL(ecall),
    .ECALLOUT(id_ex_1_ecallout), .lhu(\单周期硬布线控制器_1_lhu ), .lhuOUT(id_ex_1_lhuout), .R1(\regfile气泡_重定向_1_r1 ),
    .R1OUT(id_ex_1_r1out), .R2(\regfile气泡_重定向_1_r2 ), .R2OUT_prime(id_ex_1_r2out_prime),
    .WRITEREG(ID_IR[11:7]), .WRITEREGOUT_prime(EX_WriteReg), .PC(ID_PC), .PCOUT_prime(EX_PC), .IR(ID_IR),
    .IROUT_prime(EX_IR), .IMM1(multiplexer_4_out), .IMM1OUT_prime(id_ex_1_imm1out_prime),
    .IMM2(shifter_2_out), .IMM2OUT_prime(id_ex_1_imm2out_prime), .IMM3(shifter_3_out),
    .IMM3OUT_prime(id_ex_1_imm3out_prime), .IMM4(shifter_1_out), .IMM4OUT_prime(id_ex_1_imm4out_prime),
    .EN(and_3_out), .FLUSH(or_5_out));  // open: URETOUT, R1F, R1FOUT, R2F, R2FOUT, PREDICT, PREDICTOUT
  or or_5 (or_5_out, Branch, pause);
  and and_3 (and_3_out, ~Go, halt);  // AND_Gate
  or or_6 (or_6_out, JALR, JAL);
  or or_7 (or_7_out, RST, or_6_out);
  Counter #(.width(16), .max('hffff), .ongoal("wrap"), .trigger("rising"), .behavior("new")) counter_4 (
    .count(or_7_out), .Q(\无条件分支数 ), .clk(CLK), .clr(RST));  // open: load, D, carry, preset, down
  and and_4 (en, id_ex_1_ecallout, comparator_2_eq);
  Comparator #(.width(32), .mode("twosComplement")) comparator_2 (
    .a(id_ex_1_r1out), .b(32'h22), .eq(comparator_2_eq));  // open: gt, lt
  Adder #(.width(32)) adder_2 (.a(id_ex_1_imm4out_prime), .b(EX_PC), .out(adder_2_out));  // open: cin, cout
  Adder #(.width(32)) adder_3 (.a(EX_PC), .b(id_ex_1_imm2out_prime), .out(b_t));  // open: cin, cout
  Adder #(.width(32)) adder_4 (.a(id_ex_1_imm3out_prime), .b(EX_PC), .out(jal_t));  // open: cin, cout
  assign jalr_t = aluresult & 32'hfffffffe;  // AND_Gate and_5, 32 bits wide
  and and_6 (and_6_out, id_ex_1_ecallout, not_3_out);
  not not_3 (not_3_out, comparator_2_eq);
  Multiplexer #(.select(1), .width(32), .disabled("Z"), .enable("false")) multiplexer_5 (
    .in0({32{1'b0}}), .in1(id_ex_1_r2out_prime), .out(multiplexer_5_out), .sel(en));
  and and_7 (and_7_out, id_ex_1_beqout, alu_1_equal);
  Multiplexer #(.select(1), .width(32), .disabled("Z"), .enable("false")) multiplexer_6 (
    .in0(id_ex_1_r2out_prime), .in1(id_ex_1_imm1out_prime), .out(multiplexer_6_out), .sel(id_ex_1_alusrcout));
  Register #(.width(32), .trigger("rising"), .Select("low")) register_1 (
    .D(multiplexer_5_out), .en(en), .Q(LedData), .clk(CLK));  // open: clr
  and and_8 (and_8_out, id_ex_1_bneout, not_4_out);
  not not_4 (not_4_out, alu_1_equal);
  ALU alu_1 (
    .X(id_ex_1_r1out), .Y(multiplexer_6_out), .AluOP(id_ex_1_aluopout), .Equal(alu_1_equal),
    .Result(aluresult), .out_6(alu_1_out_6));  // open: Result_2, out_4
  Adder #(.width(32)) adder_5 (.a(EX_PC), .b(32'h4), .out(adder_5_out));  // open: cin, cout
  or or_8 (or_8_out, RST, B);
  or or_9 (or_9_out, and_7_out, and_8_out);
  Counter #(.width(16), .max('hffff), .ongoal("wrap"), .trigger("rising"), .behavior("new")) counter_5 (
    .count(or_8_out), .Q(\条件分支成功数 ), .clk(CLK), .clr(RST));  // open: load, D, carry, preset, down
  and and_9 (and_9_out, blt, alu_1_out_6);
  or or_10 (B, and_9_out, or_9_out);
  and and_10 (and_10_out, ~Go, halt);  // AND_Gate
  EX_MEM ex_mem_1 (
    .J(or_6_out), .MEMWRITE(id_ex_1_memwriteout), .MEMTOREG(id_ex_1_memtoregout), .REGWRITE(EX_RegWrite),
    .UTYPE(id_ex_1_utypeout), .HALT(and_6_out), .lhu(id_ex_1_lhuout), .ALURESULT(aluresult),
    .WRITEDATA_R2(id_ex_1_r2out_prime), .WRITEREG(EX_WriteReg), .PC(EX_PC), .IR(EX_IR), .IMM(adder_5_out),
    .AUIPC_IMM(adder_2_out), .JOUT(ex_mem_1_jout), .MEMWRITEOUT(MemWrite),
    .MEMTOREGOUT(ex_mem_1_memtoregout), .REGWRITEOUT(MEM_RegWrite), .UTYPEOUT(ex_mem_1_utypeout),
    .HALTOUT(ex_mem_1_haltout), .lhuOUT(ex_mem_1_lhuout), .ALURESULTOUT(ex_mem_1_aluresultout),
    .WRITEDATAOUT_R2(MDin), .WRITEREGOUT(MEM_WriteReg), .PCOUT(M_PC), .IROUT(MEM_IR),
    .IMMOUT(ex_mem_1_immout), .AUPICIMMOUT(ex_mem_1_aupicimmout), .CLK(CLK), .RST(RST), .FLUSH(1'b0),
    .EN(and_10_out));
  RAM #(.addrWidth(10), .dataWidth(32), .bus("separate"), .Select("high")) ram_1 (
    .addr(ex_mem_1_aluresultout[11:2]), .din(MDin), .data(ram_1_data), .str(MemWrite), .clk(CLK),
    .ld(not_5_out));  // open: sel, clr
  not not_5 (not_5_out, MemWrite);
  MEM_WB mem_wb_1 (
    .J(ex_mem_1_jout), .MEMTOREG(ex_mem_1_memtoregout), .REGWRITE(MEM_RegWrite), .UTYPE(ex_mem_1_utypeout),
    .HALT(ex_mem_1_haltout), .ALURESULT(ex_mem_1_aluresultout), .MEMDATA(ram_1_data), .lhu(ex_mem_1_lhuout),
    .WRITEREG(MEM_WriteReg), .PC(M_PC), .IR(MEM_IR), .IMM(ex_mem_1_immout), .AUIPCIMM(ex_mem_1_aupicimmout),
    .JOUT(mem_wb_1_jout), .MEMTOREGOUT(mem_wb_1_memtoregout), .REGWRITEOUT(RegWrite),
    .UTYPEOUT(mem_wb_1_utypeout), .HALTOUT(halt), .ALURESULTOUT(mem_wb_1_aluresultout),
    .MEMDATAOUT(mem_wb_1_memdataout), .lhuout(mem_wb_1_lhuout), .WRITEREGOUT(W_num), .PCOUT(WB_PC),
    .IROUT(WB_IR), .IMMOUT(mem_wb_1_immout), .AUIPCIMMOUT(mem_wb_1_auipcimmout), .CLK(CLK), .RST(RST),
    .FLUSH(1'b0), .EN(and_10_out));
  Multiplexer #(.select(1), .width(32), .disabled("Z"), .enable("false")) multiplexer_7 (
    .in0(mem_wb_1_aluresultout), .in1(mem_wb_1_memdataout), .out(multiplexer_7_out),
    .sel(mem_wb_1_memtoregout));
  Multiplexer #(.select(1), .width(32), .disabled("Z"), .enable("false")) multiplexer_8 (
    .in0(multiplexer_7_out), .in1(mem_wb_1_auipcimmout), .out(multiplexer_8_out), .sel(mem_wb_1_utypeout));
  Multiplexer #(.select(1), .width(16), .disabled("Z"), .enable("false")) multiplexer_9 (
    .in0(mem_wb_1_memdataout[15:0]), .in1(mem_wb_1_memdataout[31:16]), .out(multiplexer_9_out),
    .sel(mem_wb_1_aluresultout[1]));
  Multiplexer #(.select(1), .width(32), .disabled("Z"), .enable("false")) multiplexer_10 (
    .in0(multiplexer_8_out), .in1(mem_wb_1_immout), .out(multiplexer_10_out), .sel(mem_wb_1_jout));
  assign bit_extender_6_out = {{16{1'b0}}, multiplexer_9_out};  // Bit_Extender bit_extender_6
  Multiplexer #(.select(1), .width(32), .disabled("Z"), .enable("false")) multiplexer_11 (
    .in0(multiplexer_10_out), .in1(bit_extender_6_out), .out(RDin), .sel(mem_wb_1_lhuout));

  // Other names for the same wires on the sheet: writereg[4:0] = ID_IR[11:7]; MEM_PC[31:0] = M_PC

  // Notes on the sheet:
  //   中断源
  //   时空图监测，可删除
  //   中断等待指示
  //   数码管输出
  //   取指
  //   contents of rom_1 (hex, n*v repeats v):
  //   100493 100006f 100493 200913 300993 100006f 100493 200913 300993 100006f 100493 200913 300993
  //   100006f 100493 200913 300993 414000ef 100413 100493 1f49493 900533 2200893 73 24d493 48463 fedff06f
  //   900533 2200893 73 100493 249493 900533 2200893 73 48463 fedff06f 100493 1f49493 900533 2200893 73
  //   4034d493 900533 2200893 73 4044d493 900533 2200893 73 4044d493 900533 2200893 73 4044d493 900533
  //   2200893 73 4044d493 900533 2200893 73 4044d493 900533 2200893 73 4044d493 900533 2200893 73 4044d493
  //   900533 2200893 73 100413 1f41993 41f9d993 433 c00913 300b13 140413 f47413 800293 100313 499993
  //   89e9b3 1300533 2200893 73 406282b3 fe0294e3 140413 f00f93 1f47433 1c41413 800293 100313 49d993
  //   89e9b3 1300533 2200893 73 406282b3 fe0294e3 1c45413 406b0b33 b0463 f95ff06f 2b3 fff2c293 829293
  //   ff2e293 500533 2200893 73 fff00413 493 84a023 140413 448493 84a023 140413 448493 84a023 140413
  //   448493 84a023 140413 448493 84a023 140413 448493 84a023 140413 448493 84a023 140413 448493 84a023
  //   140413 448493 84a023 140413 448493 84a023 140413 448493 84a023 140413 448493 84a023 140413 448493
  //   84a023 140413 448493 84a023 140413 448493 84a023 140413 448493 84a023 140413 448493 140413 433
  //   3c00493 42983 4aa03 149a2b3 28663 134a023 1442023 ffc48493 fe9412e3 800533 2200893 73 440413 3c00493
  //   fc9416e3 a00893 73 100293 300313 800493 849493 7648493 1449493 900533 2200893 73 800e13 4054d4b3
  //   4064d4b3 900533 2200893 73 fffe0e13 fe0e14e3 a00893 73 13 430497 900533 2200893 73 430497 900533
  //   2200893 73 430497 900533 2200893 73 430497 900533 2200893 73 430497 900533 2200893 73 430497 900533
  //   2200893 73 430497 900533 2200893 73 430497 900533 2200893 73 a00893 73 313 1000e13 8400493 849493
  //   8348493 400913 891913 490913 849493 8248493 849493 8148493 891913 490913 891913 490913 932023
  //   12484b3 430313 fffe0e13 fe0e18e3 2000e13 313 35483 900533 2200893 73 230313 fffe0e13 fe0e14e3 a00893
  //   73 ff100493 900533 2200893 73 148493 fe04c8e3 a00893 73 413 140413 800533 2200893 73 240413 800533
  //   2200893 73 340413 800533 2200893 73 440413 800533 2200893 73 540413 800533 2200893 73 640413 800533
  //   2200893 73 740413 800533 2200893 73 840413 800533 2200893 2200893 73 8067
  //   指令探针
  //   指令存储器
  //   控制位
  //   指令字
  //   I型
  //   S型
  //   U型
  //   流水调试日志用
  //   暂停节拍，不能为0
  //   译码
  //   JAL
  //   blt
  //   JALR
  //   URET
  //   lhu
  //   B型Imm
  //   J型Imm
  //   戳工具置1进入计数暂停模式，ctrl+k时钟自动运行到对应节拍暂停
  //   ctrl+k关闭时钟连续运行，将控制位置零，进入单步调试模式调试
  //   Beq
  //   Bne
  //   MemToReg
  //   MemWrite
  //   AluOP
  //   AluSrcB
  //   RegWrite
  //   S_Type
  //   可计数暂停的时钟源
  //   auipc
  //   为方便自动评测，需要输出流水线各段保存的PC值，注意是PC不是PC+4，另外ID段寄存器写入信息，Mem段内存写入信息也要输出
  //   jal
  //   jalr
  //   beq/bne/blt
  //   执行
  //   PC+4
  //   访存
  //   数据存储器
  //   写回
endmodule

module \重定向流水线  (
  output RegWrite,
  output MemWrite,
  output [31:0] IF_PC,
  output [31:0] ID_PC,
  output [31:0] EX_PC,
  output [31:0] M_PC,
  output [31:0] WB_PC,
  output [31:0] RDin,
  output [31:0] MDin,
  output [31:0] LedData
);

  wire alu_1_equal, alu_1_out_6, and_1_out, and_2_out, and_3_out, and_6_out, and_7_out, and_8_out, and_9_out,
       and_10_out, AUIPC, B, blt, Branch, CLK, clock_1_out, comparator_1_eq, comparator_1_lt,
       comparator_2_eq, d_ff_1_q, ecall, en, ex_mem_1_haltout, ex_mem_1_lhuout, ex_mem_1_memtoregout,
       EX_MemToReg, EX_RegWrite, Go, halt, id_ex_1_alusrcout, id_ex_1_beqout, id_ex_1_bneout,
       id_ex_1_ecallout, id_ex_1_lhuout, id_ex_1_memwriteout, id_ex_1_utypeout, IR1, IR2, IR3, JAL, JALR,
       loaduse, MEM_J, MEM_RegWrite, mem_wb_1_jout, mem_wb_1_lhuout, mem_wb_1_memtoregout, mem_wb_1_utypeout,
       nand_1_out, not_1_out, not_2_out, not_3_out, not_4_out, not_5_out, or_2_out, or_3_out, or_4_out,
       or_5_out, or_6_out, or_7_out, or_8_out, or_9_out, RST, S_Type, W1, W2, W3, \单周期硬布线控制器_1_alu_src ,
       \单周期硬布线控制器_1_beq , \单周期硬布线控制器_1_blt , \单周期硬布线控制器_1_bne , \单周期硬布线控制器_1_jal , \单周期硬布线控制器_1_jalr ,
       \单周期硬布线控制器_1_lhu , \单周期硬布线控制器_1_memtoreg , \单周期硬布线控制器_1_memwrite , \单周期硬布线控制器_1_regwrite ,
       \单周期硬布线控制器_1_u_type , \单周期硬布线控制器_1_uret ;
  wire [1:0] EX_R1F, EX_R2F, priority_encoder_1_out, R1Foward, R2Foward;
  wire [3:0] id_ex_1_aluopout, \单周期硬布线控制器_1_alu_op ;
  wire [4:0] EX_WriteReg, MEM_WriteReg, multiplexer_4_out, multiplexer_5_out, W_num;
  wire [12:0] CNT_num;
  wire [15:0] \LoadUse次数 , multiplexer_13_out, \总周期数 , \无条件分支数 , \条件分支成功数 ;
  wire [31:0] adder_5_out, aluresult, b_t, bit_extender_1_out, bit_extender_2_out, bit_extender_3_out,
       bit_extender_4_out, bit_extender_5_out, bit_extender_6_out, EX_AUIPC, EX_IR, ex_mem_1_aluresultout,
       ex_mem_1_aupicimmout, ex_mem_1_immout, EX_R1, EX_R2, id_ex_1_imm1out_prime, id_ex_1_imm2out_prime,
       id_ex_1_imm3out_prime, id_ex_1_imm4out_prime, ID_IR, IF_IR, jal_t, jalr_t, MEM_IR, MEM_Result,
       mem_wb_1_aluresultout, mem_wb_1_auipcimmout, mem_wb_1_immout, mem_wb_1_memdataout, multiplexer_1_out,
       multiplexer_6_out, multiplexer_7_out, multiplexer_8_out, multiplexer_9_out, multiplexer_11_out,
       multiplexer_12_out, multiplexer_14_out, PC_4, R1R, R2R, ram_1_data, \regfile气泡_重定向_1_r1 ,
       \regfile气泡_重定向_1_r2 , shifter_1_out, shifter_2_out, shifter_3_out, WB_IR;

  Button \u_总复位  (.out(RST));
  Button _1 (.out(IR1));
  Button _2 (.out(IR2));
  Button _3 (.out(IR3));
  // Probe on \总周期数 
  // Probe on \总周期数 
  Button \u_继续运行  (.out(Go));
  LED #(.active("true")) led_1 (.in(W1));
  LED #(.active("true")) led_2 (.in(W2));
  LED #(.active("true")) led_3 (.in(W3));
  Hex_Digit_Display hex_digit_display_1 (.value(LedData[31:28]));  // open: dp
  // Probe on IF_PC[19:0]
  // RiscV_Probe riscv_probe_1: pin names not known; wires that end beside it: IF_IR
  not not_1 (not_1_out, halt);
  or or_1 (Branch, B, JAL, JALR);
  Hex_Digit_Display hex_digit_display_2 (.value(LedData[27:24]));  // open: dp
  Hex_Digit_Display hex_digit_display_3 (.value(LedData[23:20]));  // open: dp
  // Probe on ID_PC[19:0]
  // RiscV_Probe riscv_probe_2: pin names not known; wires that end beside it: ID_IR
  or or_2 (or_2_out, Go, not_1_out);
  Counter #(.width(16), .max('hffff), .ongoal("wrap"), .trigger("rising"), .behavior("new")) counter_1 (
    .count(or_2_out), .Q(\总周期数 ), .clk(CLK), .clr(RST));  // open: load, D, carry, preset, down
  \重定向冲突检测逻辑  \u_重定向冲突检测逻辑_1  (
    .EX_REGWRITE(EX_RegWrite), .MEM_REGWRITE(MEM_RegWrite), .MEM_WRITEREG(MEM_WriteReg),
    .EX_WRITEREG(EX_WriteReg), .EX_MEMTOREG(EX_MemToReg), .ID_IR(ID_IR), .R1FOWARD(R1Foward),
    .LOADUSE(loaduse), .R2FOWARD(R2Foward));
  Priority_Encoder #(.select(2), .disabled("Z")) priority_encoder_1 (
    .in0(1'b1), .in1(B), .in2(JAL), .in3(JALR), .out(priority_encoder_1_out));  // open: gs, en_out, en_in
  Multiplexer #(.select(2), .width(32), .disabled("Z"), .enable("false")) multiplexer_1 (
    .in0(PC_4), .in1(b_t), .in2(jal_t), .in3(jalr_t), .out(multiplexer_1_out), .sel(priority_encoder_1_out));
  and and_1 (and_1_out, ~loaduse, or_3_out);  // AND_Gate
  or or_3 (or_3_out, Go, not_2_out);
  not not_2 (not_2_out, halt);
  Hex_Digit_Display hex_digit_display_4 (.value(LedData[19:16]));  // open: dp
  Hex_Digit_Display hex_digit_display_5 (.value(LedData[15:12]));  // open: dp
  Register #(.width(32), .trigger("rising"), .Select("low")) PC (
    .D(multiplexer_1_out), .en(and_1_out), .Q(IF_PC), .clk(CLK), .clr(RST));
  Hex_Digit_Display hex_digit_display_6 (.value(LedData[11:8]));  // open: dp
  Hex_Digit_Display hex_digit_display_7 (.value(LedData[7:4]));  // open: dp
  // Probe on EX_PC[19:0]
  // RiscV_Probe riscv_probe_3: pin names not known; wires that end beside it: EX_IR
  Adder #(.width(32)) adder_1 (.a(IF_PC), .b(32'h4), .out(PC_4));  // open: cin, cout
  Multiplexer #(.select(2), .width(32), .disabled("Z"), .enable("false")) multiplexer_2 (
    .in0(EX_R1), .in1(RDin), .in2(MEM_Result), .in3(MEM_Result), .out(R1R), .sel(EX_R1F));
  Multiplexer #(.select(2), .width(32), .disabled("Z"), .enable("false")) multiplexer_3 (
    .in0(EX_R2), .in1(RDin), .in2(MEM_Result), .in3(MEM_Result), .out(R2R), .sel(EX_R2F));
  Hex_Digit_Display hex_digit_display_8 (.value(LedData[3:0]));  // open: dp
  ROM #(.addrWidth(10), .dataWidth(32), .Select("high")) rom_1 (.addr(IF_PC[11:2]), .data(IF_IR));
  // Probe on \总周期数 
  // Probe on M_PC[19:0]
  // RiscV_Probe riscv_probe_4: pin names not known; wires that end beside it: MEM_IR
  // Probe on \总周期数 
  // Probe on \无条件分支数 
  // Probe on \条件分支成功数 
  // Probe on \LoadUse次数 
  // Probe on \LoadUse次数 
  IF_ID if_id_1 (
    .IR(IF_IR), .PC(IF_PC), .IROUT(ID_IR), .PCOUT(ID_PC), .CLK(CLK), .RST(RST), .FLUSH(Branch), .EN(or_4_out));  // open: PREDICT, PREDICTOUT
  or or_4 (or_4_out, and_2_out, loaduse);
  and and_2 (and_2_out, ~Go, halt);  // AND_Gate
  // Probe on IF_PC[11:0]
  // Probe on WB_PC[19:0]
  // RiscV_Probe riscv_probe_5: pin names not known; wires that end beside it: WB_IR, loaduse
  // RiscV_Probe riscv_probe_6: pin names not known; wires that end beside it: CLK, RST, ID_IR
  // Probe on ID_PC[11:0]
  // Probe on EX_PC[11:0]
  // Probe on M_PC[11:0]
  D_Flip_Flop #(.trigger("high"), .Pre_Clr_Positions("LEGACY"), .NegatePresetClear("false"), .enable("true"), .NewFFLayout("false")) d_ff_1 (.Q(d_ff_1_q));  // open: clk, D, Qn, preset, en, reset
  // Probe on 13'hc
  Counter #(.width(16), .max('hffff), .ongoal("wrap"), .trigger("rising"), .behavior("new")) counter_2 (
    .count(loaduse), .Q(\LoadUse次数 ), .clk(CLK), .clr(RST));  // open: load, D, carry, preset, down
  Multiplexer #(.select(1), .width(5), .disabled("Z"), .enable("false")) multiplexer_4 (
    .in0(ID_IR[19:15]), .in1(5'b10001), .out(multiplexer_4_out), .sel(ecall));
  // Probe on WB_PC[11:0]
  Comparator #(.width(13), .mode("twosComplement")) comparator_1 (
    .a(CNT_num), .b(13'hc), .eq(comparator_1_eq), .lt(comparator_1_lt));  // open: gt
  Clock #(.highDuration(1), .lowDuration(1)) clock_1 (.out(clock_1_out));
  \单周期硬布线控制器  \u_单周期硬布线控制器_1  (
    .Funct({ID_IR[30], ID_IR[25], ID_IR[14:12]}), .OP(ID_IR[6:2]), .ALU_OP(\单周期硬布线控制器_1_alu_op ),
    .MemToReg(\单周期硬布线控制器_1_memtoreg ), .MemWrite(\单周期硬布线控制器_1_memwrite ), .ALU_SRC(\单周期硬布线控制器_1_alu_src ),
    .RegWrite(\单周期硬布线控制器_1_regwrite ), .ecall(ecall), .S_type(S_Type), .Jalr(\单周期硬布线控制器_1_jalr ),
    .Beq(\单周期硬布线控制器_1_beq ), .JAL(\单周期硬布线控制器_1_jal ), .Bne(\单周期硬布线控制器_1_bne ), .in_3(ID_IR[21]),
    .uret(\单周期硬布线控制器_1_uret ), .blt(\单周期硬布线控制器_1_blt ), .U_type(\单周期硬布线控制器_1_u_type ), .lhu(\单周期硬布线控制器_1_lhu ));  // open: csrrsi, csrrci
  Multiplexer #(.select(1), .width(5), .disabled("Z"), .enable("false")) multiplexer_5 (
    .in0(ID_IR[24:20]), .in1(5'b01010), .out(multiplexer_5_out), .sel(ecall));
  assign bit_extender_1_out = {{20{ID_IR[31]}}, ID_IR[31:20]};  // Bit_Extender bit_extender_1
  assign bit_extender_2_out = {{20{ID_IR[31]}}, {ID_IR[31:25], ID_IR[11:7]}};  // Bit_Extender bit_extender_2
  assign bit_extender_3_out = {{12{ID_IR[31]}}, ID_IR[31:12]};  // Bit_Extender bit_extender_3
  assign bit_extender_4_out = {{20{ID_IR[31]}}, {ID_IR[31], ID_IR[7], ID_IR[30:25], ID_IR[11:8]}};  // Bit_Extender bit_extender_4
  assign bit_extender_5_out = {{12{ID_IR[31]}}, {ID_IR[31], ID_IR[19:12], ID_IR[20], ID_IR[30:21]}};  // Bit_Extender bit_extender_5
  nand nand_1 (nand_1_out, d_ff_1_q, comparator_1_eq);
  Counter #(.width(13), .max('h1fff), .ongoal("stay"), .trigger("rising"), .behavior("old")) counter_3 (
    .count(comparator_1_lt), .Q(CNT_num), .clk(clock_1_out));  // open: load, D, carry, clr, preset
  Multiplexer #(.select(1), .width(32), .disabled("Z"), .enable("false")) multiplexer_6 (
    .in0(bit_extender_1_out), .in1(bit_extender_2_out), .out(multiplexer_6_out), .sel(S_Type));
  Shifter #(.width(32), .shift("ll")) shifter_1 (.in(bit_extender_3_out), .\dist (5'b01100), .out(shifter_1_out));
  Shifter #(.width(32), .shift("ll")) shifter_2 (.in(bit_extender_4_out), .\dist (5'b00001), .out(shifter_2_out));
  Shifter #(.width(32), .shift("ll")) shifter_3 (.in(bit_extender_5_out), .\dist (5'b00001), .out(shifter_3_out));
  assign CLK = nand_1_out ? clock_1_out : 1'bz;  // Controlled_Buffer controlled_buffer_1
  \regfile气泡_重定向  \regfile气泡_重定向_1  (
    .Din(RDin), .Clk(CLK), .R1(\regfile气泡_重定向_1_r1 ), .R2(\regfile气泡_重定向_1_r2 ), .WE(RegWrite),
    .W_num(W_num), .R1_num(multiplexer_4_out), .R2_num(multiplexer_5_out));
  Pull_Resistor #(.pull(1)) pull_resistor_1 (.node(CLK));
  or or_5 (or_5_out, Branch, loaduse);
  and and_3 (and_3_out, ~Go, halt);  // AND_Gate
  ID_EX id_ex_1 (
    .CLK(CLK), .RST(RST), .JAL(\单周期硬布线控制器_1_jal ), .JALOUT(JAL), .JALR(\单周期硬布线控制器_1_jalr ), .JALROUT(JALR),
    .URET(\单周期硬布线控制器_1_uret ), .beq(\单周期硬布线控制器_1_beq ), .BEQOUT(id_ex_1_beqout), .BNE(\单周期硬布线控制器_1_bne ),
    .BNEOUT(id_ex_1_bneout), .MEMTOREG(\单周期硬布线控制器_1_memtoreg ), .MEMTOREGOUT(EX_MemToReg),
    .MEMWRITE(\单周期硬布线控制器_1_memwrite ), .MEMWRITEOUT(id_ex_1_memwriteout), .ALUOP(\单周期硬布线控制器_1_alu_op ),
    .ALUOPOUT(id_ex_1_aluopout), .ALUSRC(\单周期硬布线控制器_1_alu_src ), .ALUSRCOUT(id_ex_1_alusrcout),
    .REGWRITE(\单周期硬布线控制器_1_regwrite ), .REGWRITEOUT(EX_RegWrite), .U_type(\单周期硬布线控制器_1_u_type ),
    .UTYPEOUT(id_ex_1_utypeout), .BLT(\单周期硬布线控制器_1_blt ), .BLTOUT(blt), .ECALL(ecall),
    .ECALLOUT(id_ex_1_ecallout), .lhu(\单周期硬布线控制器_1_lhu ), .lhuOUT(id_ex_1_lhuout), .R1F(R1Foward),
    .R1FOUT(EX_R1F), .R1(\regfile气泡_重定向_1_r1 ), .R1OUT(EX_R1), .R2(\regfile气泡_重定向_1_r2 ),
    .R2OUT_prime(EX_R2), .R2F(R2Foward), .R2FOUT(EX_R2F), .WRITEREG(ID_IR[11:7]),
    .WRITEREGOUT_prime(EX_WriteReg), .PC(ID_PC), .PCOUT_prime(EX_PC), .IR(ID_IR), .IROUT_prime(EX_IR),
    .IMM1(multiplexer_6_out), .IMM1OUT_prime(id_ex_1_imm1out_prime), .IMM2(shifter_2_out),
    .IMM2OUT_prime(id_ex_1_imm2out_prime), .IMM3(shifter_3_out), .IMM3OUT_prime(id_ex_1_imm3out_prime),
    .IMM4(shifter_1_out), .IMM4OUT_prime(id_ex_1_imm4out_prime), .EN(and_3_out), .FLUSH(or_5_out));  // open: URETOUT, PREDICT, PREDICTOUT
  or or_6 (or_6_out, RST, or_7_out);
  or or_7 (or_7_out, JALR, JAL);
  and and_4 (en, id_ex_1_ecallout, comparator_2_eq);
  Comparator #(.width(32), .mode("twosComplement")) comparator_2 (
    .a(R1R), .b(32'h22), .eq(comparator_2_eq));  // open: gt, lt
  Adder #(.width(32)) adder_2 (.a(id_ex_1_imm4out_prime), .b(EX_PC), .out(EX_AUIPC));  // open: cin, cout
  Adder #(.width(32)) adder_3 (.a(EX_PC), .b(id_ex_1_imm2out_prime), .out(b_t));  // open: cin, cout
  Adder #(.width(32)) adder_4 (.a(id_ex_1_imm3out_prime), .b(EX_PC), .out(jal_t));  // open: cin, cout
  Counter #(.width(16), .max('hffff), .ongoal("wrap"), .trigger("rising"), .behavior("new")) counter_4 (
    .count(or_6_out), .Q(\无条件分支数 ), .clk(CLK), .clr(RST));  // open: load, D, carry, preset, down
  not not_3 (not_3_out, comparator_2_eq);
  Multiplexer #(.select(1), .width(32), .disabled("Z"), .enable("false")) multiplexer_7 (
    .in0({32{1'b0}}), .in1(R2R), .out(multiplexer_7_out), .sel(en));
  assign jalr_t = aluresult & 32'hfffffffe;  // AND_Gate and_5, 32 bits wide
  and and_6 (and_6_out, id_ex_1_beqout, alu_1_equal);
  and and_7 (and_7_out, id_ex_1_ecallout, not_3_out);
  Multiplexer #(.select(1), .width(32), .disabled("Z"), .enable("false")) multiplexer_8 (
    .in0(R2R), .in1(id_ex_1_imm1out_prime), .out(multiplexer_8_out), .sel(id_ex_1_alusrcout));
  Register #(.width(32), .trigger("rising"), .Select("low")) register_1 (
    .D(multiplexer_7_out), .en(en), .Q(LedData), .clk(CLK));  // open: clr
  not not_4 (not_4_out, alu_1_equal);
  ALU alu_1 (
    .X(R1R), .Y(multiplexer_8_out), .AluOP(id_ex_1_aluopout), .Equal(alu_1_equal), .Result(aluresult),
    .out_6(alu_1_out_6));  // open: Result_2, out_4
  Adder #(.width(32)) adder_5 (.a(EX_PC), .b(32'h4), .out(adder_5_out));  // open: cin, cout
  or or_8 (or_8_out, RST, B);
  or or_9 (or_9_out, and_6_out, and_8_out);
  and and_8 (and_8_out, id_ex_1_bneout, not_4_out);
  Counter #(.width(16), .max('hffff), .ongoal("wrap"), .trigger("rising"), .behavior("new")) counter_5 (
    .count(or_8_out), .Q(\条件分支成功数 ), .clk(CLK), .clr(RST));  // open: load, D, carry, preset, down
  and and_9 (and_9_out, blt, alu_1_out_6);
  or or_10 (B, and_9_out, or_9_out);
  and and_10 (and_10_out, ~Go, halt);  // AND_Gate
  EX_MEM ex_mem_1 (
    .J(or_7_out), .MEMWRITE(id_ex_1_memwriteout), .MEMTOREG(EX_MemToReg), .REGWRITE(EX_RegWrite),
    .UTYPE(id_ex_1_utypeout), .HALT(and_7_out), .lhu(id_ex_1_lhuout), .ALURESULT(aluresult),
    .WRITEDATA_R2(R2R), .WRITEREG(EX_WriteReg), .PC(EX_PC), .IR(EX_IR), .IMM(adder_5_out),
    .AUIPC_IMM(EX_AUIPC), .JOUT(MEM_J), .MEMWRITEOUT(MemWrite), .MEMTOREGOUT(ex_mem_1_memtoregout),
    .REGWRITEOUT(MEM_RegWrite), .UTYPEOUT(AUIPC), .HALTOUT(ex_mem_1_haltout), .lhuOUT(ex_mem_1_lhuout),
    .ALURESULTOUT(ex_mem_1_aluresultout), .WRITEDATAOUT_R2(MDin), .WRITEREGOUT(MEM_WriteReg), .PCOUT(M_PC),
    .IROUT(MEM_IR), .IMMOUT(ex_mem_1_immout), .AUPICIMMOUT(ex_mem_1_aupicimmout), .CLK(CLK), .RST(RST),
    .FLUSH(1'b0), .EN(and_10_out));
  Multiplexer #(.select(1), .width(32), .disabled("Z"), .enable("false")) multiplexer_9 (
    .in0(ex_mem_1_aluresultout), .in1(ex_mem_1_immout), .out(multiplexer_9_out), .sel(MEM_J));
  not not_5 (not_5_out, MemWrite);
  Multiplexer #(.select(1), .width(32), .disabled("Z"), .enable("false")) multiplexer_10 (
    .in0(multiplexer_9_out), .in1(ex_mem_1_aupicimmout), .out(MEM_Result), .sel(AUIPC));
  RAM #(.addrWidth(10), .dataWidth(32), .bus("separate"), .Select("high")) ram_1 (
    .addr(ex_mem_1_aluresultout[11:2]), .din(MDin), .data(ram_1_data), .str(MemWrite), .clk(CLK),
    .ld(not_5_out));  // open: sel, clr
  MEM_WB mem_wb_1 (
    .J(MEM_J), .MEMTOREG(ex_mem_1_memtoregout), .REGWRITE(MEM_RegWrite), .UTYPE(AUIPC),
    .HALT(ex_mem_1_haltout), .ALURESULT(ex_mem_1_aluresultout), .MEMDATA(ram_1_data), .lhu(ex_mem_1_lhuout),
    .WRITEREG(MEM_WriteReg), .PC(M_PC), .IR(MEM_IR), .IMM(ex_mem_1_immout), .AUIPCIMM(ex_mem_1_aupicimmout),
    .JOUT(mem_wb_1_jout), .MEMTOREGOUT(mem_wb_1_memtoregout), .REGWRITEOUT(RegWrite),
    .UTYPEOUT(mem_wb_1_utypeout), .HALTOUT(halt), .ALURESULTOUT(mem_wb_1_aluresultout),
    .MEMDATAOUT(mem_wb_1_memdataout), .lhuout(mem_wb_1_lhuout), .WRITEREGOUT(W_num), .PCOUT(WB_PC),
    .IROUT(WB_IR), .IMMOUT(mem_wb_1_immout), .AUIPCIMMOUT(mem_wb_1_auipcimmout), .CLK(CLK), .RST(RST),
    .FLUSH(1'b0), .EN(and_10_out));
  Multiplexer #(.select(1), .width(32), .disabled("Z"), .enable("false")) multiplexer_11 (
    .in0(mem_wb_1_aluresultout), .in1(mem_wb_1_memdataout), .out(multiplexer_11_out),
    .sel(mem_wb_1_memtoregout));
  Multiplexer #(.select(1), .width(32), .disabled("Z"), .enable("false")) multiplexer_12 (
    .in0(multiplexer_11_out), .in1(mem_wb_1_auipcimmout), .out(multiplexer_12_out), .sel(mem_wb_1_utypeout));
  Multiplexer #(.select(1), .width(16), .disabled("Z"), .enable("false")) multiplexer_13 (
    .in0(mem_wb_1_memdataout[15:0]), .in1(mem_wb_1_memdataout[31:16]), .out(multiplexer_13_out),
    .sel(mem_wb_1_aluresultout[1]));
  Multiplexer #(.select(1), .width(32), .disabled("Z"), .enable("false")) multiplexer_14 (
    .in0(multiplexer_12_out), .in1(mem_wb_1_immout), .out(multiplexer_14_out), .sel(mem_wb_1_jout));
  assign bit_extender_6_out = {{16{1'b0}}, multiplexer_13_out};  // Bit_Extender bit_extender_6
  Multiplexer #(.select(1), .width(32), .disabled("Z"), .enable("false")) multiplexer_15 (
    .in0(multiplexer_14_out), .in1(bit_extender_6_out), .out(RDin), .sel(mem_wb_1_lhuout));

  // Other names for the same wires on the sheet: writereg[4:0] = ID_IR[11:7]; MEM_PC[31:0] = M_PC;
  //   插入气泡数[15:0] = \LoadUse次数 

  // Notes on the sheet:
  //   中断源
  //   时空图监测，可删除
  //   中断等待指示
  //   取指
  //   数码管输出
  //   contents of rom_1 (hex, n*v repeats v):
  //   100493 100006f 100493 200913 300993 100006f 100493 200913 300993 100006f 100493 200913 300993
  //   100006f 100493 200913 300993 414000ef 100413 100493 1f49493 900533 2200893 73 24d493 48463 fedff06f
  //   900533 2200893 73 100493 249493 900533 2200893 73 48463 fedff06f 100493 1f49493 900533 2200893 73
  //   4034d493 900533 2200893 73 4044d493 900533 2200893 73 4044d493 900533 2200893 73 4044d493 900533
  //   2200893 73 4044d493 900533 2200893 73 4044d493 900533 2200893 73 4044d493 900533 2200893 73 4044d493
  //   900533 2200893 73 100413 1f41993 41f9d993 433 c00913 300b13 140413 f47413 800293 100313 499993
  //   89e9b3 1300533 2200893 73 406282b3 fe0294e3 140413 f00f93 1f47433 1c41413 800293 100313 49d993
  //   89e9b3 1300533 2200893 73 406282b3 fe0294e3 1c45413 406b0b33 b0463 f95ff06f 2b3 fff2c293 829293
  //   ff2e293 500533 2200893 73 fff00413 493 84a023 140413 448493 84a023 140413 448493 84a023 140413
  //   448493 84a023 140413 448493 84a023 140413 448493 84a023 140413 448493 84a023 140413 448493 84a023
  //   140413 448493 84a023 140413 448493 84a023 140413 448493 84a023 140413 448493 84a023 140413 448493
  //   84a023 140413 448493 84a023 140413 448493 84a023 140413 448493 84a023 140413 448493 140413 433
  //   3c00493 42983 4aa03 149a2b3 28663 134a023 1442023 ffc48493 fe9412e3 800533 2200893 73 440413 3c00493
  //   fc9416e3 a00893 73 100293 300313 800493 849493 7648493 1449493 900533 2200893 73 800e13 4054d4b3
  //   4064d4b3 900533 2200893 73 fffe0e13 fe0e14e3 a00893 73 13 430497 900533 2200893 73 430497 900533
  //   2200893 73 430497 900533 2200893 73 430497 900533 2200893 73 430497 900533 2200893 73 430497 900533
  //   2200893 73 430497 900533 2200893 73 430497 900533 2200893 73 a00893 73 313 1000e13 8400493 849493
  //   8348493 400913 891913 490913 849493 8248493 849493 8148493 891913 490913 891913 490913 932023
  //   12484b3 430313 fffe0e13 fe0e18e3 2000e13 313 35483 900533 2200893 73 230313 fffe0e13 fe0e14e3 a00893
  //   73 ff100493 900533 2200893 73 148493 fe04c8e3 a00893 73 413 140413 800533 2200893 73 240413 800533
  //   2200893 73 340413 800533 2200893 73 440413 800533 2200893 73 540413 800533 2200893 73 640413 800533
  //   2200893 73 740413 800533 2200893 73 840413 800533 2200893 2200893 73 8067
  //   指令探针
  //   指令存储器
  //   控制位
  //   指令字
  //   流水调试日志用
  //   暂停节拍，不能为0
  //   JAL
  //   blt
  //   JALR
  //   URET
  //   lhu
  //   I型
  //   S型
  //   U型
  //   B型Imm
  //   J型Imm
  //   戳工具置1进入计数暂停模式，ctrl+k时钟自动运行到对应节拍暂停
  //   ctrl+k关闭时钟连续运行，将控制位置零，进入单步调试模式调试
  //   译码
  //   Beq
  //   Bne
  //   MemToReg
  //   MemWrite
  //   AluOP
  //   AluSrcB
  //   RegWrite
  //   S_Type
  //   可计数暂停的时钟源
  //   为方便自动评测，需要输出流水线各段保存的PC值，注意是PC不是PC+4，另外ID段寄存器写入信息，Mem段内存写入信息也要输出
  //   auipc
  //   beq/bne/blt
  //   jal
  //   jalr
  //   执行
  //   PC+4
  //   访存
  //   数据存储器
  //   写回
endmodule

module \中断按键参考电路  (
  input  \同步清零信号 ,
  output \与中断屏蔽位与 
);

  wire \_1号中断_out , and_1_out, clock_1_out, d_ff_1_q, or_1_out, or_2_out;

  Clock #(.highDuration(1), .lowDuration(1)) clock_1 (.out(clock_1_out));
  Button \_1号中断  (.out(\_1号中断_out ));
  LED #(.active("true")) \_1号中断等待指示灯  (.in(or_1_out));
  or or_1 (or_1_out, \与中断屏蔽位与 , d_ff_1_q);
  D_Flip_Flop #(.trigger("rising"), .Pre_Clr_Positions("LEGACY"), .NegatePresetClear("false"), .enable("true"), .NewFFLayout("false")) d_ff_1 (
    .clk(\_1号中断_out ), .D(1'b1), .Q(d_ff_1_q), .reset(\与中断屏蔽位与 ));  // open: Qn, preset, en
  or or_2 (or_2_out, d_ff_1_q, \与中断屏蔽位与 );
  and and_1 (and_1_out, or_2_out, ~\同步清零信号 );  // AND_Gate
  D_Flip_Flop #(.trigger("rising"), .Pre_Clr_Positions("LEGACY"), .NegatePresetClear("false"), .enable("true"), .NewFFLayout("false")) IR1 (
    .clk(clock_1_out), .D(and_1_out), .Q(\与中断屏蔽位与 ));  // open: Qn, preset, en, reset

  // Notes on the sheet:
  //   中断信号采样参考电路
  //   Reset 
endmodule

module \单周期_单级中断  (
  input  IR1,
  input  IR2,
  input  IR3,
  output RegWrite,
  output MemWrite,
  output [31:0] PC,
  output [31:0] IR,
  output [31:0] RDin,
  output [31:0] MDin,
  output [31:0] LedData
);

  wire AluSrcB, and_1_out, and_2_out, and_3_out, and_8_out, and_9_out, and_10_out, B, Beq, blt, Bne, CLK,
       clock_1_out, CLR1, CLR2, CLR3, comparator_1_eq, comparator_2_eq, comparator_3_eq, comparator_4_eq,
       comparator_5_eq, comparator_6_eq, comparator_6_lt, d_ff_1_q, d_ff_2_q, d_ff_3_q, d_ff_5_q, ecall, en,
       equal, Go, halt, IE, INTR, INTR1, INTR2, INTR3, IR1_t, IR2_t, IR3_t, IRA, IRB, IRC, IRHAVE, J, JAL,
       JALR, less, lhu, MemToReg, nand_1_out, not_1_out, not_2_out, not_3_out, not_4_out, not_5_out,
       or_4_out, or_5_out, or_6_out, or_7_out, or_11_out, or_13_out, or_15_out, or_17_out, S_Type, U_type,
       uret, W1, W2, W3;
  wire [1:0] priority_encoder_1_out, priority_encoder_2_out, priority_encoder_3_out, register_1_q;
  wire [3:0] AluOP;
  wire [4:0] multiplexer_5_out, multiplexer_6_out;
  wire [12:0] CNT_num;
  wire [15:0] multiplexer_11_out, \总周期数 ;
  wire [31:0] adder_2_out, aluresult, b_t, bit_extender_1_out, bit_extender_2_out, bit_extender_3_out,
       bit_extender_4_out, bit_extender_5_out, bit_extender_6_out, IR_PC, jal_t, jalr_t, MDout, MEPC,
       multiplexer_2_out, multiplexer_3_out, multiplexer_4_out, multiplexer_7_out, multiplexer_8_out,
       multiplexer_9_out, multiplexer_10_out, PC_4, R1, result, shifter_1_out, shifter_2_out, shifter_3_out;

  Button \u_继续运行  (.out(Go));
  Button _1 (.out(IRA));
  Button _2 (.out(IRB));
  Button _3 (.out(IRC));
  LED #(.active("true")) led_1 (.in(W1));
  LED #(.active("true")) led_2 (.in(W2));
  LED #(.active("true")) led_3 (.in(W3));
  Hex_Digit_Display hex_digit_display_1 (.value(LedData[31:28]));  // open: dp
  or or_1 (W1, INTR1, d_ff_1_q);
  or or_2 (W2, INTR2, d_ff_2_q);
  or or_3 (W3, INTR3, d_ff_3_q);
  Priority_Encoder #(.select(2), .disabled("Z")) priority_encoder_1 (
    .in0(INTR1), .in1(INTR2), .in2(INTR3), .out(priority_encoder_1_out));  // open: in3, gs, en_out, en_in
  Hex_Digit_Display hex_digit_display_2 (.value(LedData[27:24]));  // open: dp
  Hex_Digit_Display hex_digit_display_3 (.value(LedData[23:20]));  // open: dp
  Comparator #(.width(16), .mode("twosComplement")) comparator_1 (
    .a(16'h23b), .b(\总周期数 ), .eq(comparator_1_eq));  // open: gt, lt
  or or_4 (or_4_out, comparator_1_eq, comparator_2_eq);
  Comparator #(.width(16), .mode("twosComplement")) comparator_2 (
    .a(\总周期数 ), .b(16'h1), .eq(comparator_2_eq));  // open: gt, lt
  Comparator #(.width(16), .mode("twosComplement")) comparator_3 (
    .a(\总周期数 ), .b(16'h4), .eq(comparator_3_eq));  // open: gt, lt
  Comparator #(.width(16), .mode("twosComplement")) comparator_4 (
    .a(\总周期数 ), .b(16'h7), .eq(comparator_4_eq));  // open: gt, lt
  D_Flip_Flop #(.trigger("rising"), .Pre_Clr_Positions("LEGACY"), .NegatePresetClear("false"), .enable("true"), .NewFFLayout("false")) d_ff_1 (
    .clk(IRA), .D(1'b1), .Q(d_ff_1_q), .reset(INTR1));  // open: Qn, preset, en
  D_Flip_Flop #(.trigger("rising"), .Pre_Clr_Positions("LEGACY"), .NegatePresetClear("false"), .enable("true"), .NewFFLayout("false")) d_ff_2 (
    .clk(IRB), .D(1'b1), .Q(d_ff_2_q), .reset(INTR2));  // open: Qn, preset, en
  D_Flip_Flop #(.trigger("rising"), .Pre_Clr_Positions("LEGACY"), .NegatePresetClear("false"), .enable("true"), .NewFFLayout("false")) d_ff_3 (
    .clk(IRC), .D(1'b1), .Q(d_ff_3_q), .reset(INTR3));  // open: Qn, preset, en
  Multiplexer #(.select(2), .width(32), .disabled("Z"), .enable("false")) multiplexer_1 (
    .in0(32'h30ac), .in1(32'h3150), .in2(32'h31f4), .out(IR_PC), .sel(priority_encoder_1_out));  // open: in3
  Hex_Digit_Display hex_digit_display_4 (.value(LedData[19:16]));  // open: dp
  Hex_Digit_Display hex_digit_display_5 (.value(LedData[15:12]));  // open: dp
  Pull_Resistor #(.pull(0)) pull_resistor_1 (.node(IRA));
  assign IRA = or_4_out ? ~CLK : 1'bz;  // Controlled_Inverter controlled_inverter_1
  Pull_Resistor #(.pull(0)) pull_resistor_2 (.node(IRB));
  assign IRB = comparator_3_eq ? ~CLK : 1'bz;  // Controlled_Inverter controlled_inverter_2
  Pull_Resistor #(.pull(0)) pull_resistor_3 (.node(IRC));
  assign IRC = comparator_4_eq ? ~CLK : 1'bz;  // Controlled_Inverter controlled_inverter_3
  or or_5 (or_5_out, d_ff_1_q, INTR1);
  and and_1 (and_1_out, or_5_out, ~CLR1);  // AND_Gate
  or or_6 (or_6_out, d_ff_2_q, INTR2);
  and and_2 (and_2_out, or_6_out, ~CLR2);  // AND_Gate
  or or_7 (or_7_out, d_ff_3_q, INTR3);
  Hex_Digit_Display hex_digit_display_6 (.value(LedData[7:4]));  // open: dp
  Hex_Digit_Display hex_digit_display_7 (.value(LedData[11:8]));  // open: dp
  // Probe on \总周期数 
  D_Flip_Flop #(.trigger("rising"), .Pre_Clr_Positions("LEGACY"), .NegatePresetClear("false"), .enable("true"), .NewFFLayout("false")) u_IR1 (
    .clk(CLK), .D(and_1_out), .Q(INTR1));  // open: Qn, preset, en, reset
  D_Flip_Flop #(.trigger("rising"), .Pre_Clr_Positions("LEGACY"), .NegatePresetClear("false"), .enable("true"), .NewFFLayout("false")) IR1_2 (
    .clk(CLK), .D(and_2_out), .Q(INTR2));  // open: Qn, preset, en, reset
  and and_3 (and_3_out, or_7_out, ~CLR3);  // AND_Gate
  Hex_Digit_Display hex_digit_display_8 (.value(LedData[3:0]));  // open: dp
  D_Flip_Flop #(.trigger("rising"), .Pre_Clr_Positions("LEGACY"), .NegatePresetClear("false"), .enable("true"), .NewFFLayout("false")) IR1_3 (
    .clk(CLK), .D(and_3_out), .Q(INTR3));  // open: Qn, preset, en, reset
  Register #(.width(2), .trigger("rising"), .Select("low")) register_1 (
    .D(priority_encoder_1_out), .en(INTR), .Q(register_1_q), .clk(CLK));  // open: clr
  or or_8 (IRHAVE, INTR1, INTR2, INTR3);
  Demultiplexer #(.select(2), .width(1), .tristate("false"), .disabled("Z"), .enable("false")) demultiplexer_1 (
    .out0(CLR1), .out1(CLR2), .out2(CLR3), .in(uret), .sel(register_1_q));  // open: out3
  or or_9 (IR1_t, IR1, IRA);
  Priority_Encoder #(.select(2), .disabled("Z")) priority_encoder_2 (
    .in0(1'b1), .in1(B), .in2(JAL), .in3(JALR), .out(priority_encoder_2_out));  // open: gs, en_out, en_in
  Multiplexer #(.select(2), .width(32), .disabled("Z"), .enable("false")) multiplexer_2 (
    .in0(PC_4), .in1(b_t), .in2(jal_t), .in3(jalr_t), .out(multiplexer_2_out), .sel(priority_encoder_2_out));
  or or_10 (IR2_t, IR2, IRB);
  and and_4 (INTR, IRHAVE, IE);
  Register #(.width(32), .trigger("rising"), .Select("low")) register_2 (
    .D(multiplexer_2_out), .en(INTR), .Q(MEPC), .clk(CLK));  // open: clr
  or or_11 (or_11_out, ~IRHAVE, uret);  // OR_Gate
  or or_12 (IR3_t, IR3, IRC);
  D_Flip_Flop #(.trigger("rising"), .Pre_Clr_Positions("LEGACY"), .NegatePresetClear("false"), .enable("true"), .NewFFLayout("true")) d_ff_4 (
    .clk(CLK), .D(or_11_out), .Q(IE));  // open: Qn, preset, en, reset
  Priority_Encoder #(.select(2), .disabled("Z")) priority_encoder_3 (
    .in0(1'b1), .in1(INTR), .in2(uret), .out(priority_encoder_3_out));  // open: in3, gs, en_out, en_in
  Multiplexer #(.select(2), .width(32), .disabled("Z"), .enable("false")) multiplexer_3 (
    .in0(multiplexer_2_out), .in1(IR_PC), .in2(MEPC), .out(multiplexer_3_out), .sel(priority_encoder_3_out));  // open: in3
  or or_13 (or_13_out, Go, not_1_out);
  Register #(.width(32), .trigger("rising"), .Select("low")) u_PC (
    .D(multiplexer_3_out), .en(or_13_out), .Q(PC), .clk(CLK));  // open: clr
  not not_1 (not_1_out, halt);
  Adder #(.width(32)) adder_1 (.a(PC), .b(32'h4), .out(PC_4));  // open: cin, cout
  Comparator #(.width(32), .mode("twosComplement")) comparator_5 (
    .a(R1), .b(32'h22), .eq(comparator_5_eq));  // open: gt, lt
  not not_2 (not_2_out, comparator_5_eq);
  and and_5 (halt, not_2_out, ecall);
  Multiplexer #(.select(1), .width(32), .disabled("Z"), .enable("false")) multiplexer_4 (
    .in0({32{1'b0}}), .in1(MDin), .out(multiplexer_4_out), .sel(en));
  // RiscV_Probe riscv_probe_1: pin names not known; wires that end beside it: IR
  and and_6 (en, ecall, comparator_5_eq);
  or or_14 (J, JALR, JAL);
  ROM #(.addrWidth(10), .dataWidth(32), .Select("high")) rom_1 (.addr(PC[11:2]), .data(IR));
  Register #(.width(32), .trigger("rising"), .Select("low")) register_3 (
    .D(multiplexer_4_out), .en(en), .Q(LedData), .clk(CLK));  // open: clr
  Multiplexer #(.select(1), .width(5), .disabled("Z"), .enable("false")) multiplexer_5 (
    .in0(IR[19:15]), .in1(5'b10001), .out(multiplexer_5_out), .sel(ecall));
  D_Flip_Flop #(.trigger("high"), .Pre_Clr_Positions("LEGACY"), .NegatePresetClear("false"), .enable("true"), .NewFFLayout("false")) d_ff_5 (.Q(d_ff_5_q));  // open: clk, D, Qn, preset, en, reset
  // Probe on 13'hc
  \单周期硬布线控制器  \u_单周期硬布线控制器_1  (
    .Funct({IR[30], IR[25], IR[14:12]}), .OP(IR[6:2]), .ALU_OP(AluOP), .MemToReg(MemToReg),
    .MemWrite(MemWrite), .ALU_SRC(AluSrcB), .RegWrite(RegWrite), .ecall(ecall), .S_type(S_Type), .Jalr(JALR),
    .Beq(Beq), .JAL(JAL), .Bne(Bne), .in_3(IR[21]), .uret(uret), .blt(blt), .U_type(U_type), .lhu(lhu));  // open: csrrsi, csrrci
  Multiplexer #(.select(1), .width(5), .disabled("Z"), .enable("false")) multiplexer_6 (
    .in0(IR[24:20]), .in1(5'b01010), .out(multiplexer_6_out), .sel(ecall));
  assign bit_extender_1_out = {{20{IR[31]}}, IR[31:20]};  // Bit_Extender bit_extender_1
  assign bit_extender_2_out = {{20{IR[31]}}, {IR[31:25], IR[11:7]}};  // Bit_Extender bit_extender_2
  assign bit_extender_3_out = {{12{IR[31]}}, IR[31:12]};  // Bit_Extender bit_extender_3
  assign bit_extender_4_out = {{20{IR[31]}}, {IR[31], IR[7], IR[30:25], IR[11:8]}};  // Bit_Extender bit_extender_4
  assign bit_extender_5_out = {{12{IR[31]}}, {IR[31], IR[19:12], IR[20], IR[30:21]}};  // Bit_Extender bit_extender_5
  Comparator #(.width(13), .mode("twosComplement")) comparator_6 (
    .a(CNT_num), .b(13'hc), .eq(comparator_6_eq), .lt(comparator_6_lt));  // open: gt
  Clock #(.highDuration(1), .lowDuration(1)) clock_1 (.out(clock_1_out));
  Multiplexer #(.select(1), .width(32), .disabled("Z"), .enable("false")) multiplexer_7 (
    .in0(bit_extender_1_out), .in1(bit_extender_2_out), .out(multiplexer_7_out), .sel(S_Type));
  Shifter #(.width(32), .shift("ll")) shifter_1 (.in(bit_extender_3_out), .\dist (5'b01100), .out(shifter_1_out));
  Counter #(.width(13), .max('h1fff), .ongoal("stay"), .trigger("rising"), .behavior("old")) counter_1 (
    .count(comparator_6_lt), .Q(CNT_num), .clk(clock_1_out));  // open: load, D, carry, clr, preset
  Regifile regifile_1 (
    .Din(RDin), .Clk(CLK), .R1(R1), .R2(MDin), .WE(RegWrite), .W_num(IR[11:7]), .R1_num(multiplexer_5_out),
    .R2_num(multiplexer_6_out));
  Shifter #(.width(32), .shift("ll")) shifter_2 (.in(bit_extender_4_out), .\dist (5'b00001), .out(shifter_2_out));
  Shifter #(.width(32), .shift("ll")) shifter_3 (.in(bit_extender_5_out), .\dist (5'b00001), .out(shifter_3_out));
  nand nand_1 (nand_1_out, d_ff_5_q, comparator_6_eq);
  Multiplexer #(.select(1), .width(32), .disabled("Z"), .enable("false")) multiplexer_8 (
    .in0(MDin), .in1(multiplexer_7_out), .out(multiplexer_8_out), .sel(AluSrcB));
  Multiplexer #(.select(1), .width(32), .disabled("Z"), .enable("false")) multiplexer_9 (
    .in0(result), .in1(adder_2_out), .out(multiplexer_9_out), .sel(U_type));
  Adder #(.width(32)) adder_2 (.a(shifter_1_out), .b(PC), .out(adder_2_out));  // open: cin, cout
  Adder #(.width(32)) adder_3 (.a(shifter_2_out), .b(PC), .out(b_t));  // open: cin, cout
  Adder #(.width(32)) adder_4 (.a(shifter_3_out), .b(PC), .out(jal_t));  // open: cin, cout
  assign jalr_t = aluresult & 32'hfffffffe;  // AND_Gate and_7, 32 bits wide
  assign CLK = nand_1_out ? clock_1_out : 1'bz;  // Controlled_Buffer controlled_buffer_1
  Pull_Resistor #(.pull(1)) pull_resistor_4 (.node(CLK));
  ALU alu_1 (
    .X(R1), .Y(multiplexer_8_out), .AluOP(AluOP), .Equal(equal), .Result(aluresult), .out_6(less));  // open: Result_2, out_4
  Multiplexer #(.select(1), .width(32), .disabled("Z"), .enable("false")) multiplexer_10 (
    .in0(multiplexer_9_out), .in1(PC_4), .out(multiplexer_10_out), .sel(J));
  not not_3 (not_3_out, halt);
  Multiplexer #(.select(1), .width(16), .disabled("Z"), .enable("false")) multiplexer_11 (
    .in0(MDout[15:0]), .in1(MDout[31:16]), .out(multiplexer_11_out), .sel(aluresult[1]));
  not not_4 (not_4_out, equal);
  or or_15 (or_15_out, Go, not_3_out);
  Counter #(.width(16), .max('hffff), .ongoal("wrap"), .trigger("rising"), .behavior("new")) counter_2 (
    .count(or_15_out), .Q(\总周期数 ), .clk(CLK));  // open: load, D, carry, clr, preset, down
  not not_5 (not_5_out, MemWrite);
  Multiplexer #(.select(1), .width(32), .disabled("Z"), .enable("false")) multiplexer_12 (
    .in0(multiplexer_10_out), .in1(bit_extender_6_out), .out(RDin), .sel(lhu));
  assign bit_extender_6_out = {{16{1'b0}}, multiplexer_11_out};  // Bit_Extender bit_extender_6
  and and_8 (and_8_out, blt, less);
  and and_9 (and_9_out, Bne, not_4_out);
  and and_10 (and_10_out, Beq, equal);
  RAM #(.addrWidth(10), .dataWidth(32), .bus("separate"), .Select("high")) ram_1 (
    .addr(aluresult[11:2]), .din(MDin), .data(MDout), .str(MemWrite), .clk(CLK), .ld(not_5_out));  // open: sel, clr
  Multiplexer #(.select(1), .width(32), .disabled("Z"), .enable("false")) multiplexer_13 (
    .in0(aluresult), .in1(MDout), .out(result), .sel(MemToReg));
  or or_16 (B, and_8_out, or_17_out);
  or or_17 (or_17_out, and_9_out, and_10_out);

  // Other names for the same wires on the sheet: R2[31:0] = MDin

  // Notes on the sheet:
  //   中断源
  //   中断等待指示
  //   总复位信号应将除ROM以外所有存储组件全部清零
  //   单级中断测试信号模拟器
  //   识别中断类型找地址
  //   数码管输出
  //   数码管输出应该用寄存器锁存，否则显示数据只能一闪而过
  //   Reset 
  //   Reset 
  //   Reset 
  //   中断响应阶段
  //   清除中断
  //   保存断点
  //   中断响应
  //   中断使能位(用于开关中断)
  //   判断中断使能
  //   为方便自动评测，需要输出PC，IR，寄存器堆写如数据RDin
  //   RAM写使能MemWrite、RAM写入数据MDin等信号
  //   指令探针
  //   指令存储器
  //   指令字
  //   contents of rom_1 (hex, n*v repeats v):
  //   7d000113 100413 1f41993 41f9d993 433 c00913 800b13 140413 f47413 800293 100313 499993 89e9b3 1300533
  //   2200893 73 406282b3 fe0294e3 140413 f00f93 1f47433 1c41413 800293 100313 49d993 89e9b3 1300533
  //   2200893 73 406282b3 fe0294e3 1c45413 406b0b33 b0463 f95ff06f 2b3 fff2c293 1029293 fff2e293 500533
  //   2200893 73 f5dff06f 1112023 410113 a12023 410113 812023 410113 1312023 410113 1412023 410113 1512023
  //   410113 1612023 410113 100b13 300a13 100a93 1600433 441413 14469b3 1300533 2200893 73 fe0416e3
  //   415a0a33 fe0a10e3 ffc10113 12b03 ffc10113 12a83 ffc10113 12a03 ffc10113 12983 ffc10113 12403
  //   ffc10113 12503 ffc10113 12883 200073 1112023 410113 a12023 410113 812023 410113 1312023 410113
  //   1412023 410113 1512023 410113 1612023 410113 200b13 300a13 100a93 1600433 441413 14469b3 1300533
  //   2200893 73 fe0416e3 415a0a33 fe0a10e3 ffc10113 12b03 ffc10113 12a83 ffc10113 12a03 ffc10113 12983
  //   ffc10113 12403 ffc10113 12503 ffc10113 12883 200073 1112023 410113 a12023 410113 812023 410113
  //   1312023 410113 1412023 410113 1512023 410113 1612023 410113 300b13 300a13 100a93 1600433 441413
  //   14469b3 1300533 2200893 73 fe0416e3 415a0a33 fe0a10e3 ffc10113 12b03 ffc10113 12a83 ffc10113 12a03
  //   ffc10113 12983 ffc10113 12403 ffc10113 12503 ffc10113 12883 200073
  //   JAL
  //   JALR
  //   URET
  //   I型
  //   S型
  //   U型
  //   B型Imm
  //   J型Imm
  //   控制位
  //   暂停节拍，不能为0
  //   Beq
  //   Bne
  //   MemToReg
  //   MemWrite
  //   AluOP
  //   AluSrcB
  //   RegWrite
  //   S_Type
  //   戳工具置1进入计数暂停模式，ctrl+k时钟自动运行到对应节拍暂停
  //   ctrl+k关闭时钟连续运行，将控制位置零，进入单步调试模式调试
  //   auipc
  //   beq/bne/blt
  //   jal
  //   jalr
  //   可计数暂停的时钟源
  //   数据存储器
endmodule

module \单周期_多级中断  (
  input  IR1,
  input  IR2,
  input  IR3,
  output RegWrite,
  output MemWrite,
  output [31:0] PC,
  output [31:0] IR,
  output [31:0] RDin,
  output [31:0] MDin,
  output [31:0] LedData
);

  wire AluSrcB, and_1_out, and_2_out, and_3_out, and_4_out, and_7_out, and_8_out, and_9_out, B, Beq, blt,
       Bne, CLK, clock_1_out, CLR1, CLR2, CLR3, comparator_1_eq, comparator_2_eq, comparator_3_eq,
       comparator_4_eq, comparator_5_eq, comparator_6_lt, comparator_7_eq, comparator_7_lt, comparator_8_eq,
       CSR, CSRRCI, CSRRSI, d_ff_1_q, d_ff_2_q, d_ff_3_q, d_ff_4_q, d_ff_6_q, ecall, en, equal, Go, halt, IE,
       INTR, INTR1, INTR2, INTR3, IR1_t, IR2_t, IR3_t, IRA, IRB, IRC, J, JAL, JALR, less, lhu, MemToReg,
       nand_1_out, not_1_out, not_2_out, not_3_out, not_4_out, not_5_out, not_6_out, or_4_out, or_5_out,
       or_6_out, or_7_out, or_8_out, or_9_out, or_12_out, or_13_out, or_16_out, or_17_out, or_19_out,
       or_21_out, S_Type, U_type, uret, W1, W2, W3;
  wire [1:0] CUR_INTR, multiplexer_3_out, multiplexer_5_out, multiplexer_8_out, priority_encoder_1_out,
       priority_encoder_2_out, priority_encoder_3_out, priority_encoder_4_out, priority_encoder_5_out,
       register_3_q, register_5_q;
  wire [3:0] AluOP;
  wire [4:0] multiplexer_10_out, multiplexer_11_out;
  wire [12:0] CNT_num;
  wire [15:0] multiplexer_16_out, \总周期数 ;
  wire [31:0] adder_2_out, aluresult, b_t, bit_extender_1_out, bit_extender_2_out, bit_extender_3_out,
       bit_extender_4_out, bit_extender_5_out, bit_extender_6_out, IR_PC, jal_t, jalr_t, MDout, MEPC,
       multiplexer_2_out, multiplexer_4_out, multiplexer_6_out, multiplexer_7_out, multiplexer_9_out,
       multiplexer_12_out, multiplexer_13_out, multiplexer_14_out, multiplexer_15_out, multiplexer_19_out,
       PC_4, R1, register_4_q, register_6_q, result, shifter_1_out, shifter_2_out, shifter_3_out;

  Button \u_继续运行  (.out(Go));
  Button _1 (.out(IRA));
  Button _2 (.out(IRB));
  Button _3 (.out(IRC));
  LED #(.active("true")) led_1 (.in(W1));
  LED #(.active("true")) led_2 (.in(W2));
  LED #(.active("true")) led_3 (.in(W3));
  Hex_Digit_Display hex_digit_display_1 (.value(LedData[31:28]));  // open: dp
  Comparator #(.width(16), .mode("twosComplement")) comparator_1 (
    .a(16'h258), .b(\总周期数 ), .eq(comparator_1_eq));  // open: gt, lt
  Comparator #(.width(16), .mode("twosComplement")) comparator_2 (
    .a(\总周期数 ), .b(16'h1), .eq(comparator_2_eq));  // open: gt, lt
  Comparator #(.width(16), .mode("twosComplement")) comparator_3 (
    .a(\总周期数 ), .b(16'h4), .eq(comparator_3_eq));  // open: gt, lt
  Comparator #(.width(16), .mode("twosComplement")) comparator_4 (
    .a(\总周期数 ), .b(16'h7), .eq(comparator_4_eq));  // open: gt, lt
  Comparator #(.width(16), .mode("twosComplement")) comparator_5 (
    .a(\总周期数 ), .b(16'h241), .eq(comparator_5_eq));  // open: gt, lt
  D_Flip_Flop #(.trigger("rising"), .Pre_Clr_Positions("LEGACY"), .NegatePresetClear("false"), .enable("true"), .NewFFLayout("false")) d_ff_1 (
    .clk(IRA), .D(1'b1), .Q(d_ff_1_q), .reset(INTR1));  // open: Qn, preset, en
  or or_1 (W1, INTR1, d_ff_1_q);
  D_Flip_Flop #(.trigger("rising"), .Pre_Clr_Positions("LEGACY"), .NegatePresetClear("false"), .enable("true"), .NewFFLayout("false")) d_ff_2 (
    .clk(IRB), .D(1'b1), .Q(d_ff_2_q), .reset(INTR2));  // open: Qn, preset, en
  or or_2 (W2, INTR2, d_ff_2_q);
  D_Flip_Flop #(.trigger("rising"), .Pre_Clr_Positions("LEGACY"), .NegatePresetClear("false"), .enable("true"), .NewFFLayout("false")) d_ff_3 (
    .clk(IRC), .D(1'b1), .Q(d_ff_3_q), .reset(INTR3));  // open: Qn, preset, en
  or or_3 (W3, INTR3, d_ff_3_q);
  Demultiplexer #(.select(2), .width(1), .tristate("false"), .disabled("Z"), .enable("false")) demultiplexer_1 (
    .out1(CLR1), .out2(CLR2), .out3(CLR3), .in(uret), .sel(CUR_INTR));  // open: out0
  Hex_Digit_Display hex_digit_display_2 (.value(LedData[27:24]));  // open: dp
  Hex_Digit_Display hex_digit_display_3 (.value(LedData[23:20]));  // open: dp
  or or_4 (or_4_out, comparator_1_eq, comparator_2_eq);
  assign IRA = or_4_out ? ~CLK : 1'bz;  // Controlled_Inverter controlled_inverter_1
  assign IRB = comparator_3_eq ? ~CLK : 1'bz;  // Controlled_Inverter controlled_inverter_2
  or or_5 (or_5_out, comparator_4_eq, comparator_5_eq);
  assign IRC = or_5_out ? ~CLK : 1'bz;  // Controlled_Inverter controlled_inverter_3
  or or_6 (or_6_out, d_ff_1_q, INTR1);
  or or_7 (or_7_out, d_ff_2_q, INTR2);
  Multiplexer #(.select(2), .width(32), .disabled("Z"), .enable("false")) multiplexer_1 (
    .in1(32'h30ac), .in2(32'h3158), .in3(32'h3204), .out(IR_PC), .sel(priority_encoder_1_out));  // open: in0
  Priority_Encoder #(.select(2), .disabled("Z")) priority_encoder_1 (
    .in0(1'b1), .in1(INTR1), .in2(INTR2), .in3(INTR3), .out(priority_encoder_1_out));  // open: gs, en_out, en_in
  Hex_Digit_Display hex_digit_display_4 (.value(LedData[15:12]));  // open: dp
  Hex_Digit_Display hex_digit_display_5 (.value(LedData[19:16]));  // open: dp
  Pull_Resistor #(.pull(0)) pull_resistor_1 (.node(IRA));
  Pull_Resistor #(.pull(0)) pull_resistor_2 (.node(IRB));
  Pull_Resistor #(.pull(0)) pull_resistor_3 (.node(IRC));
  and and_1 (and_1_out, or_6_out, ~CLR1);  // AND_Gate
  and and_2 (and_2_out, or_7_out, ~CLR2);  // AND_Gate
  or or_8 (or_8_out, d_ff_3_q, INTR3);
  and and_3 (and_3_out, or_8_out, ~CLR3);  // AND_Gate
  Hex_Digit_Display hex_digit_display_6 (.value(LedData[11:8]));  // open: dp
  Hex_Digit_Display hex_digit_display_7 (.value(LedData[7:4]));  // open: dp
  // Probe on \总周期数 
  D_Flip_Flop #(.trigger("rising"), .Pre_Clr_Positions("LEGACY"), .NegatePresetClear("false"), .enable("true"), .NewFFLayout("false")) u_IR1 (
    .clk(CLK), .D(and_1_out), .Q(INTR1));  // open: Qn, preset, en, reset
  D_Flip_Flop #(.trigger("rising"), .Pre_Clr_Positions("LEGACY"), .NegatePresetClear("false"), .enable("true"), .NewFFLayout("false")) IR1_2 (
    .clk(CLK), .D(and_2_out), .Q(INTR2));  // open: Qn, preset, en, reset
  D_Flip_Flop #(.trigger("rising"), .Pre_Clr_Positions("LEGACY"), .NegatePresetClear("false"), .enable("true"), .NewFFLayout("false")) IR1_3 (
    .clk(CLK), .D(and_3_out), .Q(INTR3));  // open: Qn, preset, en, reset
  Hex_Digit_Display hex_digit_display_8 (.value(LedData[3:0]));  // open: dp
  Priority_Encoder #(.select(2), .disabled("Z")) priority_encoder_2 (
    .in0(1'b1), .in1(INTR1), .in2(INTR2), .in3(INTR3), .out(priority_encoder_2_out));  // open: gs, en_out, en_in
  or or_9 (or_9_out, INTR1, INTR2, INTR3);
  or or_10 (IR1_t, IR1, IRA);
  D_Flip_Flop #(.trigger("rising"), .Pre_Clr_Positions("LEGACY"), .NegatePresetClear("false"), .enable("true"), .NewFFLayout("false")) d_ff_4 (
    .clk(CLK), .D(CSRRSI), .Q(d_ff_4_q), .en(CSR));  // open: Qn, preset, reset
  and and_4 (and_4_out, d_ff_4_q, not_1_out);
  not not_1 (not_1_out, CSRRCI);
  Priority_Encoder #(.select(2), .disabled("Z")) priority_encoder_3 (
    .in0(1'b1), .in1(INTR1), .in2(INTR2), .in3(INTR3), .out(priority_encoder_3_out));  // open: gs, en_out, en_in
  or or_11 (IR2_t, IR2, IRB);
  Comparator #(.width(2), .mode("unsigned")) comparator_6 (
    .a(CUR_INTR), .b(priority_encoder_2_out), .lt(comparator_6_lt));  // open: gt, eq
  or or_12 (or_12_out, ~or_9_out, uret, CSRRSI, and_4_out);  // OR_Gate
  and and_5 (INTR, comparator_6_lt, IE);
  D_Flip_Flop #(.trigger("rising"), .Pre_Clr_Positions("LEGACY"), .NegatePresetClear("false"), .enable("true"), .NewFFLayout("true")) d_ff_5 (
    .clk(CLK), .D(or_12_out), .Q(IE));  // open: Qn, preset, en, reset
  Priority_Encoder #(.select(2), .disabled("Z")) priority_encoder_4 (
    .in0(1'b1), .in1(B), .in2(JAL), .in3(JALR), .out(priority_encoder_4_out));  // open: gs, en_out, en_in
  Multiplexer #(.select(2), .width(32), .disabled("Z"), .enable("false")) multiplexer_2 (
    .in0(PC_4), .in1(b_t), .in2(jal_t), .in3(jalr_t), .out(multiplexer_2_out), .sel(priority_encoder_4_out));
  Multiplexer #(.select(1), .width(2), .disabled("Z"), .enable("false")) multiplexer_3 (
    .in0(priority_encoder_3_out), .in1(register_3_q), .out(multiplexer_3_out), .sel(uret));
  or or_13 (or_13_out, uret, INTR);
  or or_14 (IR3_t, IR3, IRC);
  or or_15 (CSR, CSRRCI, CSRRSI);
  Multiplexer #(.select(1), .width(32), .disabled("Z"), .enable("false")) multiplexer_4 (
    .in0(multiplexer_2_out), .in1(register_4_q), .out(multiplexer_4_out), .sel(uret));
  Register #(.width(2), .trigger("rising"), .Select("low")) register_1 (
    .D(multiplexer_3_out), .en(or_13_out), .Q(CUR_INTR), .clk(CLK));  // open: clr
  or or_16 (or_16_out, uret, INTR);
  Multiplexer #(.select(1), .width(2), .disabled("Z"), .enable("false")) multiplexer_5 (
    .in0(CUR_INTR), .in1(register_5_q), .out(multiplexer_5_out), .sel(uret));
  Priority_Encoder #(.select(2), .disabled("Z")) priority_encoder_5 (
    .in0(1'b1), .in1(INTR), .in2(uret), .out(priority_encoder_5_out));  // open: in3, gs, en_out, en_in
  Multiplexer #(.select(2), .width(32), .disabled("Z"), .enable("false")) multiplexer_6 (
    .in0(multiplexer_2_out), .in1(IR_PC), .in2(MEPC), .out(multiplexer_6_out), .sel(priority_encoder_5_out));  // open: in3
  Register #(.width(32), .trigger("rising"), .Select("low")) register_2 (
    .D(multiplexer_4_out), .en(or_16_out), .Q(MEPC), .clk(CLK));  // open: clr
  Multiplexer #(.select(1), .width(32), .disabled("Z"), .enable("false")) multiplexer_7 (
    .in0(MEPC), .in1(register_6_q), .out(multiplexer_7_out), .sel(uret));
  Register #(.width(2), .trigger("rising"), .Select("low")) register_3 (
    .D(multiplexer_5_out), .en(or_13_out), .Q(register_3_q), .clk(CLK));  // open: clr
  or or_17 (or_17_out, Go, not_2_out);
  Register #(.width(32), .trigger("rising"), .Select("low")) register_4 (
    .D(multiplexer_7_out), .en(or_16_out), .Q(register_4_q), .clk(CLK));  // open: clr
  Multiplexer #(.select(1), .width(2), .disabled("Z"), .enable("false")) multiplexer_8 (
    .in0(register_3_q), .in1(2'b00), .out(multiplexer_8_out), .sel(uret));
  Register #(.width(32), .trigger("rising"), .Select("low")) u_PC (
    .D(multiplexer_6_out), .en(or_17_out), .Q(PC), .clk(CLK));  // open: clr
  not not_2 (not_2_out, halt);
  Register #(.width(2), .trigger("rising"), .Select("low")) register_5 (
    .D(multiplexer_8_out), .en(or_13_out), .Q(register_5_q), .clk(CLK));  // open: clr
  Adder #(.width(32)) adder_1 (.a(PC), .b(32'h4), .out(PC_4));  // open: cin, cout
  Multiplexer #(.select(1), .width(32), .disabled("Z"), .enable("false")) multiplexer_9 (
    .in0(register_4_q), .in1({32{1'b0}}), .out(multiplexer_9_out), .sel(uret));
  Register #(.width(32), .trigger("rising"), .Select("low")) register_6 (
    .D(multiplexer_9_out), .en(or_16_out), .Q(register_6_q), .clk(CLK));  // open: clr
  // RiscV_Probe riscv_probe_1: pin names not known; wires that end beside it: IR
  D_Flip_Flop #(.trigger("high"), .Pre_Clr_Positions("LEGACY"), .NegatePresetClear("false"), .enable("true"), .NewFFLayout("false")) d_ff_6 (.Q(d_ff_6_q));  // open: clk, D, Qn, preset, en, reset
  // Probe on 13'hc
  or or_18 (J, JALR, JAL);
  ROM #(.addrWidth(10), .dataWidth(32), .Select("high")) rom_1 (.addr(PC[11:2]), .data(IR));
  Comparator #(.width(13), .mode("twosComplement")) comparator_7 (
    .a(CNT_num), .b(13'hc), .eq(comparator_7_eq), .lt(comparator_7_lt));  // open: gt
  Clock #(.highDuration(1), .lowDuration(1)) clock_1 (.out(clock_1_out));
  Multiplexer #(.select(1), .width(5), .disabled("Z"), .enable("false")) multiplexer_10 (
    .in0(IR[19:15]), .in1(5'b10001), .out(multiplexer_10_out), .sel(ecall));
  Counter #(.width(13), .max('h1fff), .ongoal("stay"), .trigger("rising"), .behavior("old")) counter_1 (
    .count(comparator_7_lt), .Q(CNT_num), .clk(clock_1_out));  // open: load, D, carry, clr, preset
  \单周期硬布线控制器  \u_单周期硬布线控制器_1  (
    .Funct({IR[30], IR[25], IR[14:12]}), .OP(IR[6:2]), .ALU_OP(AluOP), .MemToReg(MemToReg),
    .MemWrite(MemWrite), .ALU_SRC(AluSrcB), .RegWrite(RegWrite), .ecall(ecall), .S_type(S_Type), .Jalr(JALR),
    .Beq(Beq), .JAL(JAL), .Bne(Bne), .in_3(IR[21]), .uret(uret), .blt(blt), .U_type(U_type), .lhu(lhu),
    .csrrsi(CSRRSI), .csrrci(CSRRCI));
  Multiplexer #(.select(1), .width(5), .disabled("Z"), .enable("false")) multiplexer_11 (
    .in0(IR[24:20]), .in1(5'b01010), .out(multiplexer_11_out), .sel(ecall));
  assign bit_extender_1_out = {{20{IR[31]}}, IR[31:20]};  // Bit_Extender bit_extender_1
  assign bit_extender_2_out = {{20{IR[31]}}, {IR[31:25], IR[11:7]}};  // Bit_Extender bit_extender_2
  assign bit_extender_3_out = {{12{IR[31]}}, IR[31:12]};  // Bit_Extender bit_extender_3
  assign bit_extender_4_out = {{20{IR[31]}}, {IR[31], IR[7], IR[30:25], IR[11:8]}};  // Bit_Extender bit_extender_4
  assign bit_extender_5_out = {{12{IR[31]}}, {IR[31], IR[19:12], IR[20], IR[30:21]}};  // Bit_Extender bit_extender_5
  nand nand_1 (nand_1_out, d_ff_6_q, comparator_7_eq);
  Multiplexer #(.select(1), .width(32), .disabled("Z"), .enable("false")) multiplexer_12 (
    .in0(bit_extender_1_out), .in1(bit_extender_2_out), .out(multiplexer_12_out), .sel(S_Type));
  Shifter #(.width(32), .shift("ll")) shifter_1 (.in(bit_extender_3_out), .\dist (5'b01100), .out(shifter_1_out));
  assign CLK = nand_1_out ? clock_1_out : 1'bz;  // Controlled_Buffer controlled_buffer_1
  Pull_Resistor #(.pull(1)) pull_resistor_4 (.node(CLK));
  Regifile regifile_1 (
    .Din(RDin), .Clk(CLK), .R1(R1), .R2(MDin), .WE(RegWrite), .W_num(IR[11:7]), .R1_num(multiplexer_10_out),
    .R2_num(multiplexer_11_out));
  Shifter #(.width(32), .shift("ll")) shifter_2 (.in(bit_extender_4_out), .\dist (5'b00001), .out(shifter_2_out));
  Shifter #(.width(32), .shift("ll")) shifter_3 (.in(bit_extender_5_out), .\dist (5'b00001), .out(shifter_3_out));
  Multiplexer #(.select(1), .width(32), .disabled("Z"), .enable("false")) multiplexer_13 (
    .in0(MDin), .in1(multiplexer_12_out), .out(multiplexer_13_out), .sel(AluSrcB));
  Multiplexer #(.select(1), .width(32), .disabled("Z"), .enable("false")) multiplexer_14 (
    .in0(result), .in1(adder_2_out), .out(multiplexer_14_out), .sel(U_type));
  Adder #(.width(32)) adder_2 (.a(shifter_1_out), .b(PC), .out(adder_2_out));  // open: cin, cout
  Adder #(.width(32)) adder_3 (.a(shifter_2_out), .b(PC), .out(b_t));  // open: cin, cout
  Adder #(.width(32)) adder_4 (.a(shifter_3_out), .b(PC), .out(jal_t));  // open: cin, cout
  assign jalr_t = aluresult & 32'hfffffffe;  // AND_Gate and_6, 32 bits wide
  ALU alu_1 (
    .X(R1), .Y(multiplexer_13_out), .AluOP(AluOP), .Equal(equal), .Result(aluresult), .out_6(less));  // open: Result_2, out_4
  Multiplexer #(.select(1), .width(32), .disabled("Z"), .enable("false")) multiplexer_15 (
    .in0(multiplexer_14_out), .in1(PC_4), .out(multiplexer_15_out), .sel(J));
  not not_3 (not_3_out, halt);
  Multiplexer #(.select(1), .width(16), .disabled("Z"), .enable("false")) multiplexer_16 (
    .in0(MDout[15:0]), .in1(MDout[31:16]), .out(multiplexer_16_out), .sel(aluresult[1]));
  not not_4 (not_4_out, equal);
  or or_19 (or_19_out, Go, not_3_out);
  Counter #(.width(16), .max('hffff), .ongoal("wrap"), .trigger("rising"), .behavior("new")) counter_2 (
    .count(or_19_out), .Q(\总周期数 ), .clk(CLK));  // open: load, D, carry, clr, preset, down
  not not_5 (not_5_out, MemWrite);
  Multiplexer #(.select(1), .width(32), .disabled("Z"), .enable("false")) multiplexer_17 (
    .in0(multiplexer_15_out), .in1(bit_extender_6_out), .out(RDin), .sel(lhu));
  assign bit_extender_6_out = {{16{1'b0}}, multiplexer_16_out};  // Bit_Extender bit_extender_6
  and and_7 (and_7_out, blt, less);
  and and_8 (and_8_out, Bne, not_4_out);
  and and_9 (and_9_out, Beq, equal);
  RAM #(.addrWidth(10), .dataWidth(32), .bus("separate"), .Select("high")) ram_1 (
    .addr(aluresult[11:2]), .din(MDin), .data(MDout), .str(MemWrite), .clk(CLK), .ld(not_5_out));  // open: sel, clr
  Multiplexer #(.select(1), .width(32), .disabled("Z"), .enable("false")) multiplexer_18 (
    .in0(aluresult), .in1(MDout), .out(result), .sel(MemToReg));
  or or_20 (B, and_7_out, or_21_out);
  or or_21 (or_21_out, and_8_out, and_9_out);
  Multiplexer #(.select(1), .width(32), .disabled("Z"), .enable("false")) multiplexer_19 (
    .in0({32{1'b0}}), .in1(MDin), .out(multiplexer_19_out), .sel(en));
  Comparator #(.width(32), .mode("twosComplement")) comparator_8 (
    .a(R1), .b(32'h22), .eq(comparator_8_eq));  // open: gt, lt
  not not_6 (not_6_out, comparator_8_eq);
  and and_10 (halt, not_6_out, ecall);
  and and_11 (en, ecall, comparator_8_eq);
  Register #(.width(32), .trigger("rising"), .Select("low")) register_7 (
    .D(multiplexer_19_out), .en(en), .Q(LedData), .clk(CLK));  // open: clr

  // Other names for the same wires on the sheet: R2[31:0] = MDin

  // Notes on the sheet:
  //   中断源
  //   中断等待指示
  //   总复位信号应将除ROM以外所有存储组件全部清零
  //   多级中断测试信号模拟器
  //   清除中断
  //   数码管输出
  //   识别中断类型找地址
  //   数码管输出应该用寄存器锁存，否则显示数据只能一闪而过
  //   Reset 
  //   Reset 
  //   Reset 
  //   中断响应阶段
  //   中断响应
  //   中断使能位(用于开关中断)
  //   保存中断号
  //   保存断点地址
  //   为方便自动评测，需要输出PC，IR，寄存器堆写如数据RDin
  //   RAM写使能MemWrite、RAM写入数据MDin等信号
  //   指令探针
  //   指令存储器
  //   控制位
  //   暂停节拍，不能为0
  //   指令字
  //   contents of rom_1 (hex, n*v repeats v):
  //   7d000113 100413 1f41993 41f9d993 433 c00913 800b13 140413 f47413 800293 100313 499993 89e9b3 1300533
  //   2200893 73 406282b3 fe0294e3 140413 f00f93 1f47433 1c41413 800293 100313 49d993 89e9b3 1300533
  //   2200893 73 406282b3 fe0294e3 1c45413 406b0b33 b0463 f95ff06f 2b3 fff2c293 1029293 fff2e293 500533
  //   2200893 73 f5dff06f 1112023 410113 a12023 410113 812023 410113 1312023 410113 1412023 410113 1512023
  //   410113 1612023 410113 40e073 100b13 300a13 100a93 1600433 441413 14469b3 1300533 2200893 73 fe0416e3
  //   415a0a33 fe0a10e3 40f073 ffc10113 12b03 ffc10113 12a83 ffc10113 12a03 ffc10113 12983 ffc10113 12403
  //   ffc10113 12503 ffc10113 12883 200073 1112023 410113 a12023 410113 812023 410113 1312023 410113
  //   1412023 410113 1512023 410113 1612023 410113 40e073 200b13 300a13 100a93 1600433 441413 14469b3
  //   1300533 2200893 73 fe0416e3 415a0a33 fe0a10e3 40f073 ffc10113 12b03 ffc10113 12a83 ffc10113 12a03
  //   ffc10113 12983 ffc10113 12403 ffc10113 12503 ffc10113 12883 200073 1112023 410113 a12023 410113
  //   812023 410113 1312023 410113 1412023 410113 1512023 410113 1612023 410113 40e073 300b13 300a13
  //   100a93 1600433 441413 14469b3 1300533 2200893 73 fe0416e3 415a0a33 fe0a10e3 40f073 ffc10113 12b03
  //   ffc10113 12a83 ffc10113 12a03 ffc10113 12983 ffc10113 12403 ffc10113 12503 ffc10113 12883 200073
  //   戳工具置1进入计数暂停模式，ctrl+k时钟自动运行到对应节拍暂停
  //   ctrl+k关闭时钟连续运行，将控制位置零，进入单步调试模式调试
  //   JAL
  //   JALR
  //   URET
  //   I型
  //   S型
  //   U型
  //   B型Imm
  //   J型Imm
  //   Beq
  //   Bne
  //   MemToReg
  //   MemWrite
  //   AluOP
  //   AluSrcB
  //   RegWrite
  //   S_Type
  //   可计数暂停的时钟源
  //   auipc
  //   beq/bne/blt
  //   jal
  //   jalr
  //   数据存储器
endmodule

module \封装正确性测试  (
);

  wire IR1, IR2, IR3, MemW, RegW;
  wire [31:0] EX_PC, ID_PC, IF_PC, IR, LED, MDin, MDinr, MEM_PC, PC, RDin, RDinr, WB_PC;

  \单周期RISC_V  \u_单周期risc_v_1  (
    .IR1(IR1), .IR2(IR2), .IR3(IR3), .RegWrite(RegW), .MemWrite(MemW), .PC(PC), .IR(IR), .RDin(RDin),
    .MDin(MDin), .LedData(LED));
  \气泡流水线  \u_气泡流水线_1  (
    .RegWrite(RegW), .MemWrite(MemW), .IF_PC(IF_PC), .ID_PC(ID_PC), .EX_PC(EX_PC), .M_PC(MEM_PC),
    .WB_PC(WB_PC), .RDin(RDinr), .MDin(MDinr), .LedData(LED));
  \单周期_单级中断  \u_单周期_单级中断_1  (
    .IR1(IR1), .IR2(IR2), .IR3(IR3), .RegWrite(RegW), .MemWrite(MemW), .PC(PC), .IR(IR), .RDin(RDin),
    .MDin(MDin), .LedData(LED));
  \理想流水线  \u_理想流水线_1  (
    .RegWrite(RegW), .MemWrite(MemW), .IF_PC(IF_PC), .ID_PC(ID_PC), .EX_PC(EX_PC), .M_PC(MEM_PC),
    .WB_PC(WB_PC), .RDin(RDinr), .MDin(MDinr), .LedData(LED));
  \重定向流水线  \u_重定向流水线_1  (
    .RegWrite(RegW), .MemWrite(MemW), .IF_PC(IF_PC), .ID_PC(ID_PC), .EX_PC(EX_PC), .M_PC(MEM_PC),
    .WB_PC(WB_PC), .RDin(RDinr), .MDin(MDinr), .LedData(LED));
  \单周期_多级中断  \u_单周期_多级中断_1  (
    .IR1(IR1), .IR2(IR2), .IR3(IR3), .RegWrite(RegW), .MemWrite(MemW), .PC(PC), .IR(IR), .RDin(RDin),
    .MDin(MDin), .LedData(LED));

  // Notes on the sheet:
  //   单周期封装测试
  //   气泡流水封装测试
  //   单周期+单级中断封装测试
  //   请检查上面封装有无位宽不匹配，引脚标签是否和连接的标签相对应，否则无法在educoder平台上正确测试
  //   理想流水封装测试
  //   重定向流水封装测试
  //   单周期+多级中断封装测试
endmodule

module IF_ID (
  input  CLK,
  input  RST,
  input  [31:0] IR,
  input  [31:0] PC,
  input  PREDICT,
  input  FLUSH,
  input  EN,
  output [31:0] IROUT,
  output [31:0] PCOUT,
  output PREDICTOUT
);

  wire multiplexer_3_out, not_1_out;
  wire [31:0] multiplexer_1_out, multiplexer_2_out;

  Multiplexer #(.select(1), .width(32), .disabled("Z"), .enable("false")) multiplexer_1 (
    .in0(IR), .in1({32{1'b0}}), .out(multiplexer_1_out), .sel(FLUSH));
  Multiplexer #(.select(1), .width(32), .disabled("Z"), .enable("false")) multiplexer_2 (
    .in0(PC), .in1({32{1'b0}}), .out(multiplexer_2_out), .sel(FLUSH));
  Multiplexer #(.select(1), .width(1), .disabled("Z"), .enable("false")) multiplexer_3 (
    .in0(PREDICT), .in1(1'b0), .out(multiplexer_3_out), .sel(FLUSH));
  Register #(.width(32), .trigger("rising"), .Select("low")) register_1 (
    .D(multiplexer_1_out), .en(not_1_out), .Q(IROUT), .clk(CLK), .clr(RST));
  Register #(.width(32), .trigger("rising"), .Select("low")) register_2 (
    .D(multiplexer_2_out), .en(not_1_out), .Q(PCOUT), .clk(CLK), .clr(RST));
  Register #(.width(1), .trigger("rising"), .Select("low")) register_3 (
    .D(multiplexer_3_out), .en(not_1_out), .Q(PREDICTOUT), .clk(CLK));  // open: clr
  not not_1 (not_1_out, EN);
endmodule

module ID_EX (
  input  CLK,
  input  RST,
  input  JAL,
  input  JALR,
  input  URET,
  input  beq,
  input  BNE,
  input  MEMTOREG,
  input  MEMWRITE,
  input  [3:0] ALUOP,
  input  ALUSRC,
  input  REGWRITE,
  input  U_type,
  input  BLT,
  input  ECALL,
  input  lhu,
  input  [1:0] R1F,
  input  [31:0] R1,
  input  [31:0] R2,
  input  [1:0] R2F,
  input  [4:0] WRITEREG,
  input  [31:0] PC,
  input  [31:0] IR,
  input  [31:0] IMM1,
  input  [31:0] IMM2,
  input  [31:0] IMM3,
  input  [31:0] IMM4,
  input  PREDICT,
  input  EN,
  input  FLUSH,
  output JALOUT,
  output JALROUT,
  output URETOUT,
  output BEQOUT,
  output BNEOUT,
  output MEMTOREGOUT,
  output MEMWRITEOUT,
  output [3:0] ALUOPOUT,
  output ALUSRCOUT,
  output REGWRITEOUT,
  output UTYPEOUT,
  output BLTOUT,
  output ECALLOUT,
  output lhuOUT,
  output [1:0] R1FOUT,
  output [31:0] R1OUT,
  output [31:0] R2OUT_prime,
  output [1:0] R2FOUT,
  output [4:0] WRITEREGOUT_prime,
  output [31:0] PCOUT_prime,
  output [31:0] IROUT_prime,
  output [31:0] IMM1OUT_prime,
  output [31:0] IMM2OUT_prime,
  output [31:0] IMM3OUT_prime,
  output [31:0] IMM4OUT_prime,
  output PREDICTOUT
);

  wire multiplexer_1_out, multiplexer_2_out, multiplexer_3_out, multiplexer_4_out, multiplexer_5_out,
       multiplexer_6_out, multiplexer_7_out, multiplexer_9_out, multiplexer_10_out, multiplexer_11_out,
       multiplexer_12_out, multiplexer_13_out, multiplexer_14_out, multiplexer_26_out, not_1_out;
  wire [1:0] multiplexer_15_out, multiplexer_18_out;
  wire [3:0] multiplexer_8_out;
  wire [4:0] multiplexer_19_out;
  wire [31:0] multiplexer_16_out, multiplexer_17_out, multiplexer_20_out, multiplexer_21_out,
       multiplexer_22_out, multiplexer_23_out, multiplexer_24_out, multiplexer_25_out;

  Multiplexer #(.select(1), .width(1), .disabled("Z"), .enable("false")) multiplexer_1 (
    .in0(JAL), .in1(1'b0), .out(multiplexer_1_out), .sel(FLUSH));
  Multiplexer #(.select(1), .width(1), .disabled("Z"), .enable("false")) multiplexer_2 (
    .in0(JALR), .in1(1'b0), .out(multiplexer_2_out), .sel(FLUSH));
  Multiplexer #(.select(1), .width(1), .disabled("Z"), .enable("false")) multiplexer_3 (
    .in0(URET), .in1(1'b0), .out(multiplexer_3_out), .sel(FLUSH));
  Multiplexer #(.select(1), .width(1), .disabled("Z"), .enable("false")) multiplexer_4 (
    .in0(beq), .in1(1'b0), .out(multiplexer_4_out), .sel(FLUSH));
  Multiplexer #(.select(1), .width(1), .disabled("Z"), .enable("false")) multiplexer_5 (
    .in0(BNE), .in1(1'b0), .out(multiplexer_5_out), .sel(FLUSH));
  Multiplexer #(.select(1), .width(1), .disabled("Z"), .enable("false")) multiplexer_6 (
    .in0(MEMTOREG), .in1(1'b0), .out(multiplexer_6_out), .sel(FLUSH));
  Multiplexer #(.select(1), .width(1), .disabled("Z"), .enable("false")) multiplexer_7 (
    .in0(MEMWRITE), .in1(1'b0), .out(multiplexer_7_out), .sel(FLUSH));
  Multiplexer #(.select(1), .width(4), .disabled("Z"), .enable("false")) multiplexer_8 (
    .in0(ALUOP), .in1(4'b0000), .out(multiplexer_8_out), .sel(FLUSH));
  Multiplexer #(.select(1), .width(1), .disabled("Z"), .enable("false")) multiplexer_9 (
    .in0(ALUSRC), .in1(1'b0), .out(multiplexer_9_out), .sel(FLUSH));
  Multiplexer #(.select(1), .width(1), .disabled("Z"), .enable("false")) multiplexer_10 (
    .in0(REGWRITE), .in1(1'b0), .out(multiplexer_10_out), .sel(FLUSH));
  Multiplexer #(.select(1), .width(1), .disabled("Z"), .enable("false")) multiplexer_11 (
    .in0(U_type), .in1(1'b0), .out(multiplexer_11_out), .sel(FLUSH));
  Multiplexer #(.select(1), .width(1), .disabled("Z"), .enable("false")) multiplexer_12 (
    .in0(BLT), .in1(1'b0), .out(multiplexer_12_out), .sel(FLUSH));
  Multiplexer #(.select(1), .width(1), .disabled("Z"), .enable("false")) multiplexer_13 (
    .in0(ECALL), .in1(1'b0), .out(multiplexer_13_out), .sel(FLUSH));
  Multiplexer #(.select(1), .width(1), .disabled("Z"), .enable("false")) multiplexer_14 (
    .in0(lhu), .in1(1'b0), .out(multiplexer_14_out), .sel(FLUSH));
  Multiplexer #(.select(1), .width(2), .disabled("Z"), .enable("false")) multiplexer_15 (
    .in0(R1F), .in1(2'b00), .out(multiplexer_15_out), .sel(FLUSH));
  Multiplexer #(.select(1), .width(32), .disabled("Z"), .enable("false")) multiplexer_16 (
    .in0(R1), .in1({32{1'b0}}), .out(multiplexer_16_out), .sel(FLUSH));
  Multiplexer #(.select(1), .width(32), .disabled("Z"), .enable("false")) multiplexer_17 (
    .in0(R2), .in1({32{1'b0}}), .out(multiplexer_17_out), .sel(FLUSH));
  Multiplexer #(.select(1), .width(2), .disabled("Z"), .enable("false")) multiplexer_18 (
    .in0(R2F), .in1(2'b00), .out(multiplexer_18_out), .sel(FLUSH));
  Multiplexer #(.select(1), .width(5), .disabled("Z"), .enable("false")) multiplexer_19 (
    .in0(WRITEREG), .in1({5{1'b0}}), .out(multiplexer_19_out), .sel(FLUSH));
  Multiplexer #(.select(1), .width(32), .disabled("Z"), .enable("false")) multiplexer_20 (
    .in0(PC), .in1({32{1'b0}}), .out(multiplexer_20_out), .sel(FLUSH));
  Multiplexer #(.select(1), .width(32), .disabled("Z"), .enable("false")) multiplexer_21 (
    .in0(IR), .in1({32{1'b0}}), .out(multiplexer_21_out), .sel(FLUSH));
  Multiplexer #(.select(1), .width(32), .disabled("Z"), .enable("false")) multiplexer_22 (
    .in0(IMM1), .in1({32{1'b0}}), .out(multiplexer_22_out), .sel(FLUSH));
  Multiplexer #(.select(1), .width(32), .disabled("Z"), .enable("false")) multiplexer_23 (
    .in0(IMM2), .in1({32{1'b0}}), .out(multiplexer_23_out), .sel(FLUSH));
  Multiplexer #(.select(1), .width(32), .disabled("Z"), .enable("false")) multiplexer_24 (
    .in0(IMM3), .in1({32{1'b0}}), .out(multiplexer_24_out), .sel(FLUSH));
  Multiplexer #(.select(1), .width(32), .disabled("Z"), .enable("false")) multiplexer_25 (
    .in0(IMM4), .in1({32{1'b0}}), .out(multiplexer_25_out), .sel(FLUSH));
  Multiplexer #(.select(1), .width(1), .disabled("Z"), .enable("false")) multiplexer_26 (
    .in0(PREDICT), .in1(1'b0), .out(multiplexer_26_out), .sel(FLUSH));
  not not_1 (not_1_out, EN);
  Register #(.width(1), .trigger("rising"), .Select("low")) register_1 (
    .D(multiplexer_1_out), .en(not_1_out), .Q(JALOUT), .clk(CLK), .clr(RST));
  Register #(.width(1), .trigger("rising"), .Select("low")) register_2 (
    .D(multiplexer_2_out), .en(not_1_out), .Q(JALROUT), .clk(CLK), .clr(RST));
  Register #(.width(1), .trigger("rising"), .Select("low")) register_3 (
    .D(multiplexer_3_out), .en(not_1_out), .Q(URETOUT), .clk(CLK), .clr(RST));
  Register #(.width(1), .trigger("rising"), .Select("low")) register_4 (
    .D(multiplexer_4_out), .en(not_1_out), .Q(BEQOUT), .clk(CLK), .clr(RST));
  Register #(.width(1), .trigger("rising"), .Select("low")) register_5 (
    .D(multiplexer_5_out), .en(not_1_out), .Q(BNEOUT), .clk(CLK), .clr(RST));
  Register #(.width(1), .trigger("rising"), .Select("low")) register_6 (
    .D(multiplexer_6_out), .en(not_1_out), .Q(MEMTOREGOUT), .clk(CLK), .clr(RST));
  Register #(.width(1), .trigger("rising"), .Select("low")) register_7 (
    .D(multiplexer_7_out), .en(not_1_out), .Q(MEMWRITEOUT), .clk(CLK), .clr(RST));
  Register #(.width(4), .trigger("rising"), .Select("low")) register_8 (
    .D(multiplexer_8_out), .en(not_1_out), .Q(ALUOPOUT), .clk(CLK), .clr(RST));
  Register #(.width(1), .trigger("rising"), .Select("low")) register_9 (
    .D(multiplexer_9_out), .en(not_1_out), .Q(ALUSRCOUT), .clk(CLK), .clr(RST));
  Register #(.width(1), .trigger("rising"), .Select("low")) register_10 (
    .D(multiplexer_10_out), .en(not_1_out), .Q(REGWRITEOUT), .clk(CLK), .clr(RST));
  Register #(.width(1), .trigger("rising"), .Select("low")) register_11 (
    .D(multiplexer_11_out), .en(not_1_out), .Q(UTYPEOUT), .clk(CLK), .clr(RST));
  Register #(.width(1), .trigger("rising"), .Select("low")) register_12 (
    .D(multiplexer_12_out), .en(not_1_out), .Q(BLTOUT), .clk(CLK), .clr(RST));
  Register #(.width(1), .trigger("rising"), .Select("low")) register_13 (
    .D(multiplexer_13_out), .en(not_1_out), .Q(ECALLOUT), .clk(CLK), .clr(RST));
  Register #(.width(1), .trigger("rising"), .Select("low")) register_14 (
    .D(multiplexer_14_out), .en(not_1_out), .Q(lhuOUT), .clk(CLK), .clr(RST));
  Register #(.width(2), .trigger("rising"), .Select("low")) register_15 (
    .D(multiplexer_15_out), .en(not_1_out), .Q(R1FOUT), .clk(CLK), .clr(RST));
  Register #(.width(32), .trigger("rising"), .Select("low")) register_16 (
    .D(multiplexer_16_out), .en(not_1_out), .Q(R1OUT), .clk(CLK), .clr(RST));
  Register #(.width(32), .trigger("rising"), .Select("low")) register_17 (
    .D(multiplexer_17_out), .en(not_1_out), .Q(R2OUT_prime), .clk(CLK), .clr(RST));
  Register #(.width(2), .trigger("rising"), .Select("low")) register_18 (
    .D(multiplexer_18_out), .en(not_1_out), .Q(R2FOUT), .clk(CLK), .clr(RST));
  Register #(.width(5), .trigger("rising"), .Select("low")) register_19 (
    .D(multiplexer_19_out), .en(not_1_out), .Q(WRITEREGOUT_prime), .clk(CLK), .clr(RST));
  Register #(.width(32), .trigger("rising"), .Select("low")) register_20 (
    .D(multiplexer_20_out), .en(not_1_out), .Q(PCOUT_prime), .clk(CLK), .clr(RST));
  Register #(.width(32), .trigger("rising"), .Select("low")) register_21 (
    .D(multiplexer_21_out), .en(not_1_out), .Q(IROUT_prime), .clk(CLK), .clr(RST));
  Register #(.width(32), .trigger("rising"), .Select("low")) register_22 (
    .D(multiplexer_22_out), .en(not_1_out), .Q(IMM1OUT_prime), .clk(CLK), .clr(RST));
  Register #(.width(32), .trigger("rising"), .Select("low")) register_23 (
    .D(multiplexer_23_out), .en(not_1_out), .Q(IMM2OUT_prime), .clk(CLK), .clr(RST));
  Register #(.width(32), .trigger("rising"), .Select("low")) register_24 (
    .D(multiplexer_24_out), .en(not_1_out), .Q(IMM3OUT_prime), .clk(CLK), .clr(RST));
  Register #(.width(32), .trigger("rising"), .Select("low")) register_25 (
    .D(multiplexer_25_out), .en(not_1_out), .Q(IMM4OUT_prime), .clk(CLK), .clr(RST));
  Register #(.width(1), .trigger("rising"), .Select("low")) register_26 (
    .D(multiplexer_26_out), .en(not_1_out), .Q(PREDICTOUT), .clk(CLK), .clr(RST));
endmodule

module EX_MEM (
  input  CLK,
  input  RST,
  input  J,
  input  MEMWRITE,
  input  MEMTOREG,
  input  REGWRITE,
  input  UTYPE,
  input  HALT,
  input  lhu,
  input  [31:0] ALURESULT,
  input  [31:0] WRITEDATA_R2,
  input  [4:0] WRITEREG,
  input  [31:0] PC,
  input  [31:0] IR,
  input  [31:0] IMM,
  input  [31:0] AUIPC_IMM,
  input  FLUSH,
  input  EN,
  output JOUT,
  output MEMWRITEOUT,
  output MEMTOREGOUT,
  output REGWRITEOUT,
  output UTYPEOUT,
  output HALTOUT,
  output lhuOUT,
  output [31:0] ALURESULTOUT,
  output [31:0] WRITEDATAOUT_R2,
  output [4:0] WRITEREGOUT,
  output [31:0] PCOUT,
  output [31:0] IROUT,
  output [31:0] IMMOUT,
  output [31:0] AUPICIMMOUT
);

  wire multiplexer_1_out, multiplexer_2_out, multiplexer_3_out, multiplexer_4_out, multiplexer_5_out,
       multiplexer_6_out, multiplexer_7_out, not_1_out;
  wire [4:0] multiplexer_10_out;
  wire [31:0] multiplexer_8_out, multiplexer_9_out, multiplexer_11_out, multiplexer_12_out,
       multiplexer_13_out, multiplexer_14_out;

  Multiplexer #(.select(1), .width(1), .disabled("Z"), .enable("false")) multiplexer_1 (
    .in0(J), .in1(1'b0), .out(multiplexer_1_out), .sel(FLUSH));
  Multiplexer #(.select(1), .width(1), .disabled("Z"), .enable("false")) multiplexer_2 (
    .in0(MEMWRITE), .in1(1'b0), .out(multiplexer_2_out), .sel(FLUSH));
  Multiplexer #(.select(1), .width(1), .disabled("Z"), .enable("false")) multiplexer_3 (
    .in0(MEMTOREG), .in1(1'b0), .out(multiplexer_3_out), .sel(FLUSH));
  Multiplexer #(.select(1), .width(1), .disabled("Z"), .enable("false")) multiplexer_4 (
    .in0(REGWRITE), .in1(1'b0), .out(multiplexer_4_out), .sel(FLUSH));
  Multiplexer #(.select(1), .width(1), .disabled("Z"), .enable("false")) multiplexer_5 (
    .in0(UTYPE), .in1(1'b0), .out(multiplexer_5_out), .sel(FLUSH));
  Multiplexer #(.select(1), .width(1), .disabled("Z"), .enable("false")) multiplexer_6 (
    .in0(HALT), .in1(1'b0), .out(multiplexer_6_out), .sel(FLUSH));
  Multiplexer #(.select(1), .width(1), .disabled("Z"), .enable("false")) multiplexer_7 (
    .in0(lhu), .in1(1'b0), .out(multiplexer_7_out), .sel(FLUSH));
  Multiplexer #(.select(1), .width(32), .disabled("Z"), .enable("false")) multiplexer_8 (
    .in0(ALURESULT), .in1({32{1'b0}}), .out(multiplexer_8_out), .sel(FLUSH));
  Multiplexer #(.select(1), .width(32), .disabled("Z"), .enable("false")) multiplexer_9 (
    .in0(WRITEDATA_R2), .in1({32{1'b0}}), .out(multiplexer_9_out), .sel(FLUSH));
  Multiplexer #(.select(1), .width(5), .disabled("Z"), .enable("false")) multiplexer_10 (
    .in0(WRITEREG), .in1({5{1'b0}}), .out(multiplexer_10_out), .sel(FLUSH));
  Multiplexer #(.select(1), .width(32), .disabled("Z"), .enable("false")) multiplexer_11 (
    .in0(PC), .in1({32{1'b0}}), .out(multiplexer_11_out), .sel(FLUSH));
  Multiplexer #(.select(1), .width(32), .disabled("Z"), .enable("false")) multiplexer_12 (
    .in0(IR), .in1({32{1'b0}}), .out(multiplexer_12_out), .sel(FLUSH));
  Multiplexer #(.select(1), .width(32), .disabled("Z"), .enable("false")) multiplexer_13 (
    .in0(IMM), .in1({32{1'b0}}), .out(multiplexer_13_out), .sel(FLUSH));
  Multiplexer #(.select(1), .width(32), .disabled("Z"), .enable("false")) multiplexer_14 (
    .in0(AUIPC_IMM), .in1({32{1'b0}}), .out(multiplexer_14_out), .sel(FLUSH));
  not not_1 (not_1_out, EN);
  Register #(.width(1), .trigger("rising"), .Select("low")) register_1 (
    .D(multiplexer_1_out), .en(not_1_out), .Q(JOUT), .clk(CLK), .clr(RST));
  Register #(.width(1), .trigger("rising"), .Select("low")) register_2 (
    .D(multiplexer_2_out), .en(not_1_out), .Q(MEMWRITEOUT), .clk(CLK), .clr(RST));
  Register #(.width(1), .trigger("rising"), .Select("low")) register_3 (
    .D(multiplexer_3_out), .en(not_1_out), .Q(MEMTOREGOUT), .clk(CLK), .clr(RST));
  Register #(.width(1), .trigger("rising"), .Select("low")) register_4 (
    .D(multiplexer_4_out), .en(not_1_out), .Q(REGWRITEOUT), .clk(CLK), .clr(RST));
  Register #(.width(1), .trigger("rising"), .Select("low")) register_5 (
    .D(multiplexer_5_out), .en(not_1_out), .Q(UTYPEOUT), .clk(CLK), .clr(RST));
  Register #(.width(1), .trigger("rising"), .Select("low")) register_6 (
    .D(multiplexer_6_out), .en(not_1_out), .Q(HALTOUT), .clk(CLK), .clr(RST));
  Register #(.width(32), .trigger("rising"), .Select("low")) register_7 (
    .D(multiplexer_8_out), .en(not_1_out), .Q(ALURESULTOUT), .clk(CLK), .clr(RST));
  Register #(.width(32), .trigger("rising"), .Select("low")) register_8 (
    .D(multiplexer_9_out), .en(not_1_out), .Q(WRITEDATAOUT_R2), .clk(CLK), .clr(RST));
  Register #(.width(5), .trigger("rising"), .Select("low")) register_9 (
    .D(multiplexer_10_out), .en(not_1_out), .Q(WRITEREGOUT), .clk(CLK), .clr(RST));
  Register #(.width(32), .trigger("rising"), .Select("low")) register_10 (
    .D(multiplexer_11_out), .en(not_1_out), .Q(PCOUT), .clk(CLK), .clr(RST));
  Register #(.width(32), .trigger("rising"), .Select("low")) register_11 (
    .D(multiplexer_12_out), .en(not_1_out), .Q(IROUT), .clk(CLK), .clr(RST));
  Register #(.width(32), .trigger("rising"), .Select("low")) register_12 (
    .D(multiplexer_13_out), .en(not_1_out), .Q(IMMOUT), .clk(CLK), .clr(RST));
  Register #(.width(32), .trigger("rising"), .Select("low")) register_13 (
    .D(multiplexer_14_out), .en(not_1_out), .Q(AUPICIMMOUT), .clk(CLK), .clr(RST));
  Register #(.width(1), .trigger("rising"), .Select("low")) register_14 (
    .D(multiplexer_7_out), .en(not_1_out), .Q(lhuOUT), .clk(CLK), .clr(RST));
endmodule

module MEM_WB (
  input  CLK,
  input  RST,
  input  J,
  input  MEMTOREG,
  input  REGWRITE,
  input  UTYPE,
  input  HALT,
  input  [31:0] ALURESULT,
  input  [31:0] MEMDATA,
  input  lhu,
  input  [4:0] WRITEREG,
  input  [31:0] PC,
  input  [31:0] IR,
  input  [31:0] IMM,
  input  [31:0] AUIPCIMM,
  input  FLUSH,
  input  EN,
  output JOUT,
  output MEMTOREGOUT,
  output REGWRITEOUT,
  output UTYPEOUT,
  output HALTOUT,
  output [31:0] ALURESULTOUT,
  output [31:0] MEMDATAOUT,
  output lhuout,
  output [4:0] WRITEREGOUT,
  output [31:0] PCOUT,
  output [31:0] IROUT,
  output [31:0] IMMOUT,
  output [31:0] AUIPCIMMOUT
);

  wire multiplexer_1_out, multiplexer_2_out, multiplexer_3_out, multiplexer_4_out, multiplexer_5_out,
       multiplexer_8_out, not_1_out;
  wire [4:0] multiplexer_9_out;
  wire [31:0] multiplexer_6_out, multiplexer_7_out, multiplexer_10_out, multiplexer_11_out,
       multiplexer_12_out, multiplexer_13_out;

  Multiplexer #(.select(1), .width(1), .disabled("Z"), .enable("false")) multiplexer_1 (
    .in0(J), .in1(1'b0), .out(multiplexer_1_out), .sel(FLUSH));
  Multiplexer #(.select(1), .width(1), .disabled("Z"), .enable("false")) multiplexer_2 (
    .in0(MEMTOREG), .in1(1'b0), .out(multiplexer_2_out), .sel(FLUSH));
  Multiplexer #(.select(1), .width(1), .disabled("Z"), .enable("false")) multiplexer_3 (
    .in0(REGWRITE), .in1(1'b0), .out(multiplexer_3_out), .sel(FLUSH));
  Multiplexer #(.select(1), .width(1), .disabled("Z"), .enable("false")) multiplexer_4 (
    .in0(UTYPE), .in1(1'b0), .out(multiplexer_4_out), .sel(FLUSH));
  Multiplexer #(.select(1), .width(1), .disabled("Z"), .enable("false")) multiplexer_5 (
    .in0(HALT), .in1(1'b0), .out(multiplexer_5_out), .sel(FLUSH));
  Multiplexer #(.select(1), .width(32), .disabled("Z"), .enable("false")) multiplexer_6 (
    .in0(ALURESULT), .in1({32{1'b0}}), .out(multiplexer_6_out), .sel(FLUSH));
  Multiplexer #(.select(1), .width(32), .disabled("Z"), .enable("false")) multiplexer_7 (
    .in0(MEMDATA), .in1({32{1'b0}}), .out(multiplexer_7_out), .sel(FLUSH));
  Multiplexer #(.select(1), .width(1), .disabled("Z"), .enable("false")) multiplexer_8 (
    .in0(lhu), .in1(1'b0), .out(multiplexer_8_out), .sel(FLUSH));
  Multiplexer #(.select(1), .width(5), .disabled("Z"), .enable("false")) multiplexer_9 (
    .in0(WRITEREG), .in1({5{1'b0}}), .out(multiplexer_9_out), .sel(FLUSH));
  Multiplexer #(.select(1), .width(32), .disabled("Z"), .enable("false")) multiplexer_10 (
    .in0(PC), .in1({32{1'b0}}), .out(multiplexer_10_out), .sel(FLUSH));
  Multiplexer #(.select(1), .width(32), .disabled("Z"), .enable("false")) multiplexer_11 (
    .in0(IR), .in1({32{1'b0}}), .out(multiplexer_11_out), .sel(FLUSH));
  Multiplexer #(.select(1), .width(32), .disabled("Z"), .enable("false")) multiplexer_12 (
    .in0(IMM), .in1({32{1'b0}}), .out(multiplexer_12_out), .sel(FLUSH));
  Multiplexer #(.select(1), .width(32), .disabled("Z"), .enable("false")) multiplexer_13 (
    .in0(AUIPCIMM), .in1({32{1'b0}}), .out(multiplexer_13_out), .sel(FLUSH));
  not not_1 (not_1_out, EN);
  Register #(.width(1), .trigger("rising"), .Select("low")) register_1 (
    .D(multiplexer_1_out), .en(not_1_out), .Q(JOUT), .clk(CLK), .clr(RST));
  Register #(.width(1), .trigger("rising"), .Select("low")) register_2 (
    .D(multiplexer_2_out), .en(not_1_out), .Q(MEMTOREGOUT), .clk(CLK), .clr(RST));
  Register #(.width(1), .trigger("rising"), .Select("low")) register_3 (
    .D(multiplexer_3_out), .en(not_1_out), .Q(REGWRITEOUT), .clk(CLK), .clr(RST));
  Register #(.width(1), .trigger("rising"), .Select("low")) register_4 (
    .D(multiplexer_4_out), .en(not_1_out), .Q(UTYPEOUT), .clk(CLK), .clr(RST));
  Register #(.width(1), .trigger("rising"), .Select("low")) register_5 (
    .D(multiplexer_5_out), .en(not_1_out), .Q(HALTOUT), .clk(CLK), .clr(RST));
  Register #(.width(32), .trigger("rising"), .Select("low")) register_6 (
    .D(multiplexer_6_out), .en(not_1_out), .Q(ALURESULTOUT), .clk(CLK), .clr(RST));
  Register #(.width(32), .trigger("rising"), .Select("low")) register_7 (
    .D(multiplexer_7_out), .en(not_1_out), .Q(MEMDATAOUT), .clk(CLK), .clr(RST));
  Register #(.width(1), .trigger("rising"), .Select("low")) register_8 (
    .D(multiplexer_8_out), .en(not_1_out), .Q(lhuout), .clk(CLK), .clr(RST));
  Register #(.width(5), .trigger("rising"), .Select("low")) register_9 (
    .D(multiplexer_9_out), .en(not_1_out), .Q(WRITEREGOUT), .clk(CLK), .clr(RST));
  Register #(.width(32), .trigger("rising"), .Select("low")) register_10 (
    .D(multiplexer_10_out), .en(not_1_out), .Q(PCOUT), .clk(CLK), .clr(RST));
  Register #(.width(32), .trigger("rising"), .Select("low")) register_11 (
    .D(multiplexer_11_out), .en(not_1_out), .Q(IROUT), .clk(CLK), .clr(RST));
  Register #(.width(32), .trigger("rising"), .Select("low")) register_12 (
    .D(multiplexer_12_out), .en(not_1_out), .Q(IMMOUT), .clk(CLK), .clr(RST));
  Register #(.width(32), .trigger("rising"), .Select("low")) register_13 (
    .D(multiplexer_13_out), .en(not_1_out), .Q(AUIPCIMMOUT), .clk(CLK), .clr(RST));
endmodule
module \气泡冲突检测逻辑  (
  input  MEM_REGWRITE,
  input  EX_REGWRITE,
  input  [4:0] EX_WRITEREG,
  input  [4:0] MEM_WRITEREG,
  input  [31:0] ID_IR,
  output confl
);

  wire ALUSRCB, and_1_out, and_2_out, and_3_out, and_4_out, and_5_out, and_6_out, and_7_out, comparator_1_eq,
       comparator_2_eq, comparator_3_eq, comparator_4_eq, comparator_5_eq, comparator_6_eq, ID_ecall, JAL,
       not_2_out, not_3_out, not_4_out, not_5_out, R1USED, R2USED, S_type;
  wire [4:0] multiplexer_1_out, multiplexer_2_out;

  not not_1 (R1USED, JAL);
  \单周期硬布线控制器  \u_单周期硬布线控制器_1  (
    .Funct({ID_IR[30], ID_IR[25], ID_IR[14:12]}), .OP(ID_IR[6:2]), .ALU_SRC(ALUSRCB), .ecall(ID_ecall),
    .S_type(S_type), .JAL(JAL), .in_3(ID_IR[21]));  // open: ALU_OP, MemToReg, MemWrite, RegWrite, Jalr, Beq, Bne, uret, blt, U_type, lhu, csrrsi, csrrci
  Multiplexer #(.select(1), .width(5), .disabled("Z"), .enable("false")) multiplexer_1 (
    .in0(ID_IR[19:15]), .in1(5'b10001), .out(multiplexer_1_out), .sel(ID_ecall));
  not not_2 (not_2_out, JAL);
  not not_3 (not_3_out, ALUSRCB);
  Multiplexer #(.select(1), .width(5), .disabled("Z"), .enable("false")) multiplexer_2 (
    .in0(ID_IR[24:20]), .in1(5'b01010), .out(multiplexer_2_out), .sel(ID_ecall));
  and and_1 (and_1_out, not_2_out, not_3_out);
  or or_1 (R2USED, and_1_out, S_type);
  Comparator #(.width(5), .mode("twosComplement")) comparator_1 (
    .a(EX_WRITEREG), .b(multiplexer_2_out), .eq(comparator_1_eq));  // open: gt, lt
  Comparator #(.width(5), .mode("twosComplement")) comparator_2 (
    .a(EX_WRITEREG), .b(multiplexer_1_out), .eq(comparator_2_eq));  // open: gt, lt
  Comparator #(.width(5), .mode("twosComplement")) comparator_3 (
    .a(MEM_WRITEREG), .b(multiplexer_2_out), .eq(comparator_3_eq));  // open: gt, lt
  Comparator #(.width(5), .mode("twosComplement")) comparator_4 (
    .a(MEM_WRITEREG), .b(multiplexer_1_out), .eq(comparator_4_eq));  // open: gt, lt
  Comparator #(.width(5), .mode("twosComplement")) comparator_5 (
    .a(multiplexer_2_out), .b({5{1'b0}}), .eq(comparator_5_eq));  // open: gt, lt
  Comparator #(.width(5), .mode("twosComplement")) comparator_6 (
    .a(multiplexer_1_out), .b({5{1'b0}}), .eq(comparator_6_eq));  // open: gt, lt
  not not_4 (not_4_out, comparator_5_eq);
  not not_5 (not_5_out, comparator_6_eq);
  and and_2 (and_2_out, not_4_out, R2USED);
  and and_3 (and_3_out, not_5_out, R1USED);
  and and_4 (and_4_out, EX_REGWRITE, comparator_1_eq, and_2_out);
  and and_5 (and_5_out, EX_REGWRITE, comparator_2_eq, and_3_out);
  and and_6 (and_6_out, MEM_REGWRITE, comparator_3_eq, and_2_out);
  and and_7 (and_7_out, MEM_REGWRITE, comparator_4_eq, and_3_out);
  or or_2 (confl, and_4_out, and_5_out, and_6_out, and_7_out);

  // Notes on the sheet:
  //   JAL
  //   JALR
  //   URET
  //   R1
  //   R2
  //   Beq
  //   Bne
  //   AluOP
  //   AluSrcB
  //   RegWrite
  //   MemToReg
  //   MemWrite
endmodule

module \重定向冲突检测逻辑  (
  input  EX_REGWRITE,
  input  MEM_REGWRITE,
  input  [4:0] MEM_WRITEREG,
  input  [4:0] EX_WRITEREG,
  input  EX_MEMTOREG,
  input  [31:0] ID_IR,
  output [1:0] R1FOWARD,
  output LOADUSE,
  output [1:0] R2FOWARD
);

  wire ALUSRCB, and_1_out, and_2_out, and_3_out, comparator_1_eq, comparator_2_eq, comparator_3_eq,
       comparator_4_eq, comparator_5_eq, comparator_6_eq, comparator_7_eq, comparator_8_eq, comparator_9_eq,
       comparator_10_eq, ID_ecall, JAL, not_2_out, not_3_out, not_4_out, not_5_out, not_6_out, not_7_out,
       R1USED, R2USED, STYPE;
  wire [4:0] R1, R2;

  not not_1 (R1USED, JAL);
  \单周期硬布线控制器  \u_单周期硬布线控制器_1  (
    .Funct({ID_IR[30], ID_IR[25], ID_IR[14:12]}), .OP(ID_IR[6:2]), .ALU_SRC(ALUSRCB), .ecall(ID_ecall),
    .S_type(STYPE), .JAL(JAL), .in_3(ID_IR[21]));  // open: ALU_OP, MemToReg, MemWrite, RegWrite, Jalr, Beq, Bne, uret, blt, U_type, lhu, csrrsi, csrrci
  Multiplexer #(.select(1), .width(5), .disabled("Z"), .enable("false")) multiplexer_1 (
    .in0(ID_IR[19:15]), .in1(5'b10001), .out(R1), .sel(ID_ecall));
  not not_2 (not_2_out, JAL);
  not not_3 (not_3_out, ALUSRCB);
  Multiplexer #(.select(1), .width(5), .disabled("Z"), .enable("false")) multiplexer_2 (
    .in0(ID_IR[24:20]), .in1(5'b01010), .out(R2), .sel(ID_ecall));
  and and_1 (and_1_out, not_2_out, not_3_out);
  or or_1 (R2USED, and_1_out, STYPE);
  Comparator #(.width(5), .mode("twosComplement")) comparator_1 (
    .a(EX_WRITEREG), .b(R1), .eq(comparator_1_eq));  // open: gt, lt
  Comparator #(.width(5), .mode("twosComplement")) comparator_2 (
    .a(EX_WRITEREG), .b(R2), .eq(comparator_2_eq));  // open: gt, lt
  Comparator #(.width(5), .mode("twosComplement")) comparator_3 (
    .a(R1), .b({5{1'b0}}), .eq(comparator_3_eq));  // open: gt, lt
  Comparator #(.width(5), .mode("twosComplement")) comparator_4 (
    .a(R2), .b({5{1'b0}}), .eq(comparator_4_eq));  // open: gt, lt
  not not_4 (not_4_out, comparator_3_eq);
  not not_5 (not_5_out, comparator_4_eq);
  and and_2 (and_2_out, comparator_1_eq, EX_MEMTOREG, R1USED, not_4_out);
  and and_3 (and_3_out, comparator_2_eq, EX_MEMTOREG, not_5_out, R2USED);
  or or_2 (LOADUSE, and_2_out, and_3_out);
  Comparator #(.width(5), .mode("twosComplement")) comparator_5 (
    .a(R1), .b({5{1'b0}}), .eq(comparator_5_eq));  // open: gt, lt
  not not_6 (not_6_out, comparator_5_eq);
  Comparator #(.width(5), .mode("twosComplement")) comparator_6 (
    .a(EX_WRITEREG), .b(R1), .eq(comparator_6_eq));  // open: gt, lt
  Comparator #(.width(5), .mode("twosComplement")) comparator_7 (
    .a(R2), .b({5{1'b0}}), .eq(comparator_7_eq));  // open: gt, lt
  Comparator #(.width(5), .mode("twosComplement")) comparator_8 (
    .a(R1), .b(MEM_WRITEREG), .eq(comparator_8_eq));  // open: gt, lt
  Comparator #(.width(5), .mode("twosComplement")) comparator_9 (
    .a(R2), .b(MEM_WRITEREG), .eq(comparator_9_eq));  // open: gt, lt
  not not_7 (not_7_out, comparator_7_eq);
  Comparator #(.width(5), .mode("twosComplement")) comparator_10 (
    .a(EX_WRITEREG), .b(R2), .eq(comparator_10_eq));  // open: gt, lt
  and and_4 (R1FOWARD[0], comparator_8_eq, MEM_REGWRITE, not_6_out, R1USED);
  and and_5 (R1FOWARD[1], not_6_out, R1USED, EX_REGWRITE, comparator_6_eq);
  and and_6 (R2FOWARD[1], not_7_out, R2USED, EX_REGWRITE, comparator_10_eq);
  and and_7 (R2FOWARD[0], comparator_9_eq, MEM_REGWRITE, not_7_out, R2USED);

  // Notes on the sheet:
  //   R1
  //   R2
  //   JAL
  //   JALR
  //   URET
  //   Beq
  //   Bne
  //   MemToReg
  //   MemWrite
  //   AluOP
  //   AluSrcB
  //   RegWrite
endmodule

module \regfile气泡_重定向  (
  input  [31:0] Din,
  input  Clk,
  input  WE,
  input  [4:0] R1_num,
  input  [4:0] W_num,
  input  [4:0] R2_num,
  output [31:0] R1,
  output [31:0] R2
);

  // RegisterFile registerfile_1: pin names not known; wires that end beside it: Din, Clk, WE, W_num, R1_num, R2_num, R1, R2
endmodule

module \流水线中断单级EX  (
  input  IR1,
  input  IR2,
  input  IR3,
  output RegWrite,
  output MemWrite,
  output [31:0] IF_PC,
  output [31:0] ID_PC,
  output [31:0] EX_PC,
  output [31:0] M_PC,
  output [31:0] WB_PC,
  output [31:0] RDin,
  output [31:0] MDin,
  output [31:0] LedData
);

  wire alu_1_equal, alu_1_out_6, and_1_out, and_2_out, and_3_out, and_5_out, and_6_out, and_7_out,
       and_10_out, and_11_out, and_12_out, and_13_out, and_14_out, AUIPC, B, blt, Branch, CLK, clock_1_out,
       CLR1, CLR2, CLR3, comparator_1_eq, comparator_2_eq, comparator_3_eq, comparator_4_eq, comparator_5_eq,
       comparator_5_lt, comparator_6_eq, controlled_inverter_1_out, controlled_inverter_2_out,
       controlled_inverter_3_out, d_ff_1_q, d_ff_2_q, d_ff_3_q, d_ff_5_q, d_ff_6_q, ecall, en,
       ex_mem_1_haltout, ex_mem_1_lhuout, ex_mem_1_memtoregout, EX_MemToReg, EX_RegWrite, EX_URET, Go, halt,
       id_ex_1_alusrcout, id_ex_1_beqout, id_ex_1_bneout, id_ex_1_ecallout, id_ex_1_lhuout,
       id_ex_1_memwriteout, id_ex_1_utypeout, IE, INTR, INTR1, INTR2, INTR3, IR1_t, IR2_t, IR3_t, IRA, IRB,
       IRC, IRHAVE, JAL, JALR, JUMP, loaduse, MEM_J, MEM_RegWrite, mem_wb_1_jout, mem_wb_1_lhuout,
       mem_wb_1_memtoregout, mem_wb_1_utypeout, nand_1_out, not_1_out, not_2_out, not_3_out, not_4_out,
       not_5_out, or_4_out, or_5_out, or_6_out, or_7_out, or_11_out, or_12_out, or_16_out, or_17_out,
       or_18_out, or_19_out, or_20_out, RST, S_Type, W1, W2, W3, \单周期硬布线控制器_1_alu_src , \单周期硬布线控制器_1_beq ,
       \单周期硬布线控制器_1_blt , \单周期硬布线控制器_1_bne , \单周期硬布线控制器_1_jal , \单周期硬布线控制器_1_jalr , \单周期硬布线控制器_1_lhu ,
       \单周期硬布线控制器_1_memtoreg , \单周期硬布线控制器_1_memwrite , \单周期硬布线控制器_1_regwrite , \单周期硬布线控制器_1_u_type ,
       \单周期硬布线控制器_1_uret ;
  wire [1:0] EX_R1F, EX_R2F, priority_encoder_1_out, priority_encoder_2_out, priority_encoder_3_out,
       R1Foward, R2Foward, register_1_q;
  wire [3:0] id_ex_1_aluopout, \单周期硬布线控制器_1_alu_op ;
  wire [4:0] EX_WriteReg, MEM_WriteReg, multiplexer_8_out, multiplexer_9_out, W_num;
  wire [12:0] CNT_num;
  wire [15:0] \LoadUse次数 , multiplexer_17_out, \总周期数 , \插入气泡数 , \无条件分支数 , \条件分支成功数 ;
  wire [31:0] adder_2_out, adder_5_out, aluresult, b_t, bit_extender_1_out, bit_extender_2_out,
       bit_extender_3_out, bit_extender_4_out, bit_extender_5_out, bit_extender_6_out, EX_IR,
       ex_mem_1_aluresultout, ex_mem_1_aupicimmout, ex_mem_1_immout, EX_R1, EX_R2, id_ex_1_imm1out_prime,
       id_ex_1_imm2out_prime, id_ex_1_imm3out_prime, id_ex_1_imm4out_prime, ID_IR, IF_IR, IR_PC, jal_t,
       jalr_t, MEM_IR, MEM_Result, mem_wb_1_aluresultout, mem_wb_1_auipcimmout, mem_wb_1_immout,
       mem_wb_1_memdataout, MEPC, multiplexer_4_out, multiplexer_5_out, multiplexer_6_out, multiplexer_7_out,
       multiplexer_10_out, multiplexer_11_out, multiplexer_12_out, multiplexer_13_out, multiplexer_15_out,
       multiplexer_16_out, multiplexer_18_out, PC_4, R1R, R2R, ram_1_data, \regfile气泡_重定向_1_r1 ,
       \regfile气泡_重定向_1_r2 , shifter_1_out, shifter_2_out, shifter_3_out, WB_IR;

  Button \u_总复位  (.out(RST));
  Button _1 (.out(IRA));
  Button _2 (.out(IRB));
  Button _3 (.out(IRC));
  // Probe on \总周期数 
  // Probe on \总周期数 
  Button \u_继续运行  (.out(Go));
  LED #(.active("true")) led_1 (.in(W1));
  LED #(.active("true")) led_2 (.in(W2));
  LED #(.active("true")) led_3 (.in(W3));
  Hex_Digit_Display hex_digit_display_1 (.value(LedData[31:28]));  // open: dp
  // Probe on IF_PC[19:0]
  // RiscV_Probe riscv_probe_1: pin names not known; wires that end beside it: IF_IR
  Comparator #(.width(16), .mode("twosComplement")) comparator_1 (
    .a(16'h23b), .b(\总周期数 ), .eq(comparator_1_eq));  // open: gt, lt
  Comparator #(.width(16), .mode("twosComplement")) comparator_2 (
    .a(\总周期数 ), .b(16'h1), .eq(comparator_2_eq));  // open: gt, lt
  Comparator #(.width(16), .mode("twosComplement")) comparator_3 (
    .a(\总周期数 ), .b(16'h4), .eq(comparator_3_eq));  // open: gt, lt
  Comparator #(.width(16), .mode("twosComplement")) comparator_4 (
    .a(\总周期数 ), .b(16'h7), .eq(comparator_4_eq));  // open: gt, lt
  D_Flip_Flop #(.trigger("rising"), .Pre_Clr_Positions("LEGACY"), .NegatePresetClear("false"), .enable("true"), .NewFFLayout("false")) d_ff_1 (
    .clk(IRA), .D(1'b1), .Q(d_ff_1_q), .reset(INTR1));  // open: Qn, preset, en
  or or_1 (W1, INTR1, d_ff_1_q);
  D_Flip_Flop #(.trigger("rising"), .Pre_Clr_Positions("LEGACY"), .NegatePresetClear("false"), .enable("true"), .NewFFLayout("false")) d_ff_2 (
    .clk(IRB), .D(1'b1), .Q(d_ff_2_q), .reset(INTR2));  // open: Qn, preset, en
  or or_2 (W2, INTR2, d_ff_2_q);
  or or_3 (W3, INTR3, d_ff_3_q);
  Hex_Digit_Display hex_digit_display_2 (.value(LedData[23:20]));  // open: dp
  Hex_Digit_Display hex_digit_display_3 (.value(LedData[27:24]));  // open: dp
  // Probe on ID_PC[19:0]
  // RiscV_Probe riscv_probe_2: pin names not known; wires that end beside it: ID_IR, IRB, IRA
  or or_4 (or_4_out, comparator_1_eq, comparator_2_eq);
  assign controlled_inverter_1_out = or_4_out ? ~CLK : 1'bz;  // Controlled_Inverter controlled_inverter_1
  assign controlled_inverter_2_out = comparator_3_eq ? ~CLK : 1'bz;  // Controlled_Inverter controlled_inverter_2
  assign controlled_inverter_3_out = comparator_4_eq ? ~CLK : 1'bz;  // Controlled_Inverter controlled_inverter_3
  D_Flip_Flop #(.trigger("rising"), .Pre_Clr_Positions("LEGACY"), .NegatePresetClear("false"), .enable("true"), .NewFFLayout("false")) d_ff_3 (
    .clk(IRC), .D(1'b1), .Q(d_ff_3_q), .reset(INTR3));  // open: Qn, preset, en
  Multiplexer #(.select(2), .width(32), .disabled("Z"), .enable("false")) multiplexer_1 (
    .in0(32'h30ac), .in1(32'h3150), .in2(32'h31f4), .out(IR_PC), .sel(priority_encoder_1_out));  // open: in3
  Priority_Encoder #(.select(2), .disabled("Z")) priority_encoder_1 (
    .in0(INTR1), .in1(INTR2), .in2(INTR3), .out(priority_encoder_1_out));  // open: in3, gs, en_out, en_in
  Hex_Digit_Display hex_digit_display_4 (.value(LedData[19:16]));  // open: dp
  Hex_Digit_Display hex_digit_display_5 (.value(LedData[15:12]));  // open: dp
  Pull_Resistor #(.pull(0)) pull_resistor_1 (.node(controlled_inverter_1_out));
  Pull_Resistor #(.pull(0)) pull_resistor_2 (.node(controlled_inverter_2_out));
  Pull_Resistor #(.pull(0)) pull_resistor_3 (.node(controlled_inverter_3_out));
  or or_5 (or_5_out, d_ff_1_q, INTR1);
  and and_1 (and_1_out, or_5_out, ~CLR1);  // AND_Gate
  or or_6 (or_6_out, d_ff_2_q, INTR2);
  and and_2 (and_2_out, or_6_out, ~CLR2);  // AND_Gate
  or or_7 (or_7_out, d_ff_3_q, INTR3);
  and and_3 (and_3_out, or_7_out, ~CLR3);  // AND_Gate
  or or_8 (JUMP, B, JAL, JALR);
  or or_9 (Branch, B, JAL, JALR, EX_URET, INTR);
  Hex_Digit_Display hex_digit_display_6 (.value(LedData[7:4]));  // open: dp
  Hex_Digit_Display hex_digit_display_7 (.value(LedData[11:8]));  // open: dp
  // Probe on EX_PC[19:0]
  // RiscV_Probe riscv_probe_3: pin names not known; wires that end beside it: EX_IR
  D_Flip_Flop #(.trigger("rising"), .Pre_Clr_Positions("LEGACY"), .NegatePresetClear("false"), .enable("true"), .NewFFLayout("false")) u_IR1 (
    .clk(CLK), .D(and_1_out), .Q(INTR1));  // open: Qn, preset, en, reset
  D_Flip_Flop #(.trigger("rising"), .Pre_Clr_Positions("LEGACY"), .NegatePresetClear("false"), .enable("true"), .NewFFLayout("false")) IR1_2 (
    .clk(CLK), .D(and_2_out), .Q(INTR2));  // open: Qn, preset, en, reset
  D_Flip_Flop #(.trigger("rising"), .Pre_Clr_Positions("LEGACY"), .NegatePresetClear("false"), .enable("true"), .NewFFLayout("false")) IR1_3 (
    .clk(CLK), .D(and_3_out), .Q(INTR3));  // open: Qn, preset, en, reset
  Hex_Digit_Display hex_digit_display_8 (.value(LedData[3:0]));  // open: dp
  Register #(.width(2), .trigger("rising"), .Select("low")) register_1 (
    .D(priority_encoder_1_out), .en(INTR), .Q(register_1_q), .clk(CLK));  // open: clr
  // Probe on \总周期数 
  // Probe on M_PC[19:0]
  // RiscV_Probe riscv_probe_4: pin names not known; wires that end beside it: MEM_IR
  or or_10 (IRHAVE, INTR1, INTR2, INTR3);
  or or_11 (or_11_out, ~IRHAVE, EX_URET);  // OR_Gate
  // Probe on \总周期数 
  // Probe on \无条件分支数 
  // Probe on \条件分支成功数 
  // Probe on \插入气泡数 
  // Probe on \LoadUse次数 
  D_Flip_Flop #(.trigger("rising"), .Pre_Clr_Positions("LEGACY"), .NegatePresetClear("false"), .enable("true"), .NewFFLayout("true")) d_ff_4 (
    .clk(CLK), .D(or_11_out), .Q(IE));  // open: Qn, preset, en, reset
  Demultiplexer #(.select(2), .width(1), .tristate("false"), .disabled("Z"), .enable("false")) demultiplexer_1 (
    .out0(CLR1), .out1(CLR2), .out2(CLR3), .in(EX_URET), .sel(register_1_q));  // open: out3
  // Probe on IF_PC[11:0]
  // Probe on WB_PC[19:0]
  // RiscV_Probe riscv_probe_5: pin names not known; wires that end beside it: WB_IR
  and and_4 (INTR, IRHAVE, IE);
  Multiplexer #(.select(2), .width(32), .disabled("Z"), .enable("false")) multiplexer_2 (
    .in0(EX_R1), .in1(RDin), .in2(MEM_Result), .in3(MEM_Result), .out(R1R), .sel(EX_R1F));
  Multiplexer #(.select(2), .width(32), .disabled("Z"), .enable("false")) multiplexer_3 (
    .in0(EX_R2), .in1(RDin), .in2(MEM_Result), .in3(MEM_Result), .out(R2R), .sel(EX_R2F));
  // Probe on EX_PC[11:0]
  // Probe on ID_PC[11:0]
  // Probe on M_PC[11:0]
  D_Flip_Flop #(.trigger("high"), .Pre_Clr_Positions("LEGACY"), .NegatePresetClear("false"), .enable("true"), .NewFFLayout("false")) d_ff_5 (.Q(d_ff_5_q));  // open: clk, D, Qn, preset, en, reset
  // Probe on 13'hc
  D_Flip_Flop #(.trigger("rising"), .Pre_Clr_Positions("LEGACY"), .NegatePresetClear("false"), .enable("true"), .NewFFLayout("false")) d_ff_6 (
    .clk(CLK), .D(EX_URET), .Q(d_ff_6_q));  // open: Qn, preset, en, reset
  Multiplexer #(.select(1), .width(32), .disabled("Z"), .enable("false")) multiplexer_4 (
    .in0(multiplexer_6_out), .in1(multiplexer_5_out), .out(multiplexer_4_out), .sel(JUMP));
  Register #(.width(32), .trigger("rising"), .Select("low")) register_2 (
    .D(multiplexer_4_out), .en(INTR), .Q(MEPC), .clk(CLK));  // open: clr
  // Probe on WB_PC[11:0]
  Comparator #(.width(13), .mode("twosComplement")) comparator_5 (
    .a(CNT_num), .b(13'hc), .eq(comparator_5_eq), .lt(comparator_5_lt));  // open: gt
  Clock #(.highDuration(1), .lowDuration(1)) clock_1 (.out(clock_1_out));
  Priority_Encoder #(.select(2), .disabled("Z")) priority_encoder_2 (
    .in0(1'b1), .in1(B), .in2(JAL), .in3(JALR), .out(priority_encoder_2_out));  // open: gs, en_out, en_in
  Multiplexer #(.select(2), .width(32), .disabled("Z"), .enable("false")) multiplexer_5 (
    .in0(PC_4), .in1(b_t), .in2(jal_t), .in3(jalr_t), .out(multiplexer_5_out), .sel(priority_encoder_2_out));
  Multiplexer #(.select(1), .width(32), .disabled("Z"), .enable("false")) multiplexer_6 (
    .in0(ID_PC), .in1(IF_PC), .out(multiplexer_6_out), .sel(d_ff_6_q));
  nand nand_1 (nand_1_out, d_ff_5_q, comparator_5_eq);
  Counter #(.width(13), .max('h1fff), .ongoal("stay"), .trigger("rising"), .behavior("old")) counter_1 (
    .count(comparator_5_lt), .Q(CNT_num), .clk(clock_1_out));  // open: load, D, carry, clr, preset
  assign CLK = nand_1_out ? clock_1_out : 1'bz;  // Controlled_Buffer controlled_buffer_1
  Pull_Resistor #(.pull(1)) pull_resistor_4 (.node(CLK));
  Priority_Encoder #(.select(2), .disabled("Z")) priority_encoder_3 (
    .in0(1'b1), .in1(INTR), .in2(EX_URET), .out(priority_encoder_3_out));  // open: in3, gs, en_out, en_in
  Multiplexer #(.select(2), .width(32), .disabled("Z"), .enable("false")) multiplexer_7 (
    .in0(multiplexer_5_out), .in1(IR_PC), .in2(MEPC), .out(multiplexer_7_out), .sel(priority_encoder_3_out));  // open: in3
  and and_5 (and_5_out, ~loaduse, or_12_out);  // AND_Gate
  or or_12 (or_12_out, Go, not_1_out);
  not not_1 (not_1_out, halt);
  or or_13 (IR1_t, IR1, IRA);
  Register #(.width(32), .trigger("rising"), .Select("low")) PC (
    .D(multiplexer_7_out), .en(and_5_out), .Q(IF_PC), .clk(CLK), .clr(RST));
  Adder #(.width(32)) adder_1 (.a(IF_PC), .b(32'h4), .out(PC_4));  // open: cin, cout
  or or_14 (IR2_t, IR2, IRB);
  ROM #(.addrWidth(10), .dataWidth(32), .Select("high")) rom_1 (.addr(IF_PC[11:2]), .data(IF_IR));
  or or_15 (IR3_t, IR3, IRC);
  IF_ID if_id_1 (
    .IR(IF_IR), .PC(IF_PC), .IROUT(ID_IR), .PCOUT(ID_PC), .CLK(CLK), .RST(RST), .FLUSH(Branch), .EN(or_16_out));  // open: PREDICT, PREDICTOUT
  or or_16 (or_16_out, and_6_out, loaduse);
  and and_6 (and_6_out, ~Go, halt);  // AND_Gate
  // RiscV_Probe riscv_probe_6: pin names not known; wires that end beside it: CLK, RST, ID_IR
  or or_17 (or_17_out, Go, not_2_out);
  Counter #(.width(16), .max('hffff), .ongoal("wrap"), .trigger("rising"), .behavior("new")) counter_2 (
    .count(or_17_out), .Q(\总周期数 ), .clk(CLK));  // open: load, D, carry, clr, preset, down
  not not_2 (not_2_out, halt);
  Multiplexer #(.select(1), .width(5), .disabled("Z"), .enable("false")) multiplexer_8 (
    .in0(ID_IR[19:15]), .in1(5'b10001), .out(multiplexer_8_out), .sel(ecall));
  \单周期硬布线控制器  \u_单周期硬布线控制器_1  (
    .Funct({ID_IR[30], ID_IR[25], ID_IR[14:12]}), .OP(ID_IR[6:2]), .ALU_OP(\单周期硬布线控制器_1_alu_op ),
    .MemToReg(\单周期硬布线控制器_1_memtoreg ), .MemWrite(\单周期硬布线控制器_1_memwrite ), .ALU_SRC(\单周期硬布线控制器_1_alu_src ),
    .RegWrite(\单周期硬布线控制器_1_regwrite ), .ecall(ecall), .S_type(S_Type), .Jalr(\单周期硬布线控制器_1_jalr ),
    .Beq(\单周期硬布线控制器_1_beq ), .JAL(\单周期硬布线控制器_1_jal ), .Bne(\单周期硬布线控制器_1_bne ), .in_3(ID_IR[21]),
    .uret(\单周期硬布线控制器_1_uret ), .blt(\单周期硬布线控制器_1_blt ), .U_type(\单周期硬布线控制器_1_u_type ), .lhu(\单周期硬布线控制器_1_lhu ));  // open: csrrsi, csrrci
  Multiplexer #(.select(1), .width(5), .disabled("Z"), .enable("false")) multiplexer_9 (
    .in0(ID_IR[24:20]), .in1(5'b01010), .out(multiplexer_9_out), .sel(ecall));
  assign bit_extender_1_out = {{20{ID_IR[31]}}, ID_IR[31:20]};  // Bit_Extender bit_extender_1
  assign bit_extender_2_out = {{20{ID_IR[31]}}, {ID_IR[31:25], ID_IR[11:7]}};  // Bit_Extender bit_extender_2
  assign bit_extender_3_out = {{12{ID_IR[31]}}, ID_IR[31:12]};  // Bit_Extender bit_extender_3
  assign bit_extender_4_out = {{20{ID_IR[31]}}, {ID_IR[31], ID_IR[7], ID_IR[30:25], ID_IR[11:8]}};  // Bit_Extender bit_extender_4
  assign bit_extender_5_out = {{12{ID_IR[31]}}, {ID_IR[31], ID_IR[19:12], ID_IR[20], ID_IR[30:21]}};  // Bit_Extender bit_extender_5
  Multiplexer #(.select(1), .width(32), .disabled("Z"), .enable("false")) multiplexer_10 (
    .in0(bit_extender_1_out), .in1(bit_extender_2_out), .out(multiplexer_10_out), .sel(S_Type));
  Shifter #(.width(32), .shift("ll")) shifter_1 (.in(bit_extender_3_out), .\dist (5'b01100), .out(shifter_1_out));
  Shifter #(.width(32), .shift("ll")) shifter_2 (.in(bit_extender_4_out), .\dist (5'b00001), .out(shifter_2_out));
  Shifter #(.width(32), .shift("ll")) shifter_3 (.in(bit_extender_5_out), .\dist (5'b00001), .out(shifter_3_out));
  \regfile气泡_重定向  \regfile气泡_重定向_1  (
    .Din(RDin), .Clk(CLK), .R1(\regfile气泡_重定向_1_r1 ), .R2(\regfile气泡_重定向_1_r2 ), .WE(RegWrite),
    .W_num(W_num), .R1_num(multiplexer_8_out), .R2_num(multiplexer_9_out));
  or or_18 (or_18_out, Branch, loaduse);
  and and_7 (and_7_out, ~Go, halt);  // AND_Gate
  \重定向冲突检测逻辑  \u_重定向冲突检测逻辑_1  (
    .EX_REGWRITE(EX_RegWrite), .MEM_REGWRITE(MEM_RegWrite), .MEM_WRITEREG(MEM_WriteReg),
    .EX_WRITEREG(EX_WriteReg), .EX_MEMTOREG(EX_MemToReg), .ID_IR(ID_IR), .R1FOWARD(R1Foward),
    .LOADUSE(loaduse), .R2FOWARD(R2Foward));
  ID_EX id_ex_1 (
    .CLK(CLK), .RST(RST), .JAL(\单周期硬布线控制器_1_jal ), .JALOUT(JAL), .JALR(\单周期硬布线控制器_1_jalr ), .JALROUT(JALR),
    .URET(\单周期硬布线控制器_1_uret ), .URETOUT(EX_URET), .beq(\单周期硬布线控制器_1_beq ), .BEQOUT(id_ex_1_beqout),
    .BNE(\单周期硬布线控制器_1_bne ), .BNEOUT(id_ex_1_bneout), .MEMTOREG(\单周期硬布线控制器_1_memtoreg ),
    .MEMTOREGOUT(EX_MemToReg), .MEMWRITE(\单周期硬布线控制器_1_memwrite ), .MEMWRITEOUT(id_ex_1_memwriteout),
    .ALUOP(\单周期硬布线控制器_1_alu_op ), .ALUOPOUT(id_ex_1_aluopout), .ALUSRC(\单周期硬布线控制器_1_alu_src ),
    .ALUSRCOUT(id_ex_1_alusrcout), .REGWRITE(\单周期硬布线控制器_1_regwrite ), .REGWRITEOUT(EX_RegWrite),
    .U_type(\单周期硬布线控制器_1_u_type ), .UTYPEOUT(id_ex_1_utypeout), .BLT(\单周期硬布线控制器_1_blt ), .BLTOUT(blt),
    .ECALL(ecall), .ECALLOUT(id_ex_1_ecallout), .lhu(\单周期硬布线控制器_1_lhu ), .lhuOUT(id_ex_1_lhuout),
    .R1F(R1Foward), .R1FOUT(EX_R1F), .R1(\regfile气泡_重定向_1_r1 ), .R1OUT(EX_R1), .R2(\regfile气泡_重定向_1_r2 ),
    .R2OUT_prime(EX_R2), .R2F(R2Foward), .R2FOUT(EX_R2F), .WRITEREG(ID_IR[11:7]),
    .WRITEREGOUT_prime(EX_WriteReg), .PC(ID_PC), .PCOUT_prime(EX_PC), .IR(ID_IR), .IROUT_prime(EX_IR),
    .IMM1(multiplexer_10_out), .IMM1OUT_prime(id_ex_1_imm1out_prime), .IMM2(shifter_2_out),
    .IMM2OUT_prime(id_ex_1_imm2out_prime), .IMM3(shifter_3_out), .IMM3OUT_prime(id_ex_1_imm3out_prime),
    .IMM4(shifter_1_out), .IMM4OUT_prime(id_ex_1_imm4out_prime), .EN(and_7_out), .FLUSH(or_18_out));  // open: PREDICT, PREDICTOUT
  or or_19 (or_19_out, JALR, JAL);
  and and_8 (en, id_ex_1_ecallout, comparator_6_eq);
  Comparator #(.width(32), .mode("twosComplement")) comparator_6 (
    .a(R1R), .b(32'h22), .eq(comparator_6_eq));  // open: gt, lt
  Adder #(.width(32)) adder_2 (.a(id_ex_1_imm4out_prime), .b(EX_PC), .out(adder_2_out));  // open: cin, cout
  Adder #(.width(32)) adder_3 (.a(EX_PC), .b(id_ex_1_imm2out_prime), .out(b_t));  // open: cin, cout
  Adder #(.width(32)) adder_4 (.a(id_ex_1_imm3out_prime), .b(EX_PC), .out(jal_t));  // open: cin, cout
  not not_3 (not_3_out, comparator_6_eq);
  Multiplexer #(.select(1), .width(32), .disabled("Z"), .enable("false")) multiplexer_11 (
    .in0({32{1'b0}}), .in1(R2R), .out(multiplexer_11_out), .sel(en));
  assign jalr_t = aluresult & 32'hfffffffe;  // AND_Gate and_9, 32 bits wide
  and and_10 (and_10_out, id_ex_1_beqout, alu_1_equal);
  and and_11 (and_11_out, id_ex_1_ecallout, not_3_out);
  Multiplexer #(.select(1), .width(32), .disabled("Z"), .enable("false")) multiplexer_12 (
    .in0(R2R), .in1(id_ex_1_imm1out_prime), .out(multiplexer_12_out), .sel(id_ex_1_alusrcout));
  Register #(.width(32), .trigger("rising"), .Select("low")) register_3 (
    .D(multiplexer_11_out), .en(en), .Q(LedData), .clk(CLK));  // open: clr
  not not_4 (not_4_out, alu_1_equal);
  ALU alu_1 (
    .X(R1R), .Y(multiplexer_12_out), .AluOP(id_ex_1_aluopout), .Equal(alu_1_equal), .Result(aluresult),
    .out_6(alu_1_out_6));  // open: Result_2, out_4
  Adder #(.width(32)) adder_5 (.a(EX_PC), .b(32'h4), .out(adder_5_out));  // open: cin, cout
  or or_20 (or_20_out, and_10_out, and_12_out);
  and and_12 (and_12_out, id_ex_1_bneout, not_4_out);
  and and_13 (and_13_out, blt, alu_1_out_6);
  or or_21 (B, and_13_out, or_20_out);
  and and_14 (and_14_out, ~Go, halt);  // AND_Gate
  EX_MEM ex_mem_1 (
    .J(or_19_out), .MEMWRITE(id_ex_1_memwriteout), .MEMTOREG(EX_MemToReg), .REGWRITE(EX_RegWrite),
    .UTYPE(id_ex_1_utypeout), .HALT(and_11_out), .lhu(id_ex_1_lhuout), .ALURESULT(aluresult),
    .WRITEDATA_R2(R2R), .WRITEREG(EX_WriteReg), .PC(EX_PC), .IR(EX_IR), .IMM(adder_5_out),
    .AUIPC_IMM(adder_2_out), .JOUT(MEM_J), .MEMWRITEOUT(MemWrite), .MEMTOREGOUT(ex_mem_1_memtoregout),
    .REGWRITEOUT(MEM_RegWrite), .UTYPEOUT(AUIPC), .HALTOUT(ex_mem_1_haltout), .lhuOUT(ex_mem_1_lhuout),
    .ALURESULTOUT(ex_mem_1_aluresultout), .WRITEDATAOUT_R2(MDin), .WRITEREGOUT(MEM_WriteReg), .PCOUT(M_PC),
    .IROUT(MEM_IR), .IMMOUT(ex_mem_1_immout), .AUPICIMMOUT(ex_mem_1_aupicimmout), .CLK(CLK), .RST(RST),
    .FLUSH(1'b0), .EN(and_14_out));
  Multiplexer #(.select(1), .width(32), .disabled("Z"), .enable("false")) multiplexer_13 (
    .in0(ex_mem_1_aluresultout), .in1(ex_mem_1_immout), .out(multiplexer_13_out), .sel(MEM_J));
  not not_5 (not_5_out, MemWrite);
  Multiplexer #(.select(1), .width(32), .disabled("Z"), .enable("false")) multiplexer_14 (
    .in0(multiplexer_13_out), .in1(ex_mem_1_aupicimmout), .out(MEM_Result), .sel(AUIPC));
  RAM #(.addrWidth(10), .dataWidth(32), .bus("separate"), .Select("high")) ram_1 (
    .addr(ex_mem_1_aluresultout[11:2]), .din(MDin), .data(ram_1_data), .str(MemWrite), .clk(CLK),
    .ld(not_5_out));  // open: sel, clr
  MEM_WB mem_wb_1 (
    .J(MEM_J), .MEMTOREG(ex_mem_1_memtoregout), .REGWRITE(MEM_RegWrite), .UTYPE(AUIPC),
    .HALT(ex_mem_1_haltout), .ALURESULT(ex_mem_1_aluresultout), .MEMDATA(ram_1_data), .lhu(ex_mem_1_lhuout),
    .WRITEREG(MEM_WriteReg), .PC(M_PC), .IR(MEM_IR), .IMM(ex_mem_1_immout), .AUIPCIMM(ex_mem_1_aupicimmout),
    .JOUT(mem_wb_1_jout), .MEMTOREGOUT(mem_wb_1_memtoregout), .REGWRITEOUT(RegWrite),
    .UTYPEOUT(mem_wb_1_utypeout), .HALTOUT(halt), .ALURESULTOUT(mem_wb_1_aluresultout),
    .MEMDATAOUT(mem_wb_1_memdataout), .lhuout(mem_wb_1_lhuout), .WRITEREGOUT(W_num), .PCOUT(WB_PC),
    .IROUT(WB_IR), .IMMOUT(mem_wb_1_immout), .AUIPCIMMOUT(mem_wb_1_auipcimmout), .CLK(CLK), .RST(RST),
    .FLUSH(1'b0), .EN(and_14_out));
  Multiplexer #(.select(1), .width(32), .disabled("Z"), .enable("false")) multiplexer_15 (
    .in0(mem_wb_1_aluresultout), .in1(mem_wb_1_memdataout), .out(multiplexer_15_out),
    .sel(mem_wb_1_memtoregout));
  Multiplexer #(.select(1), .width(32), .disabled("Z"), .enable("false")) multiplexer_16 (
    .in0(multiplexer_15_out), .in1(mem_wb_1_auipcimmout), .out(multiplexer_16_out), .sel(mem_wb_1_utypeout));
  Multiplexer #(.select(1), .width(16), .disabled("Z"), .enable("false")) multiplexer_17 (
    .in0(mem_wb_1_memdataout[15:0]), .in1(mem_wb_1_memdataout[31:16]), .out(multiplexer_17_out),
    .sel(mem_wb_1_aluresultout[1]));
  Multiplexer #(.select(1), .width(32), .disabled("Z"), .enable("false")) multiplexer_18 (
    .in0(multiplexer_16_out), .in1(mem_wb_1_immout), .out(multiplexer_18_out), .sel(mem_wb_1_jout));
  assign bit_extender_6_out = {{16{1'b0}}, multiplexer_17_out};  // Bit_Extender bit_extender_6
  Multiplexer #(.select(1), .width(32), .disabled("Z"), .enable("false")) multiplexer_19 (
    .in0(multiplexer_18_out), .in1(bit_extender_6_out), .out(RDin), .sel(mem_wb_1_lhuout));

  // Other names for the same wires on the sheet: writereg[4:0] = ID_IR[11:7]; MEM_PC[31:0] = M_PC

  // Notes on the sheet:
  //   中断源
  //   时空图监测，可删除
  //   中断等待指示
  //   单级中断测试信号模拟器
  //   识别中断类型找地址
  //   数码管输出
  //   Reset 
  //   Reset 
  //   Reset 
  //   中断响应阶段
  //   中断使能位(用于开关中断)
  //   清除中断
  //   判断中断使能
  //   控制位
  //   中断响应
  //   流水调试日志用
  //   暂停节拍，不能为0
  //   保存断点
  //   戳工具置1进入计数暂停模式，ctrl+k时钟自动运行到对应节拍暂停
  //   ctrl+k关闭时钟连续运行，将控制位置零，进入单步调试模式调试
  //   可计数暂停的时钟源
  //   取指
  //   为方便自动评测，需要输出流水线各段保存的PC值，注意是PC不是PC+4，另外ID段寄存器写入信息，Mem段内存写入信息也要输出
  //   contents of rom_1 (hex, n*v repeats v):
  //   7d000113 100413 1f41993 41f9d993 433 c00913 800b13 140413 f47413 800293 100313 499993 89e9b3 1300533
  //   2200893 73 406282b3 fe0294e3 140413 f00f93 1f47433 1c41413 800293 100313 49d993 89e9b3 1300533
  //   2200893 73 406282b3 fe0294e3 1c45413 406b0b33 b0463 f95ff06f 2b3 fff2c293 1029293 fff2e293 500533
  //   2200893 73 f5dff06f 1112023 410113 a12023 410113 812023 410113 1312023 410113 1412023 410113 1512023
  //   410113 1612023 410113 100b13 300a13 100a93 1600433 441413 14469b3 1300533 2200893 73 fe0416e3
  //   415a0a33 fe0a10e3 ffc10113 12b03 ffc10113 12a83 ffc10113 12a03 ffc10113 12983 ffc10113 12403
  //   ffc10113 12503 ffc10113 12883 200073 1112023 410113 a12023 410113 812023 410113 1312023 410113
  //   1412023 410113 1512023 410113 1612023 410113 200b13 300a13 100a93 1600433 441413 14469b3 1300533
  //   2200893 73 fe0416e3 415a0a33 fe0a10e3 ffc10113 12b03 ffc10113 12a83 ffc10113 12a03 ffc10113 12983
  //   ffc10113 12403 ffc10113 12503 ffc10113 12883 200073 1112023 410113 a12023 410113 812023 410113
  //   1312023 410113 1412023 410113 1512023 410113 1612023 410113 300b13 300a13 100a93 1600433 441413
  //   14469b3 1300533 2200893 73 fe0416e3 415a0a33 fe0a10e3 ffc10113 12b03 ffc10113 12a83 ffc10113 12a03
  //   ffc10113 12983 ffc10113 12403 ffc10113 12503 ffc10113 12883 200073
  //   指令探针
  //   指令存储器
  //   指令字
  //   JAL
  //   blt
  //   JALR
  //   URET
  //   lhu
  //   I型
  //   S型
  //   U型
  //   B型Imm
  //   J型Imm
  //   译码
  //   Beq
  //   Bne
  //   MemToReg
  //   MemWrite
  //   AluOP
  //   AluSrcB
  //   RegWrite
  //   S_Type
  //   auipc
  //   beq/bne/blt
  //   jal
  //   jalr
  //   执行
  //   PC+4
  //   访存
  //   数据存储器
  //   写回
endmodule

module \动态分支预测  (
  output RegWrite,
  output MemWrite,
  output [31:0] IF_PC,
  output [31:0] ID_PC,
  output [31:0] EX_PC,
  output [31:0] M_PC,
  output [31:0] WB_PC,
  output [31:0] RDin,
  output [31:0] MDin,
  output [31:0] LedData
);

  wire alu_1_equal, alu_1_out_6, and_1_out, and_2_out, and_3_out, and_6_out, and_7_out, and_8_out, and_9_out,
       and_10_out, AUIPC, B, blt, Branch, btb_1_predictjump, CLK, clock_1_out, comparator_1_eq,
       comparator_1_lt, comparator_2_eq, d_ff_1_q, ecall, en, EX_BEQ, EX_BNE, EX_BRANCH, ex_mem_1_haltout,
       ex_mem_1_lhuout, ex_mem_1_memtoregout, EX_MemToReg, EX_RegWrite, Go, halt, id_ex_1_alusrcout,
       id_ex_1_ecallout, id_ex_1_lhuout, id_ex_1_memwriteout, id_ex_1_utypeout, if_id_1_predictout, IR1, IR2,
       IR3, JAL, JALR, loaduse, MEM_J, MEM_RegWrite, mem_wb_1_jout, mem_wb_1_lhuout, mem_wb_1_memtoregout,
       mem_wb_1_utypeout, nand_1_out, not_1_out, not_2_out, not_3_out, not_4_out, not_5_out, not_6_out,
       or_1_out, or_2_out, or_3_out, or_5_out, or_7_out, or_8_out, PERROR, PREDICT, RST, S_Type, W1, W2, W3,
       \单周期硬布线控制器_1_alu_src , \单周期硬布线控制器_1_beq , \单周期硬布线控制器_1_blt , \单周期硬布线控制器_1_bne , \单周期硬布线控制器_1_jal ,
       \单周期硬布线控制器_1_jalr , \单周期硬布线控制器_1_lhu , \单周期硬布线控制器_1_memtoreg , \单周期硬布线控制器_1_memwrite ,
       \单周期硬布线控制器_1_regwrite , \单周期硬布线控制器_1_u_type , \单周期硬布线控制器_1_uret ;
  wire [1:0] EX_R1F, EX_R2F, R1Foward, R2Foward;
  wire [3:0] id_ex_1_aluopout, \单周期硬布线控制器_1_alu_op ;
  wire [4:0] EX_WriteReg, MEM_WriteReg, multiplexer_6_out, multiplexer_7_out, W_num;
  wire [12:0] CNT_num;
  wire [15:0] \LoadUse次数 , multiplexer_16_out, \PERROR次数 , \总周期数 , \插入气泡数 , \无条件分支数 , \条件分支成功数 ;
  wire [31:0] adder_1_out, adder_2_out, adder_3_out, adder_4_out, adder_5_out, adder_6_out, aluresult,
       and_5_out, bit_extender_1_out, bit_extender_2_out, bit_extender_3_out, bit_extender_4_out,
       bit_extender_5_out, bit_extender_6_out, BRANCHADDR, btb_1_predictaddr, EX_IR, ex_mem_1_aluresultout,
       ex_mem_1_aupicimmout, ex_mem_1_immout, EX_R1, EX_R2, id_ex_1_imm1out_prime, id_ex_1_imm2out_prime,
       id_ex_1_imm3out_prime, id_ex_1_imm4out_prime, ID_IR, IF_IR, MEM_IR, MEM_Result, mem_wb_1_aluresultout,
       mem_wb_1_auipcimmout, mem_wb_1_immout, mem_wb_1_memdataout, multiplexer_1_out, multiplexer_2_out,
       multiplexer_3_out, multiplexer_8_out, multiplexer_9_out, multiplexer_10_out, multiplexer_11_out,
       multiplexer_13_out, multiplexer_15_out, multiplexer_17_out, multiplexer_18_out, R1R, R2R, ram_1_data,
       \regfile气泡_重定向_1_r1 , \regfile气泡_重定向_1_r2 , shifter_1_out, shifter_2_out, shifter_3_out, WB_IR;

  Button \u_总复位  (.out(RST));
  Button _1 (.out(IR1));
  Button _2 (.out(IR2));
  Button _3 (.out(IR3));
  // Probe on \总周期数 
  // Probe on \总周期数 
  Button \u_继续运行  (.out(Go));
  LED #(.active("true")) led_1 (.in(W1));
  LED #(.active("true")) led_2 (.in(W2));
  LED #(.active("true")) led_3 (.in(W3));
  Hex_Digit_Display hex_digit_display_1 (.value(LedData[31:28]));  // open: dp
  // Probe on IF_PC[19:0]
  // RiscV_Probe riscv_probe_1: pin names not known; wires that end beside it: IF_IR
  Hex_Digit_Display hex_digit_display_2 (.value(LedData[23:20]));  // open: dp
  Hex_Digit_Display hex_digit_display_3 (.value(LedData[27:24]));  // open: dp
  // Probe on ID_PC[19:0]
  // RiscV_Probe riscv_probe_2: pin names not known; wires that end beside it: ID_IR
  not not_1 (not_1_out, halt);
  Multiplexer #(.select(1), .width(32), .disabled("Z"), .enable("false")) multiplexer_1 (
    .in0(multiplexer_3_out), .in1(multiplexer_2_out), .out(multiplexer_1_out), .sel(PERROR));
  Multiplexer #(.select(1), .width(32), .disabled("Z"), .enable("false")) multiplexer_2 (
    .in0(adder_1_out), .in1(BRANCHADDR), .out(multiplexer_2_out), .sel(Branch));
  Adder #(.width(32)) adder_1 (.a(EX_PC), .b(32'h4), .out(adder_1_out));  // open: cin, cout
  Hex_Digit_Display hex_digit_display_4 (.value(LedData[15:12]));  // open: dp
  Hex_Digit_Display hex_digit_display_5 (.value(LedData[19:16]));  // open: dp
  or or_1 (or_1_out, Go, not_1_out);
  Counter #(.width(16), .max('hffff), .ongoal("wrap"), .trigger("rising"), .behavior("new")) counter_1 (
    .count(or_1_out), .Q(\总周期数 ), .clk(CLK), .clr(RST));  // open: load, D, carry, preset, down
  and and_1 (and_1_out, ~loaduse, or_2_out);  // AND_Gate
  or or_2 (or_2_out, Go, not_2_out);
  not not_2 (not_2_out, halt);
  Hex_Digit_Display hex_digit_display_6 (.value(LedData[7:4]));  // open: dp
  Hex_Digit_Display hex_digit_display_7 (.value(LedData[11:8]));  // open: dp
  // Probe on EX_PC[19:0]
  // RiscV_Probe riscv_probe_3: pin names not known; wires that end beside it: EX_IR
  \重定向冲突检测逻辑  \u_重定向冲突检测逻辑_1  (
    .EX_REGWRITE(EX_RegWrite), .MEM_REGWRITE(MEM_RegWrite), .MEM_WRITEREG(MEM_WriteReg),
    .EX_WRITEREG(EX_WriteReg), .EX_MEMTOREG(EX_MemToReg), .ID_IR(ID_IR), .R1FOWARD(R1Foward),
    .LOADUSE(loaduse), .R2FOWARD(R2Foward));
  Register #(.width(32), .trigger("rising"), .Select("low")) PC (
    .D(multiplexer_1_out), .en(and_1_out), .Q(IF_PC), .clk(CLK), .clr(RST));
  Multiplexer #(.select(1), .width(32), .disabled("Z"), .enable("false")) multiplexer_3 (
    .in0(adder_2_out), .in1(btb_1_predictaddr), .out(multiplexer_3_out), .sel(btb_1_predictjump));
  BTB btb_1 (
    .CLK(CLK), .PC(IF_PC), .EX_PC(EX_PC), .EX_BRANCHTAKEN(Branch), .EX_BRANCH(EX_BRANCH),
    .EX_BRANCHADDR(BRANCHADDR), .PREDICTJUMP(btb_1_predictjump), .PREDICTADDR(btb_1_predictaddr));
  Multiplexer #(.select(2), .width(32), .disabled("Z"), .enable("false")) multiplexer_4 (
    .in0(EX_R1), .in1(RDin), .in2(MEM_Result), .in3(MEM_Result), .out(R1R), .sel(EX_R1F));
  Multiplexer #(.select(2), .width(32), .disabled("Z"), .enable("false")) multiplexer_5 (
    .in0(EX_R2), .in1(RDin), .in2(MEM_Result), .in3(MEM_Result), .out(R2R), .sel(EX_R2F));
  Hex_Digit_Display hex_digit_display_8 (.value(LedData[3:0]));  // open: dp
  Adder #(.width(32)) adder_2 (.a(IF_PC), .b(32'h4), .out(adder_2_out));  // open: cin, cout
  // Probe on \总周期数 
  // Probe on M_PC[19:0]
  // RiscV_Probe riscv_probe_4: pin names not known; wires that end beside it: MEM_IR
  // Probe on \总周期数 
  // Probe on \无条件分支数 
  // Probe on \条件分支成功数 
  // Probe on \插入气泡数 
  // Probe on \LoadUse次数 
  ROM #(.addrWidth(10), .dataWidth(32), .Select("high")) rom_1 (.addr(IF_PC[11:2]), .data(IF_IR));
  // Probe on IF_PC[11:0]
  // Probe on WB_PC[19:0]
  // RiscV_Probe riscv_probe_5: pin names not known; wires that end beside it: WB_IR
  IF_ID if_id_1 (
    .IR(IF_IR), .PC(IF_PC), .PREDICT(btb_1_predictjump), .IROUT(ID_IR), .PCOUT(ID_PC),
    .PREDICTOUT(if_id_1_predictout), .CLK(CLK), .RST(RST), .FLUSH(PERROR), .EN(or_3_out));
  or or_3 (or_3_out, and_2_out, loaduse);
  and and_2 (and_2_out, ~Go, halt);  // AND_Gate
  or or_4 (Branch, B, JAL, JALR);
  // Probe on ID_PC[11:0]
  // RiscV_Probe riscv_probe_6: pin names not known; wires that end beside it: CLK, RST, ID_IR
  // Probe on M_PC[11:0]
  // Probe on EX_PC[11:0]
  D_Flip_Flop #(.trigger("high"), .Pre_Clr_Positions("LEGACY"), .NegatePresetClear("false"), .enable("true"), .NewFFLayout("false")) d_ff_1 (.Q(d_ff_1_q));  // open: clk, D, Qn, preset, en, reset
  // Probe on 13'hc
  // Probe on WB_PC[11:0]
  Comparator #(.width(13), .mode("twosComplement")) comparator_1 (
    .a(CNT_num), .b(13'hc), .eq(comparator_1_eq), .lt(comparator_1_lt));  // open: gt
  Clock #(.highDuration(1), .lowDuration(1)) clock_1 (.out(clock_1_out));
  Multiplexer #(.select(1), .width(5), .disabled("Z"), .enable("false")) multiplexer_6 (
    .in0(ID_IR[19:15]), .in1(5'b10001), .out(multiplexer_6_out), .sel(ecall));
  nand nand_1 (nand_1_out, d_ff_1_q, comparator_1_eq);
  Counter #(.width(13), .max('h1fff), .ongoal("stay"), .trigger("rising"), .behavior("old")) counter_2 (
    .count(comparator_1_lt), .Q(CNT_num), .clk(clock_1_out));  // open: load, D, carry, clr, preset
  Counter #(.width(16), .max('hffff), .ongoal("wrap"), .trigger("rising"), .behavior("new")) counter_3 (
    .count(loaduse), .Q(\LoadUse次数 ), .clk(CLK), .clr(RST));  // open: load, D, carry, preset, down
  \单周期硬布线控制器  \u_单周期硬布线控制器_1  (
    .Funct({ID_IR[30], ID_IR[25], ID_IR[14:12]}), .OP(ID_IR[6:2]), .ALU_OP(\单周期硬布线控制器_1_alu_op ),
    .MemToReg(\单周期硬布线控制器_1_memtoreg ), .MemWrite(\单周期硬布线控制器_1_memwrite ), .ALU_SRC(\单周期硬布线控制器_1_alu_src ),
    .RegWrite(\单周期硬布线控制器_1_regwrite ), .ecall(ecall), .S_type(S_Type), .Jalr(\单周期硬布线控制器_1_jalr ),
    .Beq(\单周期硬布线控制器_1_beq ), .JAL(\单周期硬布线控制器_1_jal ), .Bne(\单周期硬布线控制器_1_bne ), .in_3(ID_IR[21]),
    .uret(\单周期硬布线控制器_1_uret ), .blt(\单周期硬布线控制器_1_blt ), .U_type(\单周期硬布线控制器_1_u_type ), .lhu(\单周期硬布线控制器_1_lhu ));  // open: csrrsi, csrrci
  Multiplexer #(.select(1), .width(5), .disabled("Z"), .enable("false")) multiplexer_7 (
    .in0(ID_IR[24:20]), .in1(5'b01010), .out(multiplexer_7_out), .sel(ecall));
  assign bit_extender_1_out = {{20{ID_IR[31]}}, ID_IR[31:20]};  // Bit_Extender bit_extender_1
  assign bit_extender_2_out = {{20{ID_IR[31]}}, {ID_IR[31:25], ID_IR[11:7]}};  // Bit_Extender bit_extender_2
  assign bit_extender_3_out = {{12{ID_IR[31]}}, ID_IR[31:12]};  // Bit_Extender bit_extender_3
  assign bit_extender_4_out = {{20{ID_IR[31]}}, {ID_IR[31], ID_IR[7], ID_IR[30:25], ID_IR[11:8]}};  // Bit_Extender bit_extender_4
  assign bit_extender_5_out = {{12{ID_IR[31]}}, {ID_IR[31], ID_IR[19:12], ID_IR[20], ID_IR[30:21]}};  // Bit_Extender bit_extender_5
  xor xor_1 (PERROR, Branch, PREDICT);
  Multiplexer #(.select(1), .width(32), .disabled("Z"), .enable("false")) multiplexer_8 (
    .in0(bit_extender_1_out), .in1(bit_extender_2_out), .out(multiplexer_8_out), .sel(S_Type));
  Shifter #(.width(32), .shift("ll")) shifter_1 (.in(bit_extender_3_out), .\dist (5'b01100), .out(shifter_1_out));
  Shifter #(.width(32), .shift("ll")) shifter_2 (.in(bit_extender_4_out), .\dist (5'b00001), .out(shifter_2_out));
  Shifter #(.width(32), .shift("ll")) shifter_3 (.in(bit_extender_5_out), .\dist (5'b00001), .out(shifter_3_out));
  assign CLK = nand_1_out ? clock_1_out : 1'bz;  // Controlled_Buffer controlled_buffer_1
  Pull_Resistor #(.pull(1)) pull_resistor_1 (.node(CLK));
  \regfile气泡_重定向  \regfile气泡_重定向_1  (
    .Din(RDin), .Clk(CLK), .R1(\regfile气泡_重定向_1_r1 ), .R2(\regfile气泡_重定向_1_r2 ), .WE(RegWrite),
    .W_num(W_num), .R1_num(multiplexer_6_out), .R2_num(multiplexer_7_out));
  Counter #(.width(16), .max('hffff), .ongoal("wrap"), .trigger("rising"), .behavior("new")) counter_4 (
    .count(PERROR), .Q(\PERROR次数 ), .clk(CLK));  // open: load, D, carry, clr, preset, down
  // Probe on \PERROR次数 
  or or_5 (or_5_out, PERROR, loaduse);
  or or_6 (EX_BRANCH, EX_BEQ, EX_BNE, JAL, JALR);
  ID_EX id_ex_1 (
    .CLK(CLK), .RST(RST), .JAL(\单周期硬布线控制器_1_jal ), .JALOUT(JAL), .JALR(\单周期硬布线控制器_1_jalr ), .JALROUT(JALR),
    .URET(\单周期硬布线控制器_1_uret ), .beq(\单周期硬布线控制器_1_beq ), .BEQOUT(EX_BEQ), .BNE(\单周期硬布线控制器_1_bne ),
    .BNEOUT(EX_BNE), .MEMTOREG(\单周期硬布线控制器_1_memtoreg ), .MEMTOREGOUT(EX_MemToReg),
    .MEMWRITE(\单周期硬布线控制器_1_memwrite ), .MEMWRITEOUT(id_ex_1_memwriteout), .ALUOP(\单周期硬布线控制器_1_alu_op ),
    .ALUOPOUT(id_ex_1_aluopout), .ALUSRC(\单周期硬布线控制器_1_alu_src ), .ALUSRCOUT(id_ex_1_alusrcout),
    .REGWRITE(\单周期硬布线控制器_1_regwrite ), .REGWRITEOUT(EX_RegWrite), .U_type(\单周期硬布线控制器_1_u_type ),
    .UTYPEOUT(id_ex_1_utypeout), .BLT(\单周期硬布线控制器_1_blt ), .BLTOUT(blt), .ECALL(ecall),
    .ECALLOUT(id_ex_1_ecallout), .lhu(\单周期硬布线控制器_1_lhu ), .lhuOUT(id_ex_1_lhuout), .R1F(R1Foward),
    .R1FOUT(EX_R1F), .R1(\regfile气泡_重定向_1_r1 ), .R1OUT(EX_R1), .R2(\regfile气泡_重定向_1_r2 ),
    .R2OUT_prime(EX_R2), .R2F(R2Foward), .R2FOUT(EX_R2F), .WRITEREG(ID_IR[11:7]),
    .WRITEREGOUT_prime(EX_WriteReg), .PC(ID_PC), .PCOUT_prime(EX_PC), .IR(ID_IR), .IROUT_prime(EX_IR),
    .IMM1(multiplexer_8_out), .IMM1OUT_prime(id_ex_1_imm1out_prime), .IMM2(shifter_2_out),
    .IMM2OUT_prime(id_ex_1_imm2out_prime), .IMM3(shifter_3_out), .IMM3OUT_prime(id_ex_1_imm3out_prime),
    .IMM4(shifter_1_out), .IMM4OUT_prime(id_ex_1_imm4out_prime), .PREDICT(if_id_1_predictout),
    .PREDICTOUT(PREDICT), .EN(and_3_out), .FLUSH(or_5_out));  // open: URETOUT
  and and_3 (and_3_out, ~Go, halt);  // AND_Gate
  or or_7 (or_7_out, JALR, JAL);
  and and_4 (en, id_ex_1_ecallout, comparator_2_eq);
  Comparator #(.width(32), .mode("twosComplement")) comparator_2 (
    .a(R1R), .b(32'h22), .eq(comparator_2_eq));  // open: gt, lt
  Adder #(.width(32)) adder_3 (.a(id_ex_1_imm4out_prime), .b(EX_PC), .out(adder_3_out));  // open: cin, cout
  Counter #(.width(16), .max('hffff), .ongoal("wrap"), .trigger("rising"), .behavior("new")) counter_5 (
    .count(or_7_out), .Q(\无条件分支数 ), .clk(CLK));  // open: load, D, carry, clr, preset, down
  not not_3 (not_3_out, comparator_2_eq);
  Multiplexer #(.select(1), .width(32), .disabled("Z"), .enable("false")) multiplexer_9 (
    .in0({32{1'b0}}), .in1(R2R), .out(multiplexer_9_out), .sel(en));
  Adder #(.width(32)) adder_4 (.a(EX_PC), .b(id_ex_1_imm2out_prime), .out(adder_4_out));  // open: cin, cout
  Adder #(.width(32)) adder_5 (.a(id_ex_1_imm3out_prime), .b(EX_PC), .out(adder_5_out));  // open: cin, cout
  assign and_5_out = aluresult & 32'hfffffffe;  // AND_Gate and_5, 32 bits wide
  and and_6 (and_6_out, id_ex_1_ecallout, not_3_out);
  Multiplexer #(.select(1), .width(32), .disabled("Z"), .enable("false")) multiplexer_10 (
    .in0(R2R), .in1(id_ex_1_imm1out_prime), .out(multiplexer_10_out), .sel(id_ex_1_alusrcout));
  Register #(.width(32), .trigger("rising"), .Select("low")) register_1 (
    .D(multiplexer_9_out), .en(en), .Q(LedData), .clk(CLK));  // open: clr
  and and_7 (and_7_out, EX_BEQ, alu_1_equal);
  not not_4 (not_4_out, alu_1_equal);
  ALU alu_1 (
    .X(R1R), .Y(multiplexer_10_out), .AluOP(id_ex_1_aluopout), .Equal(alu_1_equal), .Result(aluresult),
    .out_6(alu_1_out_6));  // open: Result_2, out_4
  Adder #(.width(32)) adder_6 (.a(EX_PC), .b(32'h4), .out(adder_6_out));  // open: cin, cout
  Multiplexer #(.select(1), .width(32), .disabled("Z"), .enable("false")) multiplexer_11 (
    .in0(adder_5_out), .in1(and_5_out), .out(multiplexer_11_out), .sel(JALR));
  or or_8 (or_8_out, and_7_out, and_8_out);
  and and_8 (and_8_out, EX_BNE, not_4_out);
  not not_5 (not_5_out, B);
  Multiplexer #(.select(1), .width(32), .disabled("Z"), .enable("false")) multiplexer_12 (
    .in0(adder_4_out), .in1(multiplexer_11_out), .out(BRANCHADDR), .sel(not_5_out));
  Counter #(.width(16), .max('hffff), .ongoal("wrap"), .trigger("rising"), .behavior("new")) counter_6 (
    .count(B), .Q(\条件分支成功数 ), .clk(CLK), .clr(RST));  // open: load, D, carry, preset, down
  and and_9 (and_9_out, blt, alu_1_out_6);
  or or_9 (B, and_9_out, or_8_out);
  and and_10 (and_10_out, ~Go, halt);  // AND_Gate
  EX_MEM ex_mem_1 (
    .J(or_7_out), .MEMWRITE(id_ex_1_memwriteout), .MEMTOREG(EX_MemToReg), .REGWRITE(EX_RegWrite),
    .UTYPE(id_ex_1_utypeout), .HALT(and_6_out), .lhu(id_ex_1_lhuout), .ALURESULT(aluresult),
    .WRITEDATA_R2(R2R), .WRITEREG(EX_WriteReg), .PC(EX_PC), .IR(EX_IR), .IMM(adder_6_out),
    .AUIPC_IMM(adder_3_out), .JOUT(MEM_J), .MEMWRITEOUT(MemWrite), .MEMTOREGOUT(ex_mem_1_memtoregout),
    .REGWRITEOUT(MEM_RegWrite), .UTYPEOUT(AUIPC), .HALTOUT(ex_mem_1_haltout), .lhuOUT(ex_mem_1_lhuout),
    .ALURESULTOUT(ex_mem_1_aluresultout), .WRITEDATAOUT_R2(MDin), .WRITEREGOUT(MEM_WriteReg), .PCOUT(M_PC),
    .IROUT(MEM_IR), .IMMOUT(ex_mem_1_immout), .AUPICIMMOUT(ex_mem_1_aupicimmout), .CLK(CLK), .RST(RST),
    .FLUSH(1'b0), .EN(and_10_out));
  Multiplexer #(.select(1), .width(32), .disabled("Z"), .enable("false")) multiplexer_13 (
    .in0(ex_mem_1_aluresultout), .in1(ex_mem_1_immout), .out(multiplexer_13_out), .sel(MEM_J));
  not not_6 (not_6_out, MemWrite);
  Multiplexer #(.select(1), .width(32), .disabled("Z"), .enable("false")) multiplexer_14 (
    .in0(multiplexer_13_out), .in1(ex_mem_1_aupicimmout), .out(MEM_Result), .sel(AUIPC));
  RAM #(.addrWidth(10), .dataWidth(32), .bus("separate"), .Select("high")) ram_1 (
    .addr(ex_mem_1_aluresultout[11:2]), .din(MDin), .data(ram_1_data), .str(MemWrite), .clk(CLK),
    .ld(not_6_out));  // open: sel, clr
  MEM_WB mem_wb_1 (
    .J(MEM_J), .MEMTOREG(ex_mem_1_memtoregout), .REGWRITE(MEM_RegWrite), .UTYPE(AUIPC),
    .HALT(ex_mem_1_haltout), .ALURESULT(ex_mem_1_aluresultout), .MEMDATA(ram_1_data), .lhu(ex_mem_1_lhuout),
    .WRITEREG(MEM_WriteReg), .PC(M_PC), .IR(MEM_IR), .IMM(ex_mem_1_immout), .AUIPCIMM(ex_mem_1_aupicimmout),
    .JOUT(mem_wb_1_jout), .MEMTOREGOUT(mem_wb_1_memtoregout), .REGWRITEOUT(RegWrite),
    .UTYPEOUT(mem_wb_1_utypeout), .HALTOUT(halt), .ALURESULTOUT(mem_wb_1_aluresultout),
    .MEMDATAOUT(mem_wb_1_memdataout), .lhuout(mem_wb_1_lhuout), .WRITEREGOUT(W_num), .PCOUT(WB_PC),
    .IROUT(WB_IR), .IMMOUT(mem_wb_1_immout), .AUIPCIMMOUT(mem_wb_1_auipcimmout), .CLK(CLK), .RST(RST),
    .FLUSH(1'b0), .EN(and_10_out));
  Multiplexer #(.select(1), .width(32), .disabled("Z"), .enable("false")) multiplexer_15 (
    .in0(mem_wb_1_aluresultout), .in1(mem_wb_1_memdataout), .out(multiplexer_15_out),
    .sel(mem_wb_1_memtoregout));
  Multiplexer #(.select(1), .width(16), .disabled("Z"), .enable("false")) multiplexer_16 (
    .in0(mem_wb_1_memdataout[15:0]), .in1(mem_wb_1_memdataout[31:16]), .out(multiplexer_16_out),
    .sel(mem_wb_1_aluresultout[1]));
  Multiplexer #(.select(1), .width(32), .disabled("Z"), .enable("false")) multiplexer_17 (
    .in0(multiplexer_15_out), .in1(mem_wb_1_auipcimmout), .out(multiplexer_17_out), .sel(mem_wb_1_utypeout));
  Multiplexer #(.select(1), .width(32), .disabled("Z"), .enable("false")) multiplexer_18 (
    .in0(multiplexer_17_out), .in1(mem_wb_1_immout), .out(multiplexer_18_out), .sel(mem_wb_1_jout));
  assign bit_extender_6_out = {{16{1'b0}}, multiplexer_16_out};  // Bit_Extender bit_extender_6
  Multiplexer #(.select(1), .width(32), .disabled("Z"), .enable("false")) multiplexer_19 (
    .in0(multiplexer_18_out), .in1(bit_extender_6_out), .out(RDin), .sel(mem_wb_1_lhuout));

  // Other names for the same wires on the sheet: writereg[4:0] = ID_IR[11:7]; MEM_PC[31:0] = M_PC

  // Notes on the sheet:
  //   中断源
  //   时空图监测，可删除
  //   中断等待指示
  //   数码管输出
  //   取指
  //   contents of rom_1 (hex, n*v repeats v):
  //   100493 100006f 100493 200913 300993 100006f 100493 200913 300993 100006f 100493 200913 300993
  //   100006f 100493 200913 300993 414000ef 100413 100493 1f49493 900533 2200893 73 24d493 48463 fedff06f
  //   900533 2200893 73 100493 249493 900533 2200893 73 48463 fedff06f 100493 1f49493 900533 2200893 73
  //   4034d493 900533 2200893 73 4044d493 900533 2200893 73 4044d493 900533 2200893 73 4044d493 900533
  //   2200893 73 4044d493 900533 2200893 73 4044d493 900533 2200893 73 4044d493 900533 2200893 73 4044d493
  //   900533 2200893 73 100413 1f41993 41f9d993 433 c00913 300b13 140413 f47413 800293 100313 499993
  //   89e9b3 1300533 2200893 73 406282b3 fe0294e3 140413 f00f93 1f47433 1c41413 800293 100313 49d993
  //   89e9b3 1300533 2200893 73 406282b3 fe0294e3 1c45413 406b0b33 b0463 f95ff06f 2b3 fff2c293 829293
  //   ff2e293 500533 2200893 73 fff00413 493 84a023 140413 448493 84a023 140413 448493 84a023 140413
  //   448493 84a023 140413 448493 84a023 140413 448493 84a023 140413 448493 84a023 140413 448493 84a023
  //   140413 448493 84a023 140413 448493 84a023 140413 448493 84a023 140413 448493 84a023 140413 448493
  //   84a023 140413 448493 84a023 140413 448493 84a023 140413 448493 84a023 140413 448493 140413 433
  //   3c00493 42983 4aa03 149a2b3 28663 134a023 1442023 ffc48493 fe9412e3 800533 2200893 73 440413 3c00493
  //   fc9416e3 a00893 73 100293 300313 800493 849493 7648493 1449493 900533 2200893 73 800e13 4054d4b3
  //   4064d4b3 900533 2200893 73 fffe0e13 fe0e14e3 a00893 73 13 430497 900533 2200893 73 430497 900533
  //   2200893 73 430497 900533 2200893 73 430497 900533 2200893 73 430497 900533 2200893 73 430497 900533
  //   2200893 73 430497 900533 2200893 73 430497 900533 2200893 73 a00893 73 313 1000e13 8400493 849493
  //   8348493 400913 891913 490913 849493 8248493 849493 8148493 891913 490913 891913 490913 932023
  //   12484b3 430313 fffe0e13 fe0e18e3 2000e13 313 35483 900533 2200893 73 230313 fffe0e13 fe0e14e3 a00893
  //   73 ff100493 900533 2200893 73 148493 fe04c8e3 a00893 73 413 140413 800533 2200893 73 240413 800533
  //   2200893 73 340413 800533 2200893 73 440413 800533 2200893 73 540413 800533 2200893 73 640413 800533
  //   2200893 73 740413 800533 2200893 73 840413 800533 2200893 2200893 73 8067
  //   指令探针
  //   指令存储器
  //   流水调试日志用
  //   控制位
  //   暂停节拍，不能为0
  //   指令字
  //   戳工具置1进入计数暂停模式，ctrl+k时钟自动运行到对应节拍暂停
  //   ctrl+k关闭时钟连续运行，将控制位置零，进入单步调试模式调试
  //   JAL
  //   blt
  //   JALR
  //   URET
  //   lhu
  //   I型
  //   S型
  //   U型
  //   B型Imm
  //   J型Imm
  //   译码
  //   Beq
  //   Bne
  //   MemToReg
  //   MemWrite
  //   AluOP
  //   AluSrcB
  //   RegWrite
  //   S_Type
  //   可计数暂停的时钟源
  //   为方便自动评测，需要输出流水线各段保存的PC值，注意是PC不是PC+4，另外ID段寄存器写入信息，Mem段内存写入信息也要输出
  //   auipc
  //   beq/bne/blt
  //   jal
  //   jalr
  //   执行
  //   PC+4
  //   访存
  //   数据存储器
  //   写回
endmodule

module BTB (
  input  CLK,
  input  [31:0] PC,
  input  [31:0] EX_PC,
  input  EX_BRANCHTAKEN,
  input  EX_BRANCH,
  input  [31:0] EX_BRANCHADDR,
  output PREDICTJUMP,
  output [31:0] PREDICTADDR
);

  wire and_1_out, and_2_out, and_3_out, and_4_out, and_5_out, and_6_out, and_7_out, and_8_out,
       comparator_1_eq, comparator_2_eq, comparator_3_eq, comparator_4_eq, comparator_5_eq, comparator_6_eq,
       comparator_7_eq, comparator_8_eq, comparator_9_eq, comparator_10_eq, comparator_11_eq,
       comparator_12_eq, comparator_13_eq, comparator_14_eq, comparator_15_eq, comparator_16_eq, d_ff_1_q,
       d_ff_2_q, d_ff_3_q, d_ff_4_q, d_ff_5_q, d_ff_6_q, d_ff_7_q, d_ff_8_q, demultiplexer_1_out0,
       demultiplexer_1_out1, demultiplexer_1_out2, demultiplexer_1_out3, demultiplexer_1_out4,
       demultiplexer_1_out5, demultiplexer_1_out6, demultiplexer_1_out7, demultiplexer_2_out0,
       demultiplexer_2_out1, demultiplexer_2_out2, demultiplexer_2_out3, demultiplexer_2_out4,
       demultiplexer_2_out5, demultiplexer_2_out6, demultiplexer_2_out7, EX_HIT, EX_MISS, H0, H1, H2, H3, H4,
       H5, H6, H7, L0, L1, L2, L3, L4, L5, L6, L7, not_1_out, not_2_out, not_3_out, not_4_out, not_5_out,
       not_6_out, not_7_out, not_8_out, not_10_out, or_1_out, or_2_out, or_3_out, or_4_out, or_5_out,
       or_6_out, or_7_out, or_8_out, or_10_out, or_11_out, or_12_out, or_13_out, or_14_out, or_15_out,
       or_16_out, or_17_out, priority_encoder_1_gs, V0, V1, V2, V3, V4, V5, V6, V7, W0, W1, W2, W3, W4, W5,
       W6, W7;
  wire [0:0] controlled_buffer_1_out;
  wire [1:0] multiplexer_1_out, multiplexer_2_out, multiplexer_3_out, multiplexer_4_out, multiplexer_5_out,
       multiplexer_6_out, multiplexer_7_out, multiplexer_8_out, multiplexer_9_out, multiplexer_11_out, P0,
       P1, P2, P3, P4, P5, P6, P7, PNEXT;
  wire [2:0] comparison_1_max_place, comparison_2_max_place, comparison_3_max_place, comparison_4_max_place,
       comparison_5_max_place, comparison_6_max_place, comparison_7_max_place, multiplexer_10_out,
       priority_encoder_1_out, priority_encoder_2_out;
  wire [31:0] comparison_1_max, comparison_2_max, comparison_3_max, comparison_4_max, comparison_5_max,
       comparison_6_max, COUNT0, COUNT1, COUNT2, COUNT3, COUNT4, COUNT5, COUNT6, COUNT7, CUR0, CUR1, CUR2,
       CUR3, CUR4, CUR5, CUR6, CUR7, NEXT0, NEXT1, NEXT2, NEXT3, NEXT4, NEXT5, NEXT6, NEXT7;

  Register #(.width(1), .trigger("rising"), .Select("low")) register_1 (
    .D(1'b1), .en(W0), .Q(V0), .clk(CLK));  // open: clr
  Register #(.width(1), .trigger("rising"), .Select("low")) register_2 (
    .D(1'b1), .en(W1), .Q(V1), .clk(CLK));  // open: clr
  Register #(.width(1), .trigger("rising"), .Select("low")) register_3 (
    .D(1'b1), .en(W2), .Q(V2), .clk(CLK));  // open: clr
  Register #(.width(1), .trigger("rising"), .Select("low")) register_4 (
    .D(1'b1), .en(W3), .Q(V3), .clk(CLK));  // open: clr
  Register #(.width(1), .trigger("rising"), .Select("low")) register_5 (
    .D(1'b1), .en(W4), .Q(V4), .clk(CLK));  // open: clr
  Register #(.width(1), .trigger("rising"), .Select("low")) register_6 (
    .D(1'b1), .en(W5), .Q(V5), .clk(CLK));  // open: clr
  Register #(.width(1), .trigger("rising"), .Select("low")) register_7 (
    .D(1'b1), .en(W6), .Q(V6), .clk(CLK));  // open: clr
  Register #(.width(1), .trigger("rising"), .Select("low")) register_8 (
    .D(1'b1), .en(W7), .Q(V7), .clk(CLK));  // open: clr
  Register #(.width(32), .trigger("rising"), .Select("low")) register_9 (
    .D(EX_PC), .en(W0), .Q(CUR0), .clk(CLK));  // open: clr
  Register #(.width(32), .trigger("rising"), .Select("low")) register_10 (
    .D(EX_PC), .en(W1), .Q(CUR1), .clk(CLK));  // open: clr
  Register #(.width(32), .trigger("rising"), .Select("low")) register_11 (
    .D(EX_PC), .en(W2), .Q(CUR2), .clk(CLK));  // open: clr
  Register #(.width(32), .trigger("rising"), .Select("low")) register_12 (
    .D(EX_PC), .en(W3), .Q(CUR3), .clk(CLK));  // open: clr
  Register #(.width(32), .trigger("rising"), .Select("low")) register_13 (
    .D(EX_PC), .en(W4), .Q(CUR4), .clk(CLK));  // open: clr
  Register #(.width(32), .trigger("rising"), .Select("low")) register_14 (
    .D(EX_PC), .en(W5), .Q(CUR5), .clk(CLK));  // open: clr
  Register #(.width(32), .trigger("rising"), .Select("low")) register_15 (
    .D(EX_PC), .en(W6), .Q(CUR6), .clk(CLK));  // open: clr
  Register #(.width(32), .trigger("rising"), .Select("low")) register_16 (
    .D(EX_PC), .en(W7), .Q(CUR7), .clk(CLK));  // open: clr
  Register #(.width(32), .trigger("rising"), .Select("low")) register_17 (
    .D(EX_BRANCHADDR), .en(W0), .Q(NEXT0), .clk(CLK));  // open: clr
  Register #(.width(32), .trigger("rising"), .Select("low")) register_18 (
    .D(EX_BRANCHADDR), .en(W1), .Q(NEXT1), .clk(CLK));  // open: clr
  Register #(.width(32), .trigger("rising"), .Select("low")) register_19 (
    .D(EX_BRANCHADDR), .en(W2), .Q(NEXT2), .clk(CLK));  // open: clr
  Register #(.width(32), .trigger("rising"), .Select("low")) register_20 (
    .D(EX_BRANCHADDR), .en(W3), .Q(NEXT3), .clk(CLK));  // open: clr
  Register #(.width(32), .trigger("rising"), .Select("low")) register_21 (
    .D(EX_BRANCHADDR), .en(W4), .Q(NEXT4), .clk(CLK));  // open: clr
  Register #(.width(32), .trigger("rising"), .Select("low")) register_22 (
    .D(EX_BRANCHADDR), .en(W5), .Q(NEXT5), .clk(CLK));  // open: clr
  Register #(.width(32), .trigger("rising"), .Select("low")) register_23 (
    .D(EX_BRANCHADDR), .en(W6), .Q(NEXT6), .clk(CLK));  // open: clr
  Register #(.width(32), .trigger("rising"), .Select("low")) register_24 (
    .D(EX_BRANCHADDR), .en(W7), .Q(NEXT7), .clk(CLK));  // open: clr
  Multiplexer #(.select(1), .width(2), .disabled("Z"), .enable("false")) multiplexer_1 (
    .in0(2'b00), .in1(2'b11), .out(multiplexer_1_out), .sel(EX_BRANCHTAKEN));
  and and_1 (and_1_out, H0, EX_BRANCH);
  and and_2 (and_2_out, H1, EX_BRANCH);
  and and_3 (and_3_out, H2, EX_BRANCH);
  and and_4 (and_4_out, H3, EX_BRANCH);
  and and_5 (and_5_out, H4, EX_BRANCH);
  and and_6 (and_6_out, H5, EX_BRANCH);
  and and_7 (and_7_out, H6, EX_BRANCH);
  and and_8 (and_8_out, H7, EX_BRANCH);
  Multiplexer #(.select(1), .width(2), .disabled("Z"), .enable("false")) multiplexer_2 (
    .in0(PNEXT), .in1(multiplexer_1_out), .out(multiplexer_2_out), .sel(W0));
  Multiplexer #(.select(1), .width(2), .disabled("Z"), .enable("false")) multiplexer_3 (
    .in0(PNEXT), .in1(multiplexer_1_out), .out(multiplexer_3_out), .sel(W1));
  Multiplexer #(.select(1), .width(2), .disabled("Z"), .enable("false")) multiplexer_4 (
    .in0(PNEXT), .in1(multiplexer_1_out), .out(multiplexer_4_out), .sel(W2));
  Multiplexer #(.select(1), .width(2), .disabled("Z"), .enable("false")) multiplexer_5 (
    .in0(PNEXT), .in1(multiplexer_1_out), .out(multiplexer_5_out), .sel(W3));
  Multiplexer #(.select(1), .width(2), .disabled("Z"), .enable("false")) multiplexer_6 (
    .in0(PNEXT), .in1(multiplexer_1_out), .out(multiplexer_6_out), .sel(W4));
  Multiplexer #(.select(1), .width(2), .disabled("Z"), .enable("false")) multiplexer_7 (
    .in0(PNEXT), .in1(multiplexer_1_out), .out(multiplexer_7_out), .sel(W5));
  Multiplexer #(.select(1), .width(2), .disabled("Z"), .enable("false")) multiplexer_8 (
    .in0(PNEXT), .in1(multiplexer_1_out), .out(multiplexer_8_out), .sel(W6));
  Multiplexer #(.select(1), .width(2), .disabled("Z"), .enable("false")) multiplexer_9 (
    .in0(PNEXT), .in1(multiplexer_1_out), .out(multiplexer_9_out), .sel(W7));
  Register #(.width(2), .trigger("rising"), .Select("low")) register_25 (
    .D(multiplexer_2_out), .en(and_1_out), .Q(P0), .clk(CLK));  // open: clr
  Register #(.width(2), .trigger("rising"), .Select("low")) register_26 (
    .D(multiplexer_3_out), .en(and_2_out), .Q(P1), .clk(CLK));  // open: clr
  Register #(.width(2), .trigger("rising"), .Select("low")) register_27 (
    .D(multiplexer_4_out), .en(and_3_out), .Q(P2), .clk(CLK));  // open: clr
  Register #(.width(2), .trigger("rising"), .Select("low")) register_28 (
    .D(multiplexer_5_out), .en(and_4_out), .Q(P3), .clk(CLK));  // open: clr
  Register #(.width(2), .trigger("rising"), .Select("low")) register_29 (
    .D(multiplexer_6_out), .en(and_5_out), .Q(P4), .clk(CLK));  // open: clr
  Register #(.width(2), .trigger("rising"), .Select("low")) register_30 (
    .D(multiplexer_7_out), .en(and_6_out), .Q(P5), .clk(CLK));  // open: clr
  Register #(.width(2), .trigger("rising"), .Select("low")) register_31 (
    .D(multiplexer_8_out), .en(and_7_out), .Q(P6), .clk(CLK));  // open: clr
  Register #(.width(2), .trigger("rising"), .Select("low")) register_32 (
    .D(multiplexer_9_out), .en(and_8_out), .Q(P7), .clk(CLK));  // open: clr
  or or_1 (or_1_out, W0, L0);
  or or_2 (or_2_out, W1, L1);
  or or_3 (or_3_out, W2, L2);
  or or_4 (or_4_out, W3, L3);
  or or_5 (or_5_out, W4, L4);
  or or_6 (or_6_out, W5, L5);
  or or_7 (or_7_out, W6, L6);
  or or_8 (or_8_out, W7, L7);
  Counter #(.width(32), .max('hffffffff), .ongoal("wrap"), .trigger("rising"), .behavior("new")) counter_1 (
    .Q(COUNT0), .clk(CLK), .clr(d_ff_1_q));  // open: load, D, count, carry, preset, down
  D_Flip_Flop #(.trigger("rising"), .Pre_Clr_Positions("LEGACY"), .NegatePresetClear("false"), .enable("true"), .NewFFLayout("false")) d_ff_1 (
    .clk(CLK), .D(or_1_out), .Q(d_ff_1_q));  // open: Qn, preset, en, reset
  Counter #(.width(32), .max('hffffffff), .ongoal("wrap"), .trigger("rising"), .behavior("new")) counter_2 (
    .Q(COUNT1), .clk(CLK), .clr(d_ff_2_q));  // open: load, D, count, carry, preset, down
  D_Flip_Flop #(.trigger("rising"), .Pre_Clr_Positions("LEGACY"), .NegatePresetClear("false"), .enable("true"), .NewFFLayout("false")) d_ff_2 (
    .clk(CLK), .D(or_2_out), .Q(d_ff_2_q));  // open: Qn, preset, en, reset
  Counter #(.width(32), .max('hffffffff), .ongoal("wrap"), .trigger("rising"), .behavior("new")) counter_3 (
    .Q(COUNT2), .clk(CLK), .clr(d_ff_3_q));  // open: load, D, count, carry, preset, down
  D_Flip_Flop #(.trigger("rising"), .Pre_Clr_Positions("LEGACY"), .NegatePresetClear("false"), .enable("true"), .NewFFLayout("false")) d_ff_3 (
    .clk(CLK), .D(or_3_out), .Q(d_ff_3_q));  // open: Qn, preset, en, reset
  Counter #(.width(32), .max('hffffffff), .ongoal("wrap"), .trigger("rising"), .behavior("new")) counter_4 (
    .Q(COUNT3), .clk(CLK), .clr(d_ff_4_q));  // open: load, D, count, carry, preset, down
  D_Flip_Flop #(.trigger("rising"), .Pre_Clr_Positions("LEGACY"), .NegatePresetClear("false"), .enable("true"), .NewFFLayout("false")) d_ff_4 (
    .clk(CLK), .D(or_4_out), .Q(d_ff_4_q));  // open: Qn, preset, en, reset
  Counter #(.width(32), .max('hffffffff), .ongoal("wrap"), .trigger("rising"), .behavior("new")) counter_5 (
    .Q(COUNT4), .clk(CLK), .clr(d_ff_5_q));  // open: load, D, count, carry, preset, down
  D_Flip_Flop #(.trigger("rising"), .Pre_Clr_Positions("LEGACY"), .NegatePresetClear("false"), .enable("true"), .NewFFLayout("false")) d_ff_5 (
    .clk(CLK), .D(or_5_out), .Q(d_ff_5_q));  // open: Qn, preset, en, reset
  Counter #(.width(32), .max('hffffffff), .ongoal("wrap"), .trigger("rising"), .behavior("new")) counter_6 (
    .Q(COUNT5), .clk(CLK), .clr(d_ff_6_q));  // open: load, D, count, carry, preset, down
  D_Flip_Flop #(.trigger("rising"), .Pre_Clr_Positions("LEGACY"), .NegatePresetClear("false"), .enable("true"), .NewFFLayout("false")) d_ff_6 (
    .clk(CLK), .D(or_6_out), .Q(d_ff_6_q));  // open: Qn, preset, en, reset
  Counter #(.width(32), .max('hffffffff), .ongoal("wrap"), .trigger("rising"), .behavior("new")) counter_7 (
    .Q(COUNT6), .clk(CLK), .clr(d_ff_7_q));  // open: load, D, count, carry, preset, down
  D_Flip_Flop #(.trigger("rising"), .Pre_Clr_Positions("LEGACY"), .NegatePresetClear("false"), .enable("true"), .NewFFLayout("false")) d_ff_7 (
    .clk(CLK), .D(or_7_out), .Q(d_ff_7_q));  // open: Qn, preset, en, reset
  Counter #(.width(32), .max('hffffffff), .ongoal("wrap"), .trigger("rising"), .behavior("new")) counter_8 (
    .Q(COUNT7), .clk(CLK), .clr(d_ff_8_q));  // open: load, D, count, carry, preset, down
  D_Flip_Flop #(.trigger("rising"), .Pre_Clr_Positions("LEGACY"), .NegatePresetClear("false"), .enable("true"), .NewFFLayout("false")) d_ff_8 (
    .clk(CLK), .D(or_8_out), .Q(d_ff_8_q));  // open: Qn, preset, en, reset
  Comparator #(.width(32), .mode("twosComplement")) comparator_1 (
    .a(CUR0), .b(EX_PC), .eq(comparator_1_eq));  // open: gt, lt
  Comparator #(.width(32), .mode("twosComplement")) comparator_2 (
    .a(CUR1), .b(EX_PC), .eq(comparator_2_eq));  // open: gt, lt
  Comparator #(.width(32), .mode("twosComplement")) comparator_3 (
    .a(CUR2), .b(EX_PC), .eq(comparator_3_eq));  // open: gt, lt
  Comparator #(.width(32), .mode("twosComplement")) comparator_4 (
    .a(CUR3), .b(EX_PC), .eq(comparator_4_eq));  // open: gt, lt
  Comparator #(.width(32), .mode("twosComplement")) comparator_5 (
    .a(CUR4), .b(EX_PC), .eq(comparator_5_eq));  // open: gt, lt
  Comparator #(.width(32), .mode("twosComplement")) comparator_6 (
    .a(CUR5), .b(EX_PC), .eq(comparator_6_eq));  // open: gt, lt
  Comparator #(.width(32), .mode("twosComplement")) comparator_7 (
    .a(CUR6), .b(EX_PC), .eq(comparator_7_eq));  // open: gt, lt
  Comparator #(.width(32), .mode("twosComplement")) comparator_8 (
    .a(CUR7), .b(EX_PC), .eq(comparator_8_eq));  // open: gt, lt
  and and_9 (H0, comparator_1_eq, V0);
  and and_10 (H1, comparator_2_eq, V1);
  and and_11 (H2, comparator_3_eq, V2);
  and and_12 (H3, comparator_4_eq, V3);
  and and_13 (H5, comparator_6_eq, V5);
  and and_14 (H4, comparator_5_eq, V4);
  and and_15 (H6, comparator_7_eq, V6);
  and and_16 (H7, comparator_8_eq, V7);
  not not_1 (not_1_out, V0);
  not not_2 (not_2_out, V1);
  not not_3 (not_3_out, V2);
  not not_4 (not_4_out, V3);
  not not_5 (not_5_out, V4);
  not not_6 (not_6_out, V5);
  not not_7 (not_7_out, V6);
  not not_8 (not_8_out, V7);
  or or_9 (EX_HIT, H0, H1, H2, H3, H4, H5, H6, H7);
  COMPARISON comparison_1 (
    .X(COUNT0), .Y(COUNT1), .X_PLACE(3'b000), .Y_PLACE(3'b001), .MAX(comparison_1_max),
    .MAX_PLACE(comparison_1_max_place));
  COMPARISON comparison_2 (
    .X(COUNT2), .Y(COUNT3), .X_PLACE(3'b010), .Y_PLACE(3'b011), .MAX(comparison_2_max),
    .MAX_PLACE(comparison_2_max_place));
  COMPARISON comparison_3 (
    .X(COUNT4), .Y(COUNT5), .X_PLACE(3'b100), .Y_PLACE(3'b101), .MAX(comparison_3_max),
    .MAX_PLACE(comparison_3_max_place));
  COMPARISON comparison_4 (
    .X(COUNT6), .Y(COUNT7), .X_PLACE(3'b110), .Y_PLACE(3'b111), .MAX(comparison_4_max),
    .MAX_PLACE(comparison_4_max_place));
  not not_9 (EX_MISS, EX_HIT);
  Priority_Encoder #(.select(3), .disabled("Z")) priority_encoder_1 (
    .in0(not_1_out), .in1(not_2_out), .in2(not_3_out), .in3(not_4_out), .in4(not_5_out), .in5(not_6_out),
    .in6(not_7_out), .in7(not_8_out), .out(priority_encoder_1_out), .gs(priority_encoder_1_gs));  // open: en_out, en_in
  not not_10 (not_10_out, priority_encoder_1_gs);
  COMPARISON comparison_5 (
    .X(comparison_1_max), .Y(comparison_2_max), .X_PLACE(comparison_1_max_place),
    .Y_PLACE(comparison_2_max_place), .MAX(comparison_5_max), .MAX_PLACE(comparison_5_max_place));
  Multiplexer #(.select(1), .width(3), .disabled("Z"), .enable("false")) multiplexer_10 (
    .in0(3'b000), .in1(priority_encoder_1_out), .out(multiplexer_10_out), .sel(priority_encoder_1_gs));
  COMPARISON comparison_6 (
    .X(comparison_3_max), .Y(comparison_4_max), .X_PLACE(comparison_3_max_place),
    .Y_PLACE(comparison_4_max_place), .MAX(comparison_6_max), .MAX_PLACE(comparison_6_max_place));
  Demultiplexer #(.select(3), .width(1), .tristate("false"), .disabled("Z"), .enable("true")) demultiplexer_1 (
    .out0(demultiplexer_1_out0), .out1(demultiplexer_1_out1), .out2(demultiplexer_1_out2),
    .out3(demultiplexer_1_out3), .out4(demultiplexer_1_out4), .out5(demultiplexer_1_out5),
    .out6(demultiplexer_1_out6), .out7(demultiplexer_1_out7), .in(priority_encoder_1_gs),
    .sel(multiplexer_10_out));  // open: en
  Demultiplexer #(.select(3), .width(1), .tristate("false"), .disabled("Z"), .enable("false")) demultiplexer_2 (
    .out0(demultiplexer_2_out0), .out1(demultiplexer_2_out1), .out2(demultiplexer_2_out2),
    .out3(demultiplexer_2_out3), .out4(demultiplexer_2_out4), .out5(demultiplexer_2_out5),
    .out6(demultiplexer_2_out6), .out7(demultiplexer_2_out7), .in(not_10_out), .sel(comparison_7_max_place));
  COMPARISON comparison_7 (
    .X(comparison_5_max), .Y(comparison_6_max), .X_PLACE(comparison_5_max_place),
    .Y_PLACE(comparison_6_max_place), .MAX_PLACE(comparison_7_max_place));  // open: MAX
  Priority_Encoder #(.select(3), .disabled("Z")) priority_encoder_2 (
    .in0(H0), .in1(H1), .in2(H2), .in3(H3), .in4(H4), .in5(H5), .in6(H6), .in7(H7),
    .out(priority_encoder_2_out));  // open: gs, en_out, en_in
  Multiplexer #(.select(3), .width(2), .disabled("Z"), .enable("false")) multiplexer_11 (
    .in0(P0), .in1(P1), .in2(P2), .in3(P3), .in4(P4), .in5(P5), .in6(P6), .in7(P7), .out(multiplexer_11_out),
    .sel(priority_encoder_2_out));
  or or_10 (or_10_out, demultiplexer_1_out0, demultiplexer_2_out0);
  or or_11 (or_11_out, demultiplexer_1_out1, demultiplexer_2_out1);
  or or_12 (or_12_out, demultiplexer_1_out2, demultiplexer_2_out2);
  or or_13 (or_13_out, demultiplexer_1_out3, demultiplexer_2_out3);
  or or_14 (or_14_out, demultiplexer_1_out4, demultiplexer_2_out4);
  or or_15 (or_15_out, demultiplexer_1_out5, demultiplexer_2_out5);
  or or_16 (or_16_out, demultiplexer_1_out6, demultiplexer_2_out6);
  or or_17 (or_17_out, demultiplexer_1_out7, demultiplexer_2_out7);
  FSM fsm_1 (.NEXT(PNEXT), .JUMP(EX_BRANCHTAKEN), .CUR(multiplexer_11_out));
  and and_17 (W0, or_10_out, EX_MISS, EX_BRANCH);
  and and_18 (W1, or_11_out, EX_MISS, EX_BRANCH);
  and and_19 (W2, or_12_out, EX_MISS, EX_BRANCH);
  and and_20 (W3, or_13_out, EX_MISS, EX_BRANCH);
  and and_21 (W4, or_14_out, EX_MISS, EX_BRANCH);
  and and_22 (W5, or_15_out, EX_MISS, EX_BRANCH);
  and and_23 (W6, or_16_out, EX_MISS, EX_BRANCH);
  and and_24 (W7, or_17_out, EX_MISS, EX_BRANCH);
  Comparator #(.width(32), .mode("twosComplement")) comparator_9 (
    .a(CUR0), .b(PC), .eq(comparator_9_eq));  // open: gt, lt
  Comparator #(.width(32), .mode("twosComplement")) comparator_10 (
    .a(CUR1), .b(PC), .eq(comparator_10_eq));  // open: gt, lt
  Comparator #(.width(32), .mode("twosComplement")) comparator_11 (
    .a(CUR2), .b(PC), .eq(comparator_11_eq));  // open: gt, lt
  Comparator #(.width(32), .mode("twosComplement")) comparator_12 (
    .a(CUR3), .b(PC), .eq(comparator_12_eq));  // open: gt, lt
  Comparator #(.width(32), .mode("twosComplement")) comparator_13 (
    .a(CUR4), .b(PC), .eq(comparator_13_eq));  // open: gt, lt
  Comparator #(.width(32), .mode("twosComplement")) comparator_14 (
    .a(CUR5), .b(PC), .eq(comparator_14_eq));  // open: gt, lt
  Comparator #(.width(32), .mode("twosComplement")) comparator_15 (
    .a(CUR6), .b(PC), .eq(comparator_15_eq));  // open: gt, lt
  Comparator #(.width(32), .mode("twosComplement")) comparator_16 (
    .a(CUR7), .b(PC), .eq(comparator_16_eq));  // open: gt, lt
  and and_25 (L0, comparator_9_eq, V0);
  and and_26 (L1, comparator_10_eq, V1);
  and and_27 (L2, comparator_11_eq, V2);
  and and_28 (L3, comparator_12_eq, V3);
  and and_29 (L4, comparator_13_eq, V4);
  and and_30 (L5, comparator_14_eq, V5);
  and and_31 (L6, comparator_15_eq, V6);
  and and_32 (L7, comparator_16_eq, V7);
  assign {PREDICTJUMP, controlled_buffer_1_out[0]} = L0 ? P0 : 2'bz;  // Controlled_Buffer controlled_buffer_1
  assign {PREDICTJUMP, controlled_buffer_1_out[0]} = L1 ? P1 : 2'bz;  // Controlled_Buffer controlled_buffer_2
  assign {PREDICTJUMP, controlled_buffer_1_out[0]} = L2 ? P2 : 2'bz;  // Controlled_Buffer controlled_buffer_3
  assign {PREDICTJUMP, controlled_buffer_1_out[0]} = L3 ? P3 : 2'bz;  // Controlled_Buffer controlled_buffer_4
  assign {PREDICTJUMP, controlled_buffer_1_out[0]} = L4 ? P4 : 2'bz;  // Controlled_Buffer controlled_buffer_5
  assign {PREDICTJUMP, controlled_buffer_1_out[0]} = L5 ? P5 : 2'bz;  // Controlled_Buffer controlled_buffer_6
  assign {PREDICTJUMP, controlled_buffer_1_out[0]} = L6 ? P6 : 2'bz;  // Controlled_Buffer controlled_buffer_7
  assign {PREDICTJUMP, controlled_buffer_1_out[0]} = L7 ? P7 : 2'bz;  // Controlled_Buffer controlled_buffer_8
  Pull_Resistor #(.pull(0)) pull_resistor_1 (.node({PREDICTJUMP, controlled_buffer_1_out[0]}));
  assign PREDICTADDR = L0 ? NEXT0 : 32'bz;  // Controlled_Buffer controlled_buffer_9
  assign PREDICTADDR = L1 ? NEXT1 : 32'bz;  // Controlled_Buffer controlled_buffer_10
  assign PREDICTADDR = L2 ? NEXT2 : 32'bz;  // Controlled_Buffer controlled_buffer_11
  assign PREDICTADDR = L3 ? NEXT3 : 32'bz;  // Controlled_Buffer controlled_buffer_12
  assign PREDICTADDR = L4 ? NEXT4 : 32'bz;  // Controlled_Buffer controlled_buffer_13
  assign PREDICTADDR = L5 ? NEXT5 : 32'bz;  // Controlled_Buffer controlled_buffer_14
  assign PREDICTADDR = L6 ? NEXT6 : 32'bz;  // Controlled_Buffer controlled_buffer_15
  assign PREDICTADDR = L7 ? NEXT7 : 32'bz;  // Controlled_Buffer controlled_buffer_16
  Pull_Resistor #(.pull(0)) pull_resistor_2 (.node(PREDICTADDR));

  // Other names for the same wires on the sheet: PREDICTADDRl[31:0] = PREDICTADDR

  // Notes on the sheet:
  //   VALID
  //   分支指令地址
  //   分支目标地址
  //   分支预测历史位
  //   置换标记
  //   EX分支写入逻辑
  //   选择一个位置写入该分支信息
  //   更新历史预测位
  //   IF段预测逻辑
  //   预测结果
endmodule

module COMPARISON (
  input  [31:0] X,
  input  [31:0] Y,
  input  [2:0] X_PLACE,
  input  [2:0] Y_PLACE,
  output [31:0] MAX,
  output [2:0] MAX_PLACE
);

  wire comparator_1_lt;

  Comparator #(.width(32), .mode("twosComplement")) comparator_1 (.a(X), .b(Y), .lt(comparator_1_lt));  // open: gt, eq
  Multiplexer #(.select(1), .width(32), .disabled("Z"), .enable("false")) multiplexer_1 (
    .in0(X), .in1(Y), .out(MAX), .sel(comparator_1_lt));
  Multiplexer #(.select(1), .width(3), .disabled("Z"), .enable("false")) multiplexer_2 (
    .in0(X_PLACE), .in1(Y_PLACE), .out(MAX_PLACE), .sel(comparator_1_lt));
endmodule

module FSM (
  input  [1:0] CUR,
  input  JUMP,
  output [1:0] NEXT
);

  Multiplexer #(.select(3), .width(2), .disabled("Z"), .enable("false")) multiplexer_1 (
    .in0(2'b00), .in1(2'b00), .in2(2'b11), .in3(2'b00), .in4(2'b01), .in5(2'b10), .in6(2'b10), .in7(2'b10),
    .out(NEXT), .sel({JUMP, CUR}));
endmodule
